// Logisim project 28单周期 +单级中断.circ as structural Verilog: 19 circuits, main circuit ◇单周期MIPS
module \单周期MIPS  (
  input  IR1,
  input  IR2,
  input  IR3,
  output RegWrite,
  output MemWrite,
  output [31:0] PC,
  output [31:0] IR,
  output [31:0] RDin,
  output [31:0] MDin,
  output [31:0] LedData
);

  wire AluSrcB, and_3_out, and_4_out, and_5_out, Beq, BGEZ, Bne, CLK, clock_2_out, comparator_1_eq,
       comparator_1_lt, comparator_2_eq, comparator_3_eq, comparator_3_gt, d_ff_1_q, DIVU, EQUAL, Go, IR1_t,
       IR2_t, IR3_t, IRA, IRB, IRC, JAL, JMP, JMP_IF, JR, LED_en, MemToReg, MFLO, nand_1_out, or_1_out,
       or_5_out, RegDst, SB, SignedExt, stop, Syscall, W1, W2, W3;
  wire [3:0] AluOP;
  wire [4:0] multiplexer_2_out, multiplexer_3_out, multiplexer_4_out, multiplexer_5_out;
  wire [12:0] CNT_num;
  wire [15:0] \总周期数 ;
  wire [27:0] PC_4;
  wire [31:0] a0, bit_extender_1_out, bit_extender_2_out, high_out, JR_PC, low_out, mem_read,
       multiplexer_1_out, multiplexer_6_out, multiplexer_7_out, multiplexer_9_out, multiplexer_10_out,
       multiplexer_11_out, PC_imm, result1, result2, shifter_1_out;
  wire [31:28] J_JAR_PC;

  Clock #(.highDuration(1), .lowDuration(1)) clock_1 ();  // open: out
  Button _1 (.out(IRA));
  Button _2 (.out(IRB));
  Button _3 (.out(IRC));
  Button \u_继续运行  (.out(Go));
  LED #(.active("true")) led_1 (.in(W1));
  LED #(.active("true")) led_2 (.in(W2));
  LED #(.active("true")) led_3 (.in(W3));
  Multiplexer #(.select(3), .width(32), .disabled("Z"), .enable("false")) multiplexer_1 (
    .in0({J_JAR_PC, PC_4}), .in1(PC_imm), .in2({J_JAR_PC, IR[25:0], 2'b00}), .in6(JR_PC),
    .out(multiplexer_1_out), .sel({JR, JMP, JMP_IF}));  // open: in3, in4, in5, in7
  // Probe on {JR, JMP, JMP_IF}
  Hex_Digit_Display hex_digit_display_1 (.value(LedData[31:28]));  // open: dp
  Adder #(.width(32)) adder_1 (.a(PC), .b(32'h4), .out({J_JAR_PC, PC_4}));  // open: cin, cout
  Register #(.width(32), .trigger("rising"), .Select("low")) u_PC (
    .D(multiplexer_1_out), .en(or_1_out), .Q(PC), .clk(CLK));  // open: clr
  or or_1 (or_1_out, ~stop, Go);  // OR_Gate
  Hex_Digit_Display hex_digit_display_2 (.value(LedData[27:24]));  // open: dp
  Hex_Digit_Display hex_digit_display_3 (.value(LedData[23:20]));  // open: dp
  // Probe on nothing
  // Probe on PC
  Hex_Digit_Display hex_digit_display_4 (.value(LedData[19:16]));  // open: dp
  Hex_Digit_Display hex_digit_display_5 (.value(LedData[15:12]));  // open: dp
  // Mips_Probe mips_probe_1: pin names not known; wires that end beside it: 32'h32d8, PC[11:2], 32'h2002000a
  D_Flip_Flop #(.trigger("high"), .Pre_Clr_Positions("LEGACY"), .NegatePresetClear("false"), .enable("true"), .NewFFLayout("false")) d_ff_1 (.Q(d_ff_1_q));  // open: clk, D, Qn, preset, en, reset
  // Probe on 13'h607
  Hex_Digit_Display hex_digit_display_6 (.value(LedData[7:4]));  // open: dp
  Hex_Digit_Display hex_digit_display_7 (.value(LedData[11:8]));  // open: dp
  // Probe on \总周期数 
  // Mips_Probe mips_probe_2: pin names not known; wires that end beside it: IR
  ROM #(.addrWidth(10), .dataWidth(32), .Select("high")) rom_1 (.addr(PC[11:2]), .data(IR));
  Comparator #(.width(13), .mode("twosComplement")) comparator_1 (
    .a(CNT_num), .b(13'h607), .eq(comparator_1_eq), .lt(comparator_1_lt));  // open: gt
  Clock #(.highDuration(1), .lowDuration(1)) clock_2 (.out(clock_2_out));
  Hex_Digit_Display hex_digit_display_8 (.value(LedData[3:0]));  // open: dp
  nand nand_1 (nand_1_out, d_ff_1_q, comparator_1_eq);
  Counter #(.width(13), .max('h1fff), .ongoal("stay"), .trigger("rising"), .behavior("old")) counter_1 (
    .count(comparator_1_lt), .Q(CNT_num), .clk(clock_2_out));  // open: load, D, carry, clr, preset
  Multiplexer #(.select(1), .width(5), .disabled("Z"), .enable("false")) multiplexer_2 (
    .in0(IR[25:21]), .in1(5'b00010), .out(multiplexer_2_out), .sel(Syscall));
  // Probe on multiplexer_2_out
  Multiplexer #(.select(1), .width(5), .disabled("Z"), .enable("false")) multiplexer_3 (
    .in0(IR[20:16]), .in1(5'b00100), .out(multiplexer_3_out), .sel(Syscall));
  // Probe on multiplexer_3_out
  Multiplexer #(.select(1), .width(5), .disabled("Z"), .enable("false")) multiplexer_4 (
    .in0(IR[20:16]), .in1(IR[15:11]), .out(multiplexer_4_out), .sel(RegDst));
  Multiplexer #(.select(1), .width(5), .disabled("Z"), .enable("false")) multiplexer_5 (
    .in0(multiplexer_4_out), .in1({5{1'b1}}), .out(multiplexer_5_out), .sel(JAL));
  // Probe on RDin
  // Probe on multiplexer_5_out
  Counter #(.width(13), .max('h1fff), .ongoal("stay"), .trigger("rising"), .behavior("old")) counter_2 (.clk(clock_2_out));  // open: load, D, count, Q, carry, clr, preset
  or or_2 (IR1_t, IR1, IRA);
  \单周期硬布线控制器  \u_单周期硬布线控制器_1  (
    .Func(IR[5:0]), .OP(IR[31:26]), .ALU_OP(AluOP), .MemToReg(MemToReg), .MemWrite(MemWrite),
    .ALU_SRC(AluSrcB), .RegWrite(RegWrite), .SysCALL(Syscall), .SignedExt(SignedExt), .RegDst(RegDst),
    .JR(JR), .JMP(JMP), .Beq(Beq), .JAL(JAL), .Bne(Bne), .DIVU(DIVU), .MFLO(MFLO), .BGEZ(BGEZ), .SB(SB));  // open: ERET
  assign bit_extender_1_out = {{16{1'b0}}, IR[15:0]};  // Bit_Extender bit_extender_1
  assign bit_extender_2_out = {{16{IR[15]}}, IR[15:0]};  // Bit_Extender bit_extender_2
  Register #(.width(32), .trigger("rising"), .Select("low")) register_1 (
    .D(a0), .en(LED_en), .Q(LedData), .clk(CLK));  // open: clr
  assign CLK = nand_1_out ? clock_2_out : 1'bz;  // Controlled_Buffer controlled_buffer_1
  Pull_Resistor #(.pull(1)) pull_resistor_1 (.node(CLK));
  or or_3 (IR2_t, IR2, IRB);
  MIPS_Regifile mips_regifile_1 (
    .Din(RDin), .Clk(CLK), .R1(JR_PC), .R2(a0), .WE(RegWrite), .W_num(multiplexer_5_out),
    .R1_num(multiplexer_2_out), .R2_num(multiplexer_3_out));
  // Probe on a0
  Multiplexer #(.select(1), .width(32), .disabled("Z"), .enable("false")) multiplexer_6 (
    .in0(bit_extender_1_out), .in1(bit_extender_2_out), .out(multiplexer_6_out), .sel(SignedExt));
  // Probe on JR_PC
  Multiplexer #(.select(1), .width(32), .disabled("Z"), .enable("false")) multiplexer_7 (
    .in0(a0), .in1(multiplexer_6_out), .out(multiplexer_7_out), .sel(AluSrcB));
  Shifter #(.width(32), .shift("ll")) shifter_1 (.in(bit_extender_2_out), .\dist (5'b00010), .out(shifter_1_out));
  or or_4 (IR3_t, IR3, IRC);
  MIPS_ALU mips_alu_1 (
    .X(JR_PC), .Y(multiplexer_7_out), .AluOP(AluOP), .Equal(EQUAL), .Result(result1), .Result_2(result2),
    .shamt(IR[10:6]));
  Adder #(.width(32)) adder_2 (.a(shifter_1_out), .b({J_JAR_PC, PC_4}), .out(PC_imm));  // open: cin, cout
  Register #(.width(32), .trigger("rising"), .Select("low")) hi (
    .D(result2), .en(DIVU), .Q(high_out), .clk(CLK));  // open: clr
  Register #(.width(32), .trigger("rising"), .Select("low")) lo (
    .D(result1), .en(DIVU), .Q(low_out), .clk(CLK));  // open: clr
  Comparator #(.width(32), .mode("twosComplement")) comparator_2 (
    .a(JR_PC), .b(32'h22), .eq(comparator_2_eq));  // open: gt, lt
  // Probe on result1
  and and_1 (stop, ~comparator_2_eq, Syscall);  // AND_Gate
  and and_2 (LED_en, comparator_2_eq, Syscall);
  Multiplexer #(.select(1), .width(32), .disabled("Z"), .enable("false")) multiplexer_8 (
    .in0(a0), .in1(multiplexer_9_out), .out(MDin), .sel(SB));
  Multiplexer #(.select(2), .width(32), .disabled("Z"), .enable("false")) multiplexer_9 (
    .in0({mem_read[31:8], a0[7:0]}), .in1({mem_read[31:16], a0[7:0], mem_read[7:0]}),
    .in2({mem_read[31:24], a0[7:0], mem_read[15:0]}), .in3({a0[7:0], mem_read[23:0]}),
    .out(multiplexer_9_out), .sel(result1[1:0]));
  and and_3 (and_3_out, Beq, EQUAL);
  and and_4 (and_4_out, Bne, ~EQUAL);  // AND_Gate
  Comparator #(.width(32), .mode("twosComplement")) comparator_3 (
    .a(JR_PC), .b({32{1'b0}}), .gt(comparator_3_gt), .eq(comparator_3_eq));  // open: lt
  RAM #(.addrWidth(10), .dataWidth(32), .bus("separate"), .Select("high")) ram_1 (
    .addr(result1[11:2]), .din(MDin), .data(mem_read), .str(MemWrite), .clk(CLK));  // open: sel, ld, clr
  and and_5 (and_5_out, BGEZ, or_5_out);
  or or_5 (or_5_out, comparator_3_gt, comparator_3_eq);
  Multiplexer #(.select(1), .width(32), .disabled("Z"), .enable("false")) multiplexer_10 (
    .in0(result1), .in1(mem_read), .out(multiplexer_10_out), .sel(MemToReg));
  or or_6 (JMP_IF, and_3_out, and_4_out, and_5_out);
  Multiplexer #(.select(1), .width(32), .disabled("Z"), .enable("false")) multiplexer_11 (
    .in0(multiplexer_10_out), .in1({J_JAR_PC, PC_4}), .out(multiplexer_11_out), .sel(JAL));
  Multiplexer #(.select(1), .width(32), .disabled("Z"), .enable("false")) multiplexer_12 (
    .in0(multiplexer_11_out), .in1(low_out), .out(RDin), .sel(MFLO));

  // Other names for the same wires on the sheet: rt[31:0] = a0; J_JAR_PC[27:2] = IR[25:0]; PC_4[31:28] = J_JAR_PC;
  //   rs[31:0] = JR_PC; v0[31:0] = JR_PC

  // Notes on the sheet:
  //   中断源
  //   中断等待指示
  //   总复位信号应将除ROM以外所有存储组件全部清零
  //   数码管输出
  //   指令存储器
  //   控制位
  //   暂停节拍，不能为0
  //   数码管输出应该用寄存器锁存，否则显示数据只能一闪而过
  //   指令字
  //   contents of rom_1 (hex, n*v repeats v):
  //   20090000 200b0020 20110000 20120001 a1310000 112020 20020022 c 2328820 21290001 216bffff 1560fff8
  //   200b0008 20090000 8d310000 112020 20020022 c 21290004 216bffff 1560fff9 2002000a c
  //   戳工具置1进入计数暂停模式，ctrl+k时钟自动运行到对应节拍暂停
  //   ctrl+k关闭时钟连续运行，将控制位置零，进入单步调试模式调试
  //   用这个时钟源需要去掉电路中的其他时钟源
  //   OP
  //   Func
  //   rs
  //   rt
  //   rd
  //   shmat
  //   imm
  //   addr
  //   JMP
  //   JR
  //   OP
  //   Func
  //   可计数暂停的时钟源
  //   Beq
  //   Bne
  //   MemToReg
  //   MemWrite
  //   AluOP
  //   AluSrcB
  //   RegWrite
  //   JAL
  //   RegDst
  //   Syscall
  //   为方便自动评测，需要输出PC，IR，寄存器堆写如数据RDin
  //   RAM写使能MemWrite、RAM写入数据MDin等信号
endmodule

// 单周期硬布线控制器
module \单周期硬布线控制器  (
  input  [5:0] OP,
  input  [5:0] Func,
  output [3:0] ALU_OP,
  output MemToReg,
  output MemWrite,
  output DIVU,
  output MFLO,
  output BGEZ,
  output SB,
  output ALU_SRC,
  output RegWrite,
  output ERET,
  output SysCALL,
  output SignedExt,
  output RegDst,
  output Beq,
  output Bne,
  output JR,
  output JMP,
  output JAL
);

  \运算控制器自动生成  \u_运算控制器自动生成_1  (
    .OP0(OP[0]), .OP1(OP[1]), .OP2(OP[2]), .OP3(OP[3]), .OP4(OP[4]), .OP5(OP[5]), .F0(Func[0]), .F1(Func[1]),
    .F2(Func[2]), .F3(Func[3]), .F4(Func[4]), .F5(Func[5]), .S0(ALU_OP[0]), .S1(ALU_OP[1]), .S2(ALU_OP[2]),
    .S3(ALU_OP[3]));
  \控制信号自动生成  \u_控制信号自动生成_1  (
    .OP0(OP[0]), .MemToReg(MemToReg), .OP1(OP[1]), .OP2(OP[2]), .OP3(OP[3]), .OP4(OP[4]),
    .MemWrite(MemWrite), .OP5(OP[5]), .F0(Func[0]), .F1(Func[1]), .F2(Func[2]), .F3(Func[3]), .DIVU(DIVU),
    .F4(Func[4]), .F5(Func[5]), .MFLO(MFLO), .BGEZ(BGEZ), .SB(SB), .ALU_SRC(ALU_SRC), .RegWrite(RegWrite),
    .ERET(ERET), .SysCALL(SysCALL), .SignedExt(SignedExt), .RegDst(RegDst), .BEQ(Beq), .BNE(Bne), .JR(JR),
    .JUMP(JMP), .JAL(JAL));

  // Other names for the same wires on the sheet: OP_CODE[5:0] = OP

  // Notes on the sheet:
  //   控制信号生成，产生数据通路需要的其他控制信号
  //   运算器控制器，根据指令生成运算器功能选择信号
endmodule

// 运算器控制器
module \运算控制器自动生成  (
  input  OP0,
  input  OP1,
  input  OP2,
  input  OP3,
  input  OP4,
  input  OP5,
  input  F0,
  input  F1,
  input  F2,
  input  F3,
  input  F4,
  input  F5,
  output S0,
  output S1,
  output S2,
  output S3
);

  wire and_1_out, and_2_out, and_3_out, and_4_out, and_5_out, and_6_out, and_7_out, and_8_out, and_9_out,
       and_10_out, and_11_out, and_12_out, and_13_out, and_14_out, and_15_out, and_16_out, and_17_out,
       and_18_out, and_19_out, and_20_out, and_21_out, and_22_out, and_23_out, and_24_out, and_25_out,
       and_26_out, and_27_out, and_28_out, and_29_out, and_30_out, and_31_out, and_32_out, and_33_out,
       and_34_out, and_35_out, and_36_out, and_37_out, not_1_out, not_2_out, not_3_out, not_4_out, not_5_out,
       not_6_out, not_7_out, not_8_out, not_9_out, not_10_out, not_11_out, not_12_out, not_13_out,
       not_14_out, not_15_out, not_16_out, not_17_out, not_18_out, not_19_out, not_20_out, not_21_out,
       not_22_out, not_23_out, not_24_out, not_25_out, not_26_out, not_27_out, not_28_out, not_29_out,
       not_30_out, not_31_out, not_32_out, not_33_out, not_34_out, not_35_out, not_36_out, not_37_out,
       not_38_out, not_39_out, not_40_out, not_41_out, not_42_out, not_43_out, not_44_out, not_45_out,
       not_46_out, not_47_out, not_48_out, not_49_out, not_50_out, not_51_out, not_52_out, not_53_out,
       not_54_out, not_55_out, not_56_out, not_57_out, not_58_out, not_59_out, not_60_out, not_61_out,
       not_62_out, not_63_out, not_64_out, not_65_out, not_66_out, not_67_out, not_68_out, not_69_out,
       not_70_out, not_71_out, not_72_out, not_73_out, not_74_out, not_75_out, not_76_out, not_77_out,
       not_78_out, not_79_out, not_80_out, not_81_out, not_82_out, not_83_out, not_84_out, not_85_out,
       not_86_out, not_87_out, not_88_out, not_89_out, not_90_out, not_91_out, not_92_out, not_93_out,
       not_94_out, not_95_out, not_96_out, not_97_out, not_98_out, not_99_out, not_100_out, not_101_out,
       not_102_out, not_103_out, not_104_out, not_105_out, not_106_out, not_107_out, not_108_out,
       not_109_out, not_110_out, not_111_out, not_112_out, not_113_out, not_114_out, not_115_out,
       not_116_out, not_117_out, not_118_out, not_119_out, not_120_out, not_121_out, not_122_out,
       not_123_out, not_124_out, not_125_out, not_126_out, not_127_out, not_128_out, not_129_out,
       not_130_out, not_131_out, not_132_out, not_133_out, not_134_out, not_135_out, not_136_out,
       not_137_out, not_138_out, not_139_out, not_140_out, not_141_out, not_142_out, not_143_out,
       not_144_out, not_145_out, not_146_out, not_147_out, not_148_out, not_149_out, not_150_out,
       not_151_out, not_152_out, not_153_out, not_154_out, not_155_out, not_156_out, not_157_out,
       not_158_out, not_159_out, not_160_out, not_161_out, not_162_out, not_163_out, not_164_out,
       not_165_out, not_166_out, not_167_out, not_168_out, not_169_out, not_170_out, not_171_out,
       not_172_out, not_173_out, not_174_out, not_175_out, not_176_out, not_177_out, not_178_out,
       not_179_out, not_180_out, not_181_out, not_182_out, not_183_out, not_184_out, not_185_out,
       not_186_out, not_187_out, not_188_out, not_189_out, not_190_out, not_191_out, not_192_out,
       not_193_out, not_194_out, not_195_out, not_196_out, not_197_out, not_198_out, not_199_out,
       not_200_out, not_201_out, not_202_out, not_203_out, not_204_out, not_205_out, not_206_out,
       not_207_out, not_208_out, not_209_out, not_210_out, not_211_out, not_212_out, not_213_out,
       not_214_out, not_215_out, not_216_out, not_217_out, not_218_out, not_219_out, not_220_out,
       not_221_out, not_222_out, not_223_out, not_224_out, not_225_out, not_226_out, not_227_out,
       not_228_out, not_229_out, not_230_out, not_231_out, not_232_out, not_233_out, not_234_out,
       not_235_out, not_236_out, not_237_out, not_238_out, not_239_out, not_240_out, not_241_out,
       not_242_out, not_243_out, not_244_out, not_245_out, not_246_out, not_247_out, not_248_out,
       not_249_out, not_250_out, not_251_out, not_252_out;

  not not_1 (not_1_out, OP5);
  not not_2 (not_2_out, OP4);
  not not_3 (not_3_out, OP3);
  not not_4 (not_4_out, OP2);
  not not_5 (not_5_out, OP1);
  not not_6 (not_6_out, OP0);
  not not_7 (not_7_out, F5);
  not not_8 (not_8_out, F4);
  not not_9 (not_9_out, F3);
  not not_10 (not_10_out, F2);
  not not_11 (not_11_out, OP5);
  not not_12 (not_12_out, OP4);
  not not_13 (not_13_out, OP3);
  not not_14 (not_14_out, OP2);
  not not_15 (not_15_out, OP1);
  not not_16 (not_16_out, OP0);
  not not_17 (not_17_out, F4);
  not not_18 (not_18_out, F3);
  not not_19 (not_19_out, F2);
  not not_20 (not_20_out, F1);
  not not_21 (not_21_out, F0);
  not not_22 (not_22_out, OP5);
  not not_23 (not_23_out, OP4);
  not not_24 (not_24_out, OP3);
  not not_25 (not_25_out, OP2);
  not not_26 (not_26_out, OP1);
  not not_27 (not_27_out, OP0);
  not not_28 (not_28_out, F4);
  not not_29 (not_29_out, F3);
  not not_30 (not_30_out, F2);
  not not_31 (not_31_out, F1);
  not not_32 (not_32_out, OP5);
  not not_33 (not_33_out, OP4);
  not not_34 (not_34_out, OP3);
  not not_35 (not_35_out, OP2);
  not not_36 (not_36_out, OP1);
  not not_37 (not_37_out, OP0);
  not not_38 (not_38_out, F4);
  not not_39 (not_39_out, F3);
  not not_40 (not_40_out, F1);
  not not_41 (not_41_out, F0);
  not not_42 (not_42_out, OP5);
  not not_43 (not_43_out, OP4);
  not not_44 (not_44_out, OP3);
  not not_45 (not_45_out, OP2);
  not not_46 (not_46_out, OP1);
  not not_47 (not_47_out, OP0);
  not not_48 (not_48_out, F4);
  not not_49 (not_49_out, F2);
  not not_50 (not_50_out, F0);
  not not_51 (not_51_out, OP5);
  not not_52 (not_52_out, OP4);
  not not_53 (not_53_out, OP2);
  not not_54 (not_54_out, OP1);
  not not_55 (not_55_out, OP0);
  not not_56 (not_56_out, OP5);
  not not_57 (not_57_out, OP4);
  not not_58 (not_58_out, OP1);
  not not_59 (not_59_out, OP0);
  not not_60 (not_60_out, OP5);
  not not_61 (not_61_out, OP4);
  not not_62 (not_62_out, OP2);
  not not_63 (not_63_out, OP1);
  not not_64 (not_64_out, OP5);
  not not_65 (not_65_out, OP4);
  not not_66 (not_66_out, OP2);
  not not_67 (not_67_out, OP0);
  not not_68 (not_68_out, OP4);
  not not_69 (not_69_out, OP3);
  not not_70 (not_70_out, OP2);
  not not_71 (not_71_out, OP4);
  not not_72 (not_72_out, OP2);
  not not_73 (not_73_out, OP4);
  not not_74 (not_74_out, OP2);
  not not_75 (not_75_out, OP1);
  not not_76 (not_76_out, OP0);
  not not_77 (not_77_out, OP5);
  not not_78 (not_78_out, OP4);
  not not_79 (not_79_out, OP3);
  not not_80 (not_80_out, OP2);
  not not_81 (not_81_out, OP1);
  not not_82 (not_82_out, OP0);
  not not_83 (not_83_out, F5);
  not not_84 (not_84_out, F4);
  not not_85 (not_85_out, F3);
  not not_86 (not_86_out, F2);
  not not_87 (not_87_out, F0);
  not not_88 (not_88_out, OP5);
  not not_89 (not_89_out, OP4);
  not not_90 (not_90_out, OP3);
  not not_91 (not_91_out, OP2);
  not not_92 (not_92_out, OP1);
  not not_93 (not_93_out, OP0);
  not not_94 (not_94_out, F4);
  not not_95 (not_95_out, F3);
  not not_96 (not_96_out, F2);
  not not_97 (not_97_out, F0);
  not not_98 (not_98_out, OP5);
  not not_99 (not_99_out, OP4);
  not not_100 (not_100_out, OP3);
  not not_101 (not_101_out, OP2);
  not not_102 (not_102_out, OP1);
  not not_103 (not_103_out, OP0);
  not not_104 (not_104_out, F4);
  not not_105 (not_105_out, F3);
  not not_106 (not_106_out, F1);
  not not_107 (not_107_out, F0);
  not not_108 (not_108_out, OP5);
  not not_109 (not_109_out, OP4);
  not not_110 (not_110_out, OP3);
  not not_111 (not_111_out, OP2);
  not not_112 (not_112_out, OP1);
  not not_113 (not_113_out, OP0);
  not not_114 (not_114_out, F4);
  not not_115 (not_115_out, F3);
  not not_116 (not_116_out, OP5);
  not not_117 (not_117_out, OP4);
  not not_118 (not_118_out, OP3);
  not not_119 (not_119_out, OP2);
  not not_120 (not_120_out, OP1);
  not not_121 (not_121_out, OP0);
  not not_122 (not_122_out, F4);
  not not_123 (not_123_out, F2);
  not not_124 (not_124_out, F0);
  not not_125 (not_125_out, OP5);
  not not_126 (not_126_out, OP4);
  not not_127 (not_127_out, OP1);
  not not_128 (not_128_out, OP0);
  not not_129 (not_129_out, OP5);
  not not_130 (not_130_out, OP4);
  not not_131 (not_131_out, OP2);
  not not_132 (not_132_out, OP0);
  not not_133 (not_133_out, OP5);
  not not_134 (not_134_out, OP4);
  not not_135 (not_135_out, OP3);
  not not_136 (not_136_out, OP2);
  not not_137 (not_137_out, OP1);
  not not_138 (not_138_out, OP0);
  not not_139 (not_139_out, F4);
  not not_140 (not_140_out, F3);
  not not_141 (not_141_out, F2);
  not not_142 (not_142_out, F1);
  not not_143 (not_143_out, F0);
  not not_144 (not_144_out, OP5);
  not not_145 (not_145_out, OP4);
  not not_146 (not_146_out, OP3);
  not not_147 (not_147_out, OP2);
  not not_148 (not_148_out, OP1);
  not not_149 (not_149_out, OP0);
  not not_150 (not_150_out, F4);
  not not_151 (not_151_out, F3);
  not not_152 (not_152_out, F2);
  not not_153 (not_153_out, F1);
  not not_154 (not_154_out, OP5);
  not not_155 (not_155_out, OP4);
  not not_156 (not_156_out, OP3);
  not not_157 (not_157_out, OP2);
  not not_158 (not_158_out, OP1);
  not not_159 (not_159_out, OP0);
  not not_160 (not_160_out, F4);
  not not_161 (not_161_out, F3);
  not not_162 (not_162_out, F2);
  not not_163 (not_163_out, F0);
  not not_164 (not_164_out, OP5);
  not not_165 (not_165_out, OP4);
  not not_166 (not_166_out, OP3);
  not not_167 (not_167_out, OP2);
  not not_168 (not_168_out, OP1);
  not not_169 (not_169_out, OP0);
  not not_170 (not_170_out, F4);
  not not_171 (not_171_out, F3);
  not not_172 (not_172_out, F1);
  not not_173 (not_173_out, F0);
  not not_174 (not_174_out, OP5);
  not not_175 (not_175_out, OP4);
  not not_176 (not_176_out, OP3);
  not not_177 (not_177_out, OP2);
  not not_178 (not_178_out, OP1);
  not not_179 (not_179_out, OP0);
  not not_180 (not_180_out, F4);
  not not_181 (not_181_out, F2);
  not not_182 (not_182_out, OP5);
  not not_183 (not_183_out, OP4);
  not not_184 (not_184_out, OP2);
  not not_185 (not_185_out, OP1);
  not not_186 (not_186_out, OP0);
  not not_187 (not_187_out, OP5);
  not not_188 (not_188_out, OP4);
  not not_189 (not_189_out, OP1);
  not not_190 (not_190_out, OP0);
  not not_191 (not_191_out, OP5);
  not not_192 (not_192_out, OP4);
  not not_193 (not_193_out, OP2);
  not not_194 (not_194_out, OP1);
  not not_195 (not_195_out, OP4);
  not not_196 (not_196_out, OP3);
  not not_197 (not_197_out, OP2);
  not not_198 (not_198_out, OP4);
  not not_199 (not_199_out, OP2);
  not not_200 (not_200_out, OP5);
  not not_201 (not_201_out, OP4);
  not not_202 (not_202_out, OP3);
  not not_203 (not_203_out, OP2);
  not not_204 (not_204_out, OP1);
  not not_205 (not_205_out, OP0);
  not not_206 (not_206_out, F5);
  not not_207 (not_207_out, F2);
  not not_208 (not_208_out, OP4);
  not not_209 (not_209_out, OP2);
  not not_210 (not_210_out, OP1);
  not not_211 (not_211_out, OP0);
  not not_212 (not_212_out, OP5);
  not not_213 (not_213_out, OP4);
  not not_214 (not_214_out, OP3);
  not not_215 (not_215_out, OP2);
  not not_216 (not_216_out, OP1);
  not not_217 (not_217_out, OP0);
  not not_218 (not_218_out, F4);
  not not_219 (not_219_out, F3);
  not not_220 (not_220_out, F1);
  not not_221 (not_221_out, OP5);
  not not_222 (not_222_out, OP4);
  not not_223 (not_223_out, OP3);
  not not_224 (not_224_out, OP2);
  not not_225 (not_225_out, OP1);
  not not_226 (not_226_out, OP0);
  not not_227 (not_227_out, F4);
  not not_228 (not_228_out, F3);
  not not_229 (not_229_out, OP5);
  not not_230 (not_230_out, OP4);
  not not_231 (not_231_out, OP3);
  not not_232 (not_232_out, OP2);
  not not_233 (not_233_out, OP1);
  not not_234 (not_234_out, OP0);
  not not_235 (not_235_out, F4);
  not not_236 (not_236_out, F2);
  not not_237 (not_237_out, F0);
  not not_238 (not_238_out, OP5);
  not not_239 (not_239_out, OP4);
  not not_240 (not_240_out, OP3);
  not not_241 (not_241_out, OP2);
  not not_242 (not_242_out, OP1);
  not not_243 (not_243_out, OP0);
  not not_244 (not_244_out, F4);
  not not_245 (not_245_out, F2);
  not not_246 (not_246_out, OP5);
  not not_247 (not_247_out, OP4);
  not not_248 (not_248_out, OP2);
  not not_249 (not_249_out, OP0);
  not not_250 (not_250_out, OP5);
  not not_251 (not_251_out, OP4);
  not not_252 (not_252_out, OP1);
  and and_1 (and_1_out, not_1_out, not_2_out, not_3_out, not_4_out, not_5_out, not_6_out, not_7_out, not_8_out, not_9_out, not_10_out, F1, F0);
  and and_2 (and_2_out, not_11_out, not_12_out, not_13_out, not_14_out, not_15_out, not_16_out, F5, not_17_out, not_18_out, not_19_out, not_20_out, not_21_out);
  and and_3 (and_3_out, not_22_out, not_23_out, not_24_out, not_25_out, not_26_out, not_27_out, F5, not_28_out, not_29_out, not_30_out, not_31_out, F0);
  and and_4 (and_4_out, not_32_out, not_33_out, not_34_out, not_35_out, not_36_out, not_37_out, F5, not_38_out, not_39_out, F2, not_40_out, not_41_out);
  and and_5 (and_5_out, not_42_out, not_43_out, not_44_out, not_45_out, not_46_out, not_47_out, F5, not_48_out, F3, not_49_out, F1, not_50_out);
  and and_6 (and_6_out, not_51_out, not_52_out, OP3, not_53_out, not_54_out, not_55_out);
  and and_7 (and_7_out, not_56_out, not_57_out, OP3, OP2, not_58_out, not_59_out);
  and and_8 (and_8_out, not_60_out, not_61_out, OP3, not_62_out, not_63_out, OP0);
  and and_9 (and_9_out, not_64_out, not_65_out, OP3, not_66_out, OP1, not_67_out);
  and and_10 (and_10_out, OP5, not_68_out, not_69_out, not_70_out, OP1, OP0);
  and and_11 (and_11_out, OP5, not_71_out, OP3, not_72_out, OP1, OP0);
  and and_12 (and_12_out, OP5, not_73_out, OP3, not_74_out, not_75_out, not_76_out);
  and and_13 (and_13_out, not_77_out, not_78_out, not_79_out, not_80_out, not_81_out, not_82_out, not_83_out, not_84_out, not_85_out, not_86_out, F1, not_87_out);
  and and_14 (and_14_out, not_88_out, not_89_out, not_90_out, not_91_out, not_92_out, not_93_out, F5, not_94_out, not_95_out, not_96_out, F1, not_97_out);
  and and_15 (and_15_out, not_98_out, not_99_out, not_100_out, not_101_out, not_102_out, not_103_out, F5, not_104_out, not_105_out, F2, not_106_out, not_107_out);
  and and_16 (and_16_out, not_108_out, not_109_out, not_110_out, not_111_out, not_112_out, not_113_out, F5, not_114_out, not_115_out, F2, F1, F0);
  and and_17 (and_17_out, not_116_out, not_117_out, not_118_out, not_119_out, not_120_out, not_121_out, F5, not_122_out, F3, not_123_out, F1, not_124_out);
  and and_18 (and_18_out, not_125_out, not_126_out, OP3, OP2, not_127_out, not_128_out);
  and and_19 (and_19_out, not_129_out, not_130_out, OP3, not_131_out, OP1, not_132_out);
  and and_20 (and_20_out, not_133_out, not_134_out, not_135_out, not_136_out, not_137_out, not_138_out, F5, not_139_out, not_140_out, not_141_out, not_142_out, not_143_out);
  and and_21 (and_21_out, not_144_out, not_145_out, not_146_out, not_147_out, not_148_out, not_149_out, F5, not_150_out, not_151_out, not_152_out, not_153_out, F0);
  and and_22 (and_22_out, not_154_out, not_155_out, not_156_out, not_157_out, not_158_out, not_159_out, F5, not_160_out, not_161_out, not_162_out, F1, not_163_out);
  and and_23 (and_23_out, not_164_out, not_165_out, not_166_out, not_167_out, not_168_out, not_169_out, F5, not_170_out, not_171_out, F2, not_172_out, not_173_out);
  and and_24 (and_24_out, not_174_out, not_175_out, not_176_out, not_177_out, not_178_out, not_179_out, F5, not_180_out, F3, not_181_out, F1, F0);
  and and_25 (and_25_out, not_182_out, not_183_out, OP3, not_184_out, not_185_out, not_186_out);
  and and_26 (and_26_out, not_187_out, not_188_out, OP3, OP2, not_189_out, not_190_out);
  and and_27 (and_27_out, not_191_out, not_192_out, OP3, not_193_out, not_194_out, OP0);
  and and_28 (and_28_out, OP5, not_195_out, not_196_out, not_197_out, OP1, OP0);
  and and_29 (and_29_out, OP5, not_198_out, OP3, not_199_out, OP1, OP0);
  and and_30 (and_30_out, not_200_out, not_201_out, not_202_out, not_203_out, not_204_out, not_205_out, not_206_out, F4, F3, not_207_out, F1, F0);
  and and_31 (and_31_out, OP5, not_208_out, OP3, not_209_out, not_210_out, not_211_out);
  and and_32 (and_32_out, not_212_out, not_213_out, not_214_out, not_215_out, not_216_out, not_217_out, F5, not_218_out, not_219_out, F2, not_220_out, F0);
  and and_33 (and_33_out, not_221_out, not_222_out, not_223_out, not_224_out, not_225_out, not_226_out, F5, not_227_out, not_228_out, F2, F1, F0);
  and and_34 (and_34_out, not_229_out, not_230_out, not_231_out, not_232_out, not_233_out, not_234_out, F5, not_235_out, F3, not_236_out, F1, not_237_out);
  and and_35 (and_35_out, not_238_out, not_239_out, not_240_out, not_241_out, not_242_out, not_243_out, F5, not_244_out, F3, not_245_out, F1, F0);
  and and_36 (and_36_out, not_246_out, not_247_out, OP3, not_248_out, OP1, not_249_out);
  and and_37 (and_37_out, not_250_out, not_251_out, OP3, OP2, not_252_out, OP0);
  or or_1 (S1, and_13_out, and_14_out, and_15_out, and_16_out, and_17_out, and_18_out, and_19_out);
  or or_2 (S3, and_32_out, and_33_out, and_34_out, and_35_out, and_36_out, and_37_out);
  or or_3 (S0, and_1_out, and_2_out, and_3_out, and_4_out, and_5_out, and_6_out, and_7_out, and_8_out, and_9_out, and_10_out, and_11_out, and_12_out);
  or or_4 (S2, and_20_out, and_21_out, and_22_out, and_23_out, and_24_out, and_25_out, and_26_out, and_27_out, and_28_out, and_29_out, and_30_out, and_31_out);
endmodule

// 控制信号生成
module \控制信号自动生成  (
  input  OP0,
  input  OP1,
  input  OP2,
  input  OP3,
  input  OP4,
  input  OP5,
  input  F0,
  input  F1,
  input  F2,
  input  F3,
  input  F4,
  input  F5,
  output MemToReg,
  output MemWrite,
  output DIVU,
  output MFLO,
  output BGEZ,
  output SB,
  output ALU_SRC,
  output RegWrite,
  output ERET,
  output SysCALL,
  output SignedExt,
  output RegDst,
  output BEQ,
  output BNE,
  output JR,
  output JUMP,
  output JAL
);

  wire and_2_out, and_3_out, and_8_out, and_9_out, and_10_out, and_11_out, and_12_out, and_13_out,
       and_14_out, and_15_out, and_16_out, and_17_out, and_18_out, and_19_out, and_20_out, and_23_out,
       and_24_out, and_25_out, and_26_out, and_27_out, and_28_out, and_29_out, and_30_out, and_31_out,
       and_32_out, and_36_out, and_37_out, not_1_out, not_2_out, not_3_out, not_4_out, not_5_out, not_6_out,
       not_7_out, not_8_out, not_9_out, not_10_out, not_11_out, not_12_out, not_13_out, not_14_out,
       not_15_out, not_16_out, not_17_out, not_18_out, not_19_out, not_20_out, not_21_out, not_22_out,
       not_23_out, not_24_out, not_25_out, not_26_out, not_27_out, not_28_out, not_29_out, not_30_out,
       not_31_out, not_32_out, not_33_out, not_34_out, not_35_out, not_36_out, not_37_out, not_38_out,
       not_39_out, not_40_out, not_41_out, not_42_out, not_43_out, not_44_out, not_45_out, not_46_out,
       not_47_out, not_48_out, not_49_out, not_50_out, not_51_out, not_52_out, not_53_out, not_54_out,
       not_55_out, not_56_out, not_57_out, not_58_out, not_59_out, not_60_out, not_61_out, not_62_out,
       not_63_out, not_64_out, not_65_out, not_66_out, not_67_out, not_68_out, not_69_out, not_70_out,
       not_71_out, not_72_out, not_73_out, not_74_out, not_75_out, not_76_out, not_77_out, not_78_out,
       not_79_out, not_80_out, not_81_out, not_82_out, not_83_out, not_84_out, not_85_out, not_86_out,
       not_87_out, not_88_out, not_89_out, not_90_out, not_91_out, not_92_out, not_93_out, not_94_out,
       not_95_out, not_96_out, not_97_out, not_98_out, not_99_out, not_100_out, not_101_out, not_102_out,
       not_103_out, not_104_out, not_105_out, not_106_out, not_107_out, not_108_out, not_109_out,
       not_110_out, not_111_out, not_112_out, not_113_out, not_114_out, not_115_out, not_116_out,
       not_117_out, not_118_out, not_119_out, not_120_out, not_121_out, not_122_out, not_123_out,
       not_124_out, not_125_out, not_126_out, not_127_out, not_128_out, not_129_out, not_130_out,
       not_131_out, not_132_out, not_133_out, not_134_out, not_135_out, not_136_out, not_137_out,
       not_138_out, not_139_out, not_140_out, not_141_out, not_142_out, not_143_out, not_144_out,
       not_145_out, not_146_out, not_147_out, not_148_out, not_149_out, not_150_out, not_151_out,
       not_152_out, not_153_out, not_154_out, not_155_out, not_156_out, not_157_out, not_158_out,
       not_159_out, not_160_out, not_161_out, not_162_out, not_163_out, not_164_out, not_165_out,
       not_166_out, not_167_out, not_168_out, not_169_out, not_170_out, not_171_out, not_172_out,
       not_173_out, not_174_out, not_175_out, not_176_out, not_177_out, not_178_out, not_179_out,
       not_180_out, not_181_out, not_182_out, not_183_out, not_184_out, not_185_out, not_186_out,
       not_187_out, not_188_out, not_189_out, not_190_out, not_191_out, not_192_out, not_193_out,
       not_194_out, not_195_out, not_196_out, not_197_out, not_198_out, not_199_out, not_200_out,
       not_201_out, not_202_out, not_203_out, not_204_out, not_205_out, not_206_out, not_207_out,
       not_208_out, not_209_out, not_210_out, not_211_out, not_212_out, not_213_out, not_214_out,
       not_215_out, not_216_out, not_217_out, not_218_out, not_219_out, not_220_out, not_221_out,
       not_222_out, not_223_out, not_224_out, not_225_out, not_226_out, not_227_out, not_228_out,
       not_229_out, not_230_out, not_231_out, not_232_out, not_233_out, not_234_out;

  not not_1 (not_1_out, OP2);
  not not_2 (not_2_out, OP3);
  not not_3 (not_3_out, OP4);
  not not_4 (not_4_out, OP0);
  not not_5 (not_5_out, OP1);
  not not_6 (not_6_out, OP2);
  not not_7 (not_7_out, OP4);
  not not_8 (not_8_out, OP2);
  not not_9 (not_9_out, OP4);
  not not_10 (not_10_out, OP0);
  not not_11 (not_11_out, OP1);
  not not_12 (not_12_out, OP2);
  not not_13 (not_13_out, OP3);
  not not_14 (not_14_out, OP4);
  not not_15 (not_15_out, OP5);
  not not_16 (not_16_out, F2);
  not not_17 (not_17_out, F5);
  not not_18 (not_18_out, OP0);
  not not_19 (not_19_out, OP1);
  not not_20 (not_20_out, OP2);
  not not_21 (not_21_out, OP3);
  not not_22 (not_22_out, OP4);
  not not_23 (not_23_out, OP5);
  not not_24 (not_24_out, F0);
  not not_25 (not_25_out, F2);
  not not_26 (not_26_out, F3);
  not not_27 (not_27_out, F5);
  not not_28 (not_28_out, OP1);
  not not_29 (not_29_out, OP2);
  not not_30 (not_30_out, OP3);
  not not_31 (not_31_out, OP4);
  not not_32 (not_32_out, OP5);
  not not_33 (not_33_out, OP0);
  not not_34 (not_34_out, OP1);
  not not_35 (not_35_out, OP2);
  not not_36 (not_36_out, OP4);
  not not_37 (not_37_out, OP0);
  not not_38 (not_38_out, OP1);
  not not_39 (not_39_out, OP2);
  not not_40 (not_40_out, OP4);
  not not_41 (not_41_out, OP0);
  not not_42 (not_42_out, OP2);
  not not_43 (not_43_out, OP4);
  not not_44 (not_44_out, OP5);
  not not_45 (not_45_out, OP1);
  not not_46 (not_46_out, OP4);
  not not_47 (not_47_out, OP5);
  not not_48 (not_48_out, OP2);
  not not_49 (not_49_out, OP4);
  not not_50 (not_50_out, OP0);
  not not_51 (not_51_out, OP1);
  not not_52 (not_52_out, OP2);
  not not_53 (not_53_out, OP4);
  not not_54 (not_54_out, OP5);
  not not_55 (not_55_out, F0);
  not not_56 (not_56_out, F2);
  not not_57 (not_57_out, F3);
  not not_58 (not_58_out, F4);
  not not_59 (not_59_out, OP0);
  not not_60 (not_60_out, OP1);
  not not_61 (not_61_out, OP2);
  not not_62 (not_62_out, OP4);
  not not_63 (not_63_out, OP5);
  not not_64 (not_64_out, F1);
  not not_65 (not_65_out, F3);
  not not_66 (not_66_out, F4);
  not not_67 (not_67_out, OP0);
  not not_68 (not_68_out, OP1);
  not not_69 (not_69_out, OP2);
  not not_70 (not_70_out, OP4);
  not not_71 (not_71_out, OP5);
  not not_72 (not_72_out, F0);
  not not_73 (not_73_out, F2);
  not not_74 (not_74_out, F3);
  not not_75 (not_75_out, F5);
  not not_76 (not_76_out, OP0);
  not not_77 (not_77_out, OP1);
  not not_78 (not_78_out, OP2);
  not not_79 (not_79_out, OP4);
  not not_80 (not_80_out, OP5);
  not not_81 (not_81_out, F2);
  not not_82 (not_82_out, F3);
  not not_83 (not_83_out, F4);
  not not_84 (not_84_out, F5);
  not not_85 (not_85_out, OP0);
  not not_86 (not_86_out, OP1);
  not not_87 (not_87_out, OP2);
  not not_88 (not_88_out, OP4);
  not not_89 (not_89_out, OP5);
  not not_90 (not_90_out, F2);
  not not_91 (not_91_out, F4);
  not not_92 (not_92_out, OP0);
  not not_93 (not_93_out, OP1);
  not not_94 (not_94_out, OP2);
  not not_95 (not_95_out, OP4);
  not not_96 (not_96_out, OP5);
  not not_97 (not_97_out, F3);
  not not_98 (not_98_out, F4);
  not not_99 (not_99_out, OP0);
  not not_100 (not_100_out, OP2);
  not not_101 (not_101_out, OP4);
  not not_102 (not_102_out, OP5);
  not not_103 (not_103_out, OP1);
  not not_104 (not_104_out, OP4);
  not not_105 (not_105_out, OP5);
  not not_106 (not_106_out, OP2);
  not not_107 (not_107_out, OP3);
  not not_108 (not_108_out, OP4);
  not not_109 (not_109_out, OP5);
  not not_110 (not_110_out, OP3);
  not not_111 (not_111_out, OP2);
  not not_112 (not_112_out, OP1);
  not not_113 (not_113_out, OP0);
  not not_114 (not_114_out, F5);
  not not_115 (not_115_out, F2);
  not not_116 (not_116_out, F1);
  not not_117 (not_117_out, F0);
  not not_118 (not_118_out, OP0);
  not not_119 (not_119_out, OP1);
  not not_120 (not_120_out, OP2);
  not not_121 (not_121_out, OP3);
  not not_122 (not_122_out, OP4);
  not not_123 (not_123_out, OP5);
  not not_124 (not_124_out, F0);
  not not_125 (not_125_out, F1);
  not not_126 (not_126_out, F4);
  not not_127 (not_127_out, F5);
  not not_128 (not_128_out, OP0);
  not not_129 (not_129_out, OP1);
  not not_130 (not_130_out, OP2);
  not not_131 (not_131_out, OP4);
  not not_132 (not_132_out, OP0);
  not not_133 (not_133_out, OP2);
  not not_134 (not_134_out, OP4);
  not not_135 (not_135_out, OP5);
  not not_136 (not_136_out, OP1);
  not not_137 (not_137_out, OP2);
  not not_138 (not_138_out, OP4);
  not not_139 (not_139_out, OP5);
  not not_140 (not_140_out, OP2);
  not not_141 (not_141_out, OP4);
  not not_142 (not_142_out, OP0);
  not not_143 (not_143_out, OP1);
  not not_144 (not_144_out, OP2);
  not not_145 (not_145_out, OP3);
  not not_146 (not_146_out, OP4);
  not not_147 (not_147_out, OP5);
  not not_148 (not_148_out, F0);
  not not_149 (not_149_out, F2);
  not not_150 (not_150_out, F3);
  not not_151 (not_151_out, F4);
  not not_152 (not_152_out, OP0);
  not not_153 (not_153_out, OP1);
  not not_154 (not_154_out, OP2);
  not not_155 (not_155_out, OP3);
  not not_156 (not_156_out, OP4);
  not not_157 (not_157_out, OP5);
  not not_158 (not_158_out, F1);
  not not_159 (not_159_out, F3);
  not not_160 (not_160_out, F4);
  not not_161 (not_161_out, OP0);
  not not_162 (not_162_out, OP1);
  not not_163 (not_163_out, OP2);
  not not_164 (not_164_out, OP3);
  not not_165 (not_165_out, OP4);
  not not_166 (not_166_out, OP5);
  not not_167 (not_167_out, F0);
  not not_168 (not_168_out, F2);
  not not_169 (not_169_out, F3);
  not not_170 (not_170_out, F5);
  not not_171 (not_171_out, OP0);
  not not_172 (not_172_out, OP1);
  not not_173 (not_173_out, OP2);
  not not_174 (not_174_out, OP3);
  not not_175 (not_175_out, OP4);
  not not_176 (not_176_out, OP5);
  not not_177 (not_177_out, F2);
  not not_178 (not_178_out, F3);
  not not_179 (not_179_out, F4);
  not not_180 (not_180_out, F5);
  not not_181 (not_181_out, OP0);
  not not_182 (not_182_out, OP1);
  not not_183 (not_183_out, OP2);
  not not_184 (not_184_out, OP3);
  not not_185 (not_185_out, OP4);
  not not_186 (not_186_out, OP5);
  not not_187 (not_187_out, F2);
  not not_188 (not_188_out, F4);
  not not_189 (not_189_out, OP0);
  not not_190 (not_190_out, OP1);
  not not_191 (not_191_out, OP2);
  not not_192 (not_192_out, OP3);
  not not_193 (not_193_out, OP4);
  not not_194 (not_194_out, OP5);
  not not_195 (not_195_out, F3);
  not not_196 (not_196_out, F4);
  not not_197 (not_197_out, OP0);
  not not_198 (not_198_out, OP1);
  not not_199 (not_199_out, OP3);
  not not_200 (not_200_out, OP4);
  not not_201 (not_201_out, OP5);
  not not_202 (not_202_out, OP1);
  not not_203 (not_203_out, OP3);
  not not_204 (not_204_out, OP4);
  not not_205 (not_205_out, OP5);
  not not_206 (not_206_out, OP0);
  not not_207 (not_207_out, OP1);
  not not_208 (not_208_out, OP2);
  not not_209 (not_209_out, OP3);
  not not_210 (not_210_out, OP4);
  not not_211 (not_211_out, OP5);
  not not_212 (not_212_out, F0);
  not not_213 (not_213_out, F1);
  not not_214 (not_214_out, F2);
  not not_215 (not_215_out, F4);
  not not_216 (not_216_out, F5);
  not not_217 (not_217_out, OP0);
  not not_218 (not_218_out, OP2);
  not not_219 (not_219_out, OP3);
  not not_220 (not_220_out, OP4);
  not not_221 (not_221_out, OP5);
  not not_222 (not_222_out, F0);
  not not_223 (not_223_out, F1);
  not not_224 (not_224_out, F2);
  not not_225 (not_225_out, F4);
  not not_226 (not_226_out, F5);
  not not_227 (not_227_out, OP2);
  not not_228 (not_228_out, OP3);
  not not_229 (not_229_out, OP4);
  not not_230 (not_230_out, OP5);
  not not_231 (not_231_out, OP2);
  not not_232 (not_232_out, OP3);
  not not_233 (not_233_out, OP4);
  not not_234 (not_234_out, OP5);
  and and_1 (MemToReg, OP0, OP1, not_1_out, not_2_out, not_3_out, OP5);
  and and_2 (and_2_out, not_4_out, not_5_out, not_6_out, OP3, not_7_out, OP5);
  and and_3 (and_3_out, OP0, OP1, not_8_out, OP3, not_9_out, OP5);
  and and_4 (DIVU, not_10_out, not_11_out, not_12_out, not_13_out, not_14_out, not_15_out, F0, F1, not_16_out, F3, F4, not_17_out);
  and and_5 (MFLO, not_18_out, not_19_out, not_20_out, not_21_out, not_22_out, not_23_out, not_24_out, F1, not_25_out, not_26_out, F4, not_27_out);
  and and_6 (BGEZ, OP0, not_28_out, not_29_out, not_30_out, not_31_out, not_32_out);
  and and_7 (SB, not_33_out, not_34_out, not_35_out, OP3, not_36_out, OP5);
  and and_8 (and_8_out, not_37_out, not_38_out, not_39_out, OP3, not_40_out);
  and and_9 (and_9_out, not_41_out, not_42_out, OP3, not_43_out, not_44_out);
  and and_10 (and_10_out, not_45_out, OP3, not_46_out, not_47_out);
  and and_11 (and_11_out, OP0, OP1, not_48_out, not_49_out, OP5);
  and and_12 (and_12_out, not_50_out, not_51_out, not_52_out, not_53_out, not_54_out, not_55_out, not_56_out, not_57_out, not_58_out);
  and and_13 (and_13_out, not_59_out, not_60_out, not_61_out, not_62_out, not_63_out, not_64_out, not_65_out, not_66_out, F5);
  and and_14 (and_14_out, not_67_out, not_68_out, not_69_out, not_70_out, not_71_out, not_72_out, F1, not_73_out, not_74_out, not_75_out);
  and and_15 (and_15_out, not_76_out, not_77_out, not_78_out, not_79_out, not_80_out, F1, not_81_out, not_82_out, not_83_out, not_84_out);
  and and_16 (and_16_out, not_85_out, not_86_out, not_87_out, not_88_out, not_89_out, F1, not_90_out, F3, not_91_out, F5);
  and and_17 (and_17_out, not_92_out, not_93_out, not_94_out, not_95_out, not_96_out, F0, F2, not_97_out, not_98_out, F5);
  and and_18 (and_18_out, not_99_out, not_100_out, OP3, not_101_out, not_102_out);
  and and_19 (and_19_out, not_103_out, OP3, not_104_out, not_105_out);
  and and_20 (and_20_out, OP0, OP1, not_106_out, not_107_out, not_108_out);
  and and_21 (ERET, not_109_out, OP4, not_110_out, not_111_out, not_112_out, not_113_out, not_114_out, F4, F3, not_115_out, not_116_out, not_117_out);
  and and_22 (SysCALL, not_118_out, not_119_out, not_120_out, not_121_out, not_122_out, not_123_out, not_124_out, not_125_out, F2, F3, not_126_out, not_127_out);
  and and_23 (and_23_out, not_128_out, not_129_out, not_130_out, OP3, not_131_out);
  and and_24 (and_24_out, not_132_out, not_133_out, OP3, not_134_out, not_135_out);
  and and_25 (and_25_out, not_136_out, not_137_out, OP3, not_138_out, not_139_out);
  and and_26 (and_26_out, OP0, OP1, not_140_out, not_141_out, OP5);
  and and_27 (and_27_out, not_142_out, not_143_out, not_144_out, not_145_out, not_146_out, not_147_out, not_148_out, not_149_out, not_150_out, not_151_out);
  and and_28 (and_28_out, not_152_out, not_153_out, not_154_out, not_155_out, not_156_out, not_157_out, not_158_out, not_159_out, not_160_out, F5);
  and and_29 (and_29_out, not_161_out, not_162_out, not_163_out, not_164_out, not_165_out, not_166_out, not_167_out, F1, not_168_out, not_169_out, not_170_out);
  and and_30 (and_30_out, not_171_out, not_172_out, not_173_out, not_174_out, not_175_out, not_176_out, F1, not_177_out, not_178_out, not_179_out, not_180_out);
  and and_31 (and_31_out, not_181_out, not_182_out, not_183_out, not_184_out, not_185_out, not_186_out, F1, not_187_out, F3, not_188_out, F5);
  and and_32 (and_32_out, not_189_out, not_190_out, not_191_out, not_192_out, not_193_out, not_194_out, F0, F2, not_195_out, not_196_out, F5);
  and and_33 (BEQ, not_197_out, not_198_out, OP2, not_199_out, not_200_out, not_201_out);
  and and_34 (BNE, OP0, not_202_out, OP2, not_203_out, not_204_out, not_205_out);
  and and_35 (JR, not_206_out, not_207_out, not_208_out, not_209_out, not_210_out, not_211_out, not_212_out, not_213_out, not_214_out, F3, not_215_out, not_216_out);
  and and_36 (and_36_out, not_217_out, not_218_out, not_219_out, not_220_out, not_221_out, not_222_out, not_223_out, not_224_out, F3, not_225_out, not_226_out);
  and and_37 (and_37_out, OP1, not_227_out, not_228_out, not_229_out, not_230_out);
  and and_38 (JAL, OP0, OP1, not_231_out, not_232_out, not_233_out, not_234_out);
  or or_1 (MemWrite, and_2_out, and_3_out);
  or or_2 (ALU_SRC, and_8_out, and_9_out, and_10_out, and_11_out);
  or or_3 (RegWrite, and_12_out, and_13_out, and_14_out, and_15_out, and_16_out, and_17_out, and_18_out, and_19_out, and_20_out);
  or or_4 (SignedExt, and_23_out, and_24_out, and_25_out, and_26_out);
  or or_5 (RegDst, and_27_out, and_28_out, and_29_out, and_30_out, and_31_out, and_32_out);
  or or_6 (JUMP, and_36_out, and_37_out);
endmodule

// ALU
module MIPS_ALU (
  input  [4:0] shamt,
  input  [31:0] X,
  input  [31:0] Y,
  input  [3:0] AluOP,
  output Equal,
  output [31:0] Result,
  output [31:0] Result_2
);

  wire [0:0] comparator_1_lt, comparator_2_lt;
  wire [31:0] adder_1_out, AND_out, divider_1_out, divider_1_rem, multiplier_1_cout, multiplier_1_out,
       NOR_out, OR_out, shifter_1_out, shifter_2_out, shifter_3_out, subtractor_1_out, XOR_out;

  assign AND_out = X & Y;  // AND_Gate AND, 32 bits wide
  assign OR_out = X | Y;  // OR_Gate OR, 32 bits wide
  Shifter #(.width(32), .shift("ll")) shifter_1 (.in(Y), .\dist (shamt), .out(shifter_1_out));
  Shifter #(.width(32), .shift("ar")) shifter_2 (.in(Y), .\dist (shamt), .out(shifter_2_out));
  Shifter #(.width(32), .shift("lr")) shifter_3 (.in(Y), .\dist (shamt), .out(shifter_3_out));
  Multiplier #(.width(32)) multiplier_1 (.a(X), .b(Y), .out(multiplier_1_out), .cout(multiplier_1_cout));  // open: cin
  Divider #(.width(32)) divider_1 (.a(X), .b(Y), .out(divider_1_out), .rem(divider_1_rem));  // open: upper
  Adder #(.width(32)) adder_1 (.a(X), .b(Y), .out(adder_1_out));  // open: cin, cout
  Subtractor #(.width(32)) subtractor_1 (.a(X), .b(Y), .out(subtractor_1_out));  // open: bin, bout
  assign XOR_out = X ^ Y;  // XOR_Gate XOR, 32 bits wide
  assign NOR_out = ~(X | Y);  // NOR_Gate NOR, 32 bits wide
  Comparator #(.width(32), .mode("twosComplement")) comparator_1 (
    .a(X), .b(Y), .eq(Equal), .lt(comparator_1_lt[0]));  // open: gt
  Comparator #(.width(32), .mode("unsigned")) comparator_2 (.a(X), .b(Y), .lt(comparator_2_lt[0]));  // open: gt, eq
  Multiplexer #(.select(4), .width(32), .disabled("Z"), .enable("false")) multiplexer_1 (
    .in0(shifter_1_out), .in1(shifter_2_out), .in2(shifter_3_out), .in3(multiplier_1_out),
    .in4(divider_1_out), .in5(adder_1_out), .in6(subtractor_1_out), .in7(AND_out), .in8(OR_out),
    .in9(XOR_out), .in10(NOR_out), .in11({{31{1'b0}}, comparator_1_lt[0]}),
    .in12({{31{1'b0}}, comparator_2_lt[0]}), .in13({32{1'b0}}), .in14({32{1'b0}}), .in15({32{1'b0}}),
    .out(Result), .sel(AluOP));
  Multiplexer #(.select(4), .width(32), .disabled("Z"), .enable("false")) multiplexer_2 (
    .in0({32{1'b0}}), .in1({32{1'b0}}), .in2({32{1'b0}}), .in3(multiplier_1_cout), .in4(divider_1_rem),
    .in5({32{1'b0}}), .in6({32{1'b0}}), .in7({32{1'b0}}), .in8({32{1'b0}}), .in9({32{1'b0}}),
    .in10({32{1'b0}}), .in11({32{1'b0}}), .in12({32{1'b0}}), .in13({32{1'b0}}), .in14({32{1'b0}}),
    .in15({32{1'b0}}), .out(Result_2), .sel(AluOP));

  // Other names for the same wires on the sheet: Result2[31:0] = Result_2; S[3:0] = AluOP

  // Notes on the sheet:
  //   不要改变此引脚区域内容，也不要改变ALU封装形式
  //   输入引脚
  //   输出引脚
endmodule

module MIPS_Regifile (
  input  [31:0] Din,
  input  Clk,
  input  WE,
  input  [4:0] R1_num,
  input  [4:0] W_num,
  input  [4:0] R2_num,
  output [31:0] R1,
  output [31:0] R2
);

  // RegisterFile registerfile_1: pin names not known; wires that end beside it: Din, Clk, WE, W_num, R1_num, R2_num, R1, R2
endmodule

module \理想流水线  (
  output RegWrite,
  output MemWrite,
  output [31:0] IF_PC,
  output [31:0] ID_PC,
  output [31:0] EX_PC,
  output [31:0] M_PC,
  output [31:0] WB_PC,
  output [31:0] RDin,
  output [31:0] MDin,
  output [31:0] LedData
);

  wire AluSrcB, and_3_out, and_4_out, Beq, Beq_EX, Bne, Bne_EX, CLK, clock_1_out, clock_2_out,
       comparator_1_eq, comparator_2_eq, comparator_2_lt, d_ff_1_q, en, EQUAL, ex_mem_1_jal_out,
       ex_mem_1_memtoreg_out, ex_mem_1_regdst_out, ex_mem_1_regwrite_out, ex_mem_1_syscall_out, Go,
       id_ex_1_alusrcb_out, id_ex_1_jal_out, id_ex_1_memtoreg_out, id_ex_1_regdst_out, id_ex_1_regwrite_out,
       id_ex_1_signedext_out, id_ex_1_syscall_out, IR1, IR2, IR3, JAL, JAL_WB, JMP, JMP_EX, JMP_IF, JR,
       JR_EX, LED_en, mem_wb_1_memtoreg_out, MemToReg, MemWrite_EX, MemWrite_t, nand_1_out, RegDst,
       RegDst_WB, RegWrite_t, RST, SignedExt, stop, stop_final, Syscall, W1, W2, W3;
  wire [3:0] AluOP, AluOP_EX;
  wire [4:0] id_ex_1_shamt_out, multiplexer_2_out, multiplexer_3_out, multiplexer_4_out, multiplexer_5_out,
       RD, RT;
  wire [9:0] ex_mem_1_alur_out_2;
  wire [12:0] CNT_num;
  wire [15:0] id_ex_1_imm_out, \LoadUse次数 , \总周期数 , \插入气泡数 , \无条件分支数 , \条件分支成功数 ;
  wire [31:0] a0, bit_extender_1_out, bit_extender_2_out, EX_IR, ex_mem_1_alur_out, ex_mem_1_pc_4_out, ID_IR,
       if_id_1_pc_4_out, IF_IR, J_JAL_PC, J_JAR_PC, JR_PC, MEM_IR, mem_wb_1_alur_out, mem_wb_1_memd_out,
       mem_wb_1_pc_4_out, mips_alu_1_result, multiplexer_1_out, multiplexer_6_out, multiplexer_7_out,
       multiplexer_8_out, PC_4, PC_4_EX, PC_imm, R2_EX, ram_1_data, shifter_1_out, v0, WB_IR;

  Button \u_总复位  (.out(RST));
  Button _1 (.out(IR1));
  Button _2 (.out(IR2));
  Button _3 (.out(IR3));
  // Probe on \总周期数 
  // Probe on \总周期数 
  // Probe on {JR_EX, JMP_EX, JMP_IF}
  Button \u_继续运行  (.out(Go));
  LED #(.active("true")) led_1 (.in(W1));
  LED #(.active("true")) led_2 (.in(W2));
  LED #(.active("true")) led_3 (.in(W3));
  Multiplexer #(.select(3), .width(32), .disabled("Z"), .enable("false")) multiplexer_1 (
    .in0(PC_4), .in1(PC_imm), .in2(J_JAR_PC), .in6(JR_PC), .out(multiplexer_1_out),
    .sel({JR_EX, JMP_EX, JMP_IF}));  // open: in3, in4, in5, in7
  Hex_Digit_Display hex_digit_display_1 (.value(LedData[31:28]));  // open: dp
  // Probe on IF_PC[19:0]
  // Mips_Probe mips_probe_1: pin names not known; wires that end beside it: IF_IR
  Register #(.width(32), .trigger("rising"), .Select("low")) PC (
    .D(multiplexer_1_out), .en(en), .Q(IF_PC), .clk(CLK));  // open: clr
  Adder #(.width(32)) adder_1 (.a(IF_PC), .b(32'h4), .out(PC_4));  // open: cin, cout
  Hex_Digit_Display hex_digit_display_2 (.value(LedData[27:24]));  // open: dp
  Hex_Digit_Display hex_digit_display_3 (.value(LedData[23:20]));  // open: dp
  // Probe on ID_PC[19:0]
  // Mips_Probe mips_probe_2: pin names not known; wires that end beside it: ID_IR
  Hex_Digit_Display hex_digit_display_4 (.value(LedData[15:12]));  // open: dp
  Hex_Digit_Display hex_digit_display_5 (.value(LedData[19:16]));  // open: dp
  ROM #(.addrWidth(10), .dataWidth(32), .Select("high")) rom_1 (.addr(IF_PC[11:2]), .data(IF_IR));
  Hex_Digit_Display hex_digit_display_6 (.value(LedData[11:8]));  // open: dp
  Hex_Digit_Display hex_digit_display_7 (.value(LedData[7:4]));  // open: dp
  Clock #(.highDuration(1), .lowDuration(1)) clock_1 (.out(clock_1_out));
  // Probe on EX_PC[19:0]
  // Mips_Probe mips_probe_3: pin names not known; wires that end beside it: clock_1_out, EX_IR, CLK
  Hex_Digit_Display hex_digit_display_8 (.value(LedData[3:0]));  // open: dp
  IF_ID if_id_1 (
    .PC_4_in(PC_4), .PC_in(IF_PC), .IR_in(IF_IR), .PC_4_out(if_id_1_pc_4_out), .PC_out(ID_PC),
    .IR_out(ID_IR), .Reset(RST), .CLK(CLK), .Enable(en));  // open: in_4, out_11
  // Probe on \总周期数 
  // Probe on M_PC[19:0]
  // Mips_Probe mips_probe_4: pin names not known; wires that end beside it: MEM_IR
  // Mips_Probe mips_probe_5: pin names not known; wires that end beside it: ID_IR, 5'b00010, 5'b00100
  // Probe on \总周期数 
  // Probe on \无条件分支数 
  // Probe on \条件分支成功数 
  // Probe on \插入气泡数 
  // Probe on \LoadUse次数 
  Multiplexer #(.select(1), .width(5), .disabled("Z"), .enable("false")) multiplexer_2 (
    .in0(RT), .in1(RD), .out(multiplexer_2_out), .sel(RegDst_WB));
  Comparator #(.width(32), .mode("twosComplement")) comparator_1 (
    .a(v0), .b(32'h22), .eq(comparator_1_eq));  // open: gt, lt
  // Probe on IF_PC[11:0]
  // Probe on WB_PC[19:0]
  // Mips_Probe mips_probe_6: pin names not known; wires that end beside it: {WB_IR[31:21], RT, RD, WB_IR[10:0]}
  \单周期硬布线控制器  \u_单周期硬布线控制器_1  (
    .Func(ID_IR[5:0]), .OP(ID_IR[31:26]), .ALU_OP(AluOP), .MemToReg(MemToReg), .MemWrite(MemWrite_t),
    .ALU_SRC(AluSrcB), .RegWrite(RegWrite_t), .SysCALL(Syscall), .SignedExt(SignedExt), .RegDst(RegDst),
    .JR(JR), .JMP(JMP), .Beq(Beq), .JAL(JAL), .Bne(Bne));  // open: DIVU, MFLO, BGEZ, SB, ERET
  Multiplexer #(.select(1), .width(5), .disabled("Z"), .enable("false")) multiplexer_3 (
    .in0(ID_IR[25:21]), .out(multiplexer_3_out), .sel(Syscall));  // open: in1
  Multiplexer #(.select(1), .width(5), .disabled("Z"), .enable("false")) multiplexer_4 (
    .in0(ID_IR[20:16]), .out(multiplexer_4_out), .sel(Syscall));  // open: in1
  Multiplexer #(.select(1), .width(5), .disabled("Z"), .enable("false")) multiplexer_5 (
    .in0(multiplexer_2_out), .in1({5{1'b1}}), .out(multiplexer_5_out), .sel(JAL_WB));
  and and_1 (stop, ~comparator_1_eq, Syscall);  // AND_Gate
  and and_2 (LED_en, comparator_1_eq, Syscall);
  Register #(.width(32), .trigger("rising"), .Select("low")) register_1 (
    .D(a0), .en(LED_en), .Q(LedData), .clk(CLK));  // open: clr
  // Probe on ID_PC[11:0]
  // Probe on EX_PC[11:0]
  MIPS_Regifile mips_regifile_1 (
    .Din(RDin), .Clk(CLK), .R1(v0), .R2(a0), .WE(RegWrite), .W_num(multiplexer_5_out),
    .R1_num(multiplexer_3_out), .R2_num(multiplexer_4_out));
  // Probe on M_PC[11:0]
  D_Flip_Flop #(.trigger("high"), .Pre_Clr_Positions("LEGACY"), .NegatePresetClear("false"), .enable("true"), .NewFFLayout("false")) d_ff_1 (.Q(d_ff_1_q));  // open: clk, D, Qn, preset, en, reset
  // Probe on 13'hc
  // Probe on WB_PC[11:0]
  Comparator #(.width(13), .mode("twosComplement")) comparator_2 (
    .a(CNT_num), .b(13'hc), .eq(comparator_2_eq), .lt(comparator_2_lt));  // open: gt
  Clock #(.highDuration(1), .lowDuration(1)) clock_2 (.out(clock_2_out));
  ID_EX id_ex_1 (
    .IR_in(ID_IR), .BEQ_in(Beq), .PC_in(ID_PC), .BNE_in(Bne), .R1_in(v0), .MemToReg_in(MemToReg),
    .MemWrite_in(MemWrite_t), .R2_in(a0), .AluSrcB_in(AluSrcB), .Imm_in(ID_IR[15:0]),
    .RegWrite_in(RegWrite_t), .Address_in({if_id_1_pc_4_out[31:28], ID_IR[25:0], 2'b00}), .JAL_in(JAL),
    .AluOP_in(AluOP), .RegDst_in(RegDst), .Shamt_in(ID_IR[10:6]), .Syscall_in(stop), .JMP_in(JMP),
    .JR_in(JR), .PC_4_in(if_id_1_pc_4_out), .signedext_in(SignedExt), .IR_out(EX_IR), .BEQ_out(Beq_EX),
    .PC_out(EX_PC), .BNE_out(Bne_EX), .R1_out(JR_PC), .MemToReg_out(id_ex_1_memtoreg_out),
    .MemWrite_out(MemWrite_EX), .R2_out(R2_EX), .AluSrcB_out(id_ex_1_alusrcb_out), .Imm_out(id_ex_1_imm_out),
    .RegWrite_out(id_ex_1_regwrite_out), .Address_out(J_JAL_PC), .JAL_out(id_ex_1_jal_out),
    .AluOP_out(AluOP_EX), .RegDst_out(id_ex_1_regdst_out), .Shamt_out(id_ex_1_shamt_out),
    .Syscall_out(id_ex_1_syscall_out), .JMP_out(JMP_EX), .JR_out(JR_EX), .PC_4_out(PC_4_EX),
    .signedext_out(id_ex_1_signedext_out), .Reset(RST), .Enable(en), .CLK(CLK));
  nand nand_1 (nand_1_out, d_ff_1_q, comparator_2_eq);
  Counter #(.width(13), .max('h1fff), .ongoal("stay"), .trigger("rising"), .behavior("old")) counter_1 (
    .count(comparator_2_lt), .Q(CNT_num), .clk(clock_2_out));  // open: load, D, carry, clr, preset
  assign CLK = nand_1_out ? clock_2_out : 1'bz;  // Controlled_Buffer controlled_buffer_1
  assign bit_extender_1_out = {{16{1'b0}}, id_ex_1_imm_out};  // Bit_Extender bit_extender_1
  assign bit_extender_2_out = {{16{id_ex_1_imm_out[15]}}, id_ex_1_imm_out};  // Bit_Extender bit_extender_2
  and and_3 (and_3_out, Beq_EX, EQUAL);
  and and_4 (and_4_out, Bne_EX, ~EQUAL);  // AND_Gate
  Pull_Resistor #(.pull(1)) pull_resistor_1 (.node(CLK));
  Multiplexer #(.select(1), .width(32), .disabled("Z"), .enable("false")) multiplexer_6 (
    .in0(R2_EX), .in1(multiplexer_7_out), .out(multiplexer_6_out), .sel(id_ex_1_alusrcb_out));
  Multiplexer #(.select(1), .width(32), .disabled("Z"), .enable("false")) multiplexer_7 (
    .in0(bit_extender_1_out), .in1(bit_extender_2_out), .out(multiplexer_7_out), .sel(id_ex_1_signedext_out));
  Shifter #(.width(32), .shift("ll")) shifter_1 (.in(bit_extender_2_out), .\dist (5'b00010), .out(shifter_1_out));
  or or_1 (JMP_IF, and_3_out, and_4_out);
  MIPS_ALU mips_alu_1 (
    .X(JR_PC), .Y(multiplexer_6_out), .AluOP(AluOP_EX), .Equal(EQUAL), .Result(mips_alu_1_result),
    .shamt(id_ex_1_shamt_out));  // open: Result_2
  Adder #(.width(32)) adder_2 (.a(shifter_1_out), .b(PC_4_EX), .out(PC_imm));  // open: cin, cout
  // Probe on mips_alu_1_result
  // Probe on R2_EX
  EX_MEM ex_mem_1 (
    .MemToReg_in(id_ex_1_memtoreg_out), .IR_in(EX_IR), .MemWrite_in(MemWrite_EX), .PC_in(EX_PC),
    .RegWrite_in(id_ex_1_regwrite_out), .R2_in(R2_EX), .JAL_in(id_ex_1_jal_out), .AluR_in(mips_alu_1_result),
    .RegDst_in(id_ex_1_regdst_out), .Syscall_in(id_ex_1_syscall_out), .PC_4_in(PC_4_EX),
    .MemToReg_out(ex_mem_1_memtoreg_out), .IR_out(MEM_IR), .MemWrite_out(MemWrite), .PC_out(M_PC),
    .RegWrite_out(ex_mem_1_regwrite_out), .R2_out(MDin), .JAL_out(ex_mem_1_jal_out),
    .AluR_out({ex_mem_1_alur_out[31:12], ex_mem_1_alur_out_2, ex_mem_1_alur_out[1:0]}),
    .RegDst_out(ex_mem_1_regdst_out), .Syscall_out(ex_mem_1_syscall_out), .PC_4_out(ex_mem_1_pc_4_out),
    .Reset(RST), .Enable(en), .CLK(CLK));  // open: _2out, _1in, W__in, _3in, _2out_2, _1out, W__out, _4out
  // Probe on MDin
  RAM #(.addrWidth(10), .dataWidth(32), .bus("separate"), .Select("high")) ram_1 (
    .addr(ex_mem_1_alur_out_2), .din(MDin), .data(ram_1_data), .str(MemWrite), .clk(CLK));  // open: sel, ld, clr
  MEM_WB mem_wb_1 (
    .MemToReg_in(ex_mem_1_memtoreg_out), .IR_in(MEM_IR), .RegWrite_in(ex_mem_1_regwrite_out), .PC_in(M_PC),
    .JAL_in(ex_mem_1_jal_out), .MemD_in(ram_1_data), .RegDst_in(ex_mem_1_regdst_out),
    .AluR_in({ex_mem_1_alur_out[31:12], ex_mem_1_alur_out_2, ex_mem_1_alur_out[1:0]}),
    .Syscall_in(ex_mem_1_syscall_out), .PC_4_in(ex_mem_1_pc_4_out), .MemToReg_out(mem_wb_1_memtoreg_out),
    .IR_out({WB_IR[31:21], RT, RD, WB_IR[10:0]}), .RegWrite_out(RegWrite), .PC_out(WB_PC), .JAL_out(JAL_WB),
    .MemD_out(mem_wb_1_memd_out), .RegDst_out(RegDst_WB), .AluR_out(mem_wb_1_alur_out),
    .Syscall_out(stop_final), .PC_4_out(mem_wb_1_pc_4_out), .Reset(RST), .Enable(en), .CLK(CLK));  // open: Halt_in, W__in, Interrupt_in, R2_in, Halt_out, W__out, Interrupt_out, R2_out
  or or_2 (en, ~stop_final, Go);  // OR_Gate
  Multiplexer #(.select(1), .width(32), .disabled("Z"), .enable("false")) multiplexer_8 (
    .in0(mem_wb_1_alur_out), .in1(mem_wb_1_memd_out), .out(multiplexer_8_out), .sel(mem_wb_1_memtoreg_out));
  Multiplexer #(.select(1), .width(32), .disabled("Z"), .enable("false")) multiplexer_9 (
    .in0(multiplexer_8_out), .in1(mem_wb_1_pc_4_out), .out(RDin), .sel(JAL_WB));
  // Probe on RDin

  // Other names for the same wires on the sheet: MEM_PC[31:0] = M_PC; MemWrite_MEM = MemWrite; PC[31:0] = IF_PC;
  //   RegWrite_WB = RegWrite; WB_IR[20:11] = {RT, RD}

  // Notes on the sheet:
  //   中断源
  //   时空图监测，可删除
  //   中断等待指示
  //   指令存储器
  //   数码管输出
  //   contents of rom_1 (hex, n*v repeats v):
  //   20100000 20110000 20120000 20130000 36100000 36310001 36520002 36730003 ae100000 ae110004 ae120008
  //   ae13000c 2002000a 20110000 20120000 20130000 c
  //   JMP
  //   JR
  //   OP
  //   Func
  //   OP
  //   Func
  //   rt
  //   rd
  //   shmat
  //   imm
  //   addr
  //   Beq
  //   Bne
  //   AluOP
  //   AluSrcB
  //   RegWrite
  //   JAL
  //   RegDst
  //   控制位
  //   MemToReg
  //   MemWrite
  //   流水调试日志用
  //   暂停节拍，不能为0
  //   戳工具置1进入计数暂停模式，ctrl+k时钟自动运行到对应节拍暂停
  //   ctrl+k关闭时钟连续运行，将控制位置零，进入单步调试模式调试
  //   用这个时钟源需要去掉电路中的其他时钟源
  //   可计数暂停的时钟源
  //   bne beq的转跳地址
  //   为方便自动评测，需要输出流水线各段保存的PC值，注意是PC不是PC+4，另外ID段寄存器写入信息，Mem段内存写入信息也要输出
  //   rt
  //   rd
endmodule

module \气泡流水线  (
  output RegWrite,
  output MemWrite,
  output [31:0] IF_PC,
  output [31:0] ID_PC,
  output [31:0] EX_PC,
  output [31:0] M_PC,
  output [31:0] WB_PC,
  output [31:0] RDin,
  output [31:0] MDin,
  output [31:0] LedData
);

  wire AluSrcB, and_1_out, and_2_out, and_5_out, and_6_out, Beq, Beq_EX, Bne, Bne_EX, CLK, clock_1_out,
       clock_2_out, comparator_1_eq, comparator_2_eq, comparator_2_lt, d_ff_1_q, en, EQUAL, ex_mem_1_jal_out,
       ex_mem_1_memtoreg_out, ex_mem_1_regdst_out, ex_mem_1_syscall_out, EX_RegWrite, Go,
       id_ex_1_alusrcb_out, id_ex_1_jal_out, id_ex_1_memtoreg_out, id_ex_1_regdst_out, id_ex_1_signedext_out,
       id_ex_1_syscall_out, IR1, IR2, IR3, JAL, JAL_WB, JMP, JMP_EX, JMP_IF, JR, JR_EX, LED_en, MEM_RegWrite,
       mem_wb_1_memtoreg_out, MemToReg, MemWrite_EX, MemWrite_t, nand_1_out, or_1_out, or_2_out, or_3_out,
       RegDst, RegDst_WB, RegWrite_t, RST, SignedExt, stop, stop_final, Syscall, W1, W2, W3, \分支成功 ,
       \寄存器_1_rs , \寄存器_1_rt , \数据冲突 ;
  wire [3:0] AluOP, AluOP_EX;
  wire [4:0] EX_REG_num, id_ex_1_shamt_out, MEM_REG_num, multiplexer_4_out, multiplexer_5_out,
       multiplexer_8_out, multiplexer_10_out, R1_num, R2_num, RD, RT;
  wire [9:0] ex_mem_1_alur_out_2;
  wire [12:0] CNT_num;
  wire [15:0] id_ex_1_imm_out, \LoadUse次数 , \总周期数 , \插入气泡数 , \无条件分支数 , \条件分支成功数 ;
  wire [31:0] a0, bit_extender_1_out, bit_extender_2_out, EX_IR, ex_mem_1_alur_out, ex_mem_1_pc_4_out, ID_IR,
       if_id_1_pc_4_out, IF_IR, J_JAL_PC, JR_PC, MEM_IR, mem_wb_1_alur_out, mem_wb_1_memd_out,
       mem_wb_1_pc_4_out, mips_alu_1_result, multiplexer_1_out, multiplexer_6_out, multiplexer_7_out,
       multiplexer_12_out, PC_4, PC_4_EX, PC_imm, R2_EX, ram_1_data, shifter_1_out, v0, WB_IR;

  Button \u_总复位  (.out(RST));
  Button _1 (.out(IR1));
  Button _2 (.out(IR2));
  Button _3 (.out(IR3));
  // Probe on \总周期数 
  // Probe on \总周期数 
  Button \u_继续运行  (.out(Go));
  LED #(.active("true")) led_1 (.in(W1));
  LED #(.active("true")) led_2 (.in(W2));
  LED #(.active("true")) led_3 (.in(W3));
  Hex_Digit_Display hex_digit_display_1 (.value(LedData[31:28]));  // open: dp
  // Probe on IF_PC[19:0]
  // Mips_Probe mips_probe_1: pin names not known; wires that end beside it: IF_IR
  Hex_Digit_Display hex_digit_display_2 (.value(LedData[27:24]));  // open: dp
  Hex_Digit_Display hex_digit_display_3 (.value(LedData[23:20]));  // open: dp
  // Probe on ID_PC[19:0]
  // Mips_Probe mips_probe_2: pin names not known; wires that end beside it: ID_IR
  // Probe on {JR_EX, JMP_EX, JMP_IF}
  Hex_Digit_Display hex_digit_display_4 (.value(LedData[15:12]));  // open: dp
  Hex_Digit_Display hex_digit_display_5 (.value(LedData[19:16]));  // open: dp
  Multiplexer #(.select(3), .width(32), .disabled("Z"), .enable("false")) multiplexer_1 (
    .in0(PC_4), .in1(PC_imm), .in2(J_JAL_PC), .in6(JR_PC), .out(multiplexer_1_out),
    .sel({JR_EX, JMP_EX, JMP_IF}));  // open: in3, in4, in5, in7
  Register #(.width(32), .trigger("rising"), .Select("low")) PC (
    .D(multiplexer_1_out), .en(and_1_out), .Q(IF_PC), .clk(CLK));  // open: clr
  and and_1 (and_1_out, en, ~\数据冲突 );  // AND_Gate
  Hex_Digit_Display hex_digit_display_6 (.value(LedData[11:8]));  // open: dp
  Hex_Digit_Display hex_digit_display_7 (.value(LedData[7:4]));  // open: dp
  Clock #(.highDuration(1), .lowDuration(1)) clock_1 (.out(clock_1_out));
  // Probe on EX_PC[19:0]
  // Mips_Probe mips_probe_3: pin names not known; wires that end beside it: EX_IR, clock_1_out, CLK
  Adder #(.width(32)) adder_1 (.a(IF_PC), .b(32'h4), .out(PC_4));  // open: cin, cout
  Hex_Digit_Display hex_digit_display_8 (.value(LedData[3:0]));  // open: dp
  ROM #(.addrWidth(10), .dataWidth(32), .Select("high")) rom_1 (.addr(IF_PC[11:2]), .data(IF_IR));
  // Probe on \总周期数 
  // Probe on M_PC[19:0]
  // Mips_Probe mips_probe_4: pin names not known; wires that end beside it: MEM_IR
  // Mips_Probe mips_probe_5: pin names not known; wires that end beside it: {32{1'b0}}
  or or_1 (or_1_out, \分支成功 , and_2_out);
  and and_2 (and_2_out, en, ~\数据冲突 );  // AND_Gate
  // Probe on \总周期数 
  // Probe on \无条件分支数 
  // Probe on \条件分支成功数 
  // Probe on \插入气泡数 
  // Probe on \LoadUse次数 
  or or_2 (or_2_out, RST, \分支成功 );
  IF_ID if_id_1 (
    .PC_4_in(PC_4), .PC_in(IF_PC), .IR_in(IF_IR), .PC_4_out(if_id_1_pc_4_out), .PC_out(ID_PC),
    .IR_out(ID_IR), .Reset(or_2_out), .CLK(CLK), .Enable(or_1_out));  // open: in_4, out_11
  // Probe on IF_PC[11:0]
  // Probe on WB_PC[19:0]
  // Mips_Probe mips_probe_6: pin names not known; wires that end beside it: {WB_IR[31:21], RT, RD, WB_IR[10:0]}
  // Probe on ID_PC[11:0]
  // Probe on EX_PC[11:0]
  // Mips_Probe mips_probe_7: pin names not known; wires that end beside it: ID_IR
  // Probe on M_PC[11:0]
  D_Flip_Flop #(.trigger("high"), .Pre_Clr_Positions("LEGACY"), .NegatePresetClear("false"), .enable("true"), .NewFFLayout("false")) d_ff_1 (.Q(d_ff_1_q));  // open: clk, D, Qn, preset, en, reset
  // Probe on 13'hc
  Multiplexer #(.select(1), .width(5), .disabled("Z"), .enable("false")) multiplexer_2 (
    .in0(ID_IR[25:21]), .in1(5'b00010), .out(R1_num), .sel(Syscall));
  Multiplexer #(.select(1), .width(5), .disabled("Z"), .enable("false")) multiplexer_3 (
    .in0(ID_IR[20:16]), .in1(5'b00100), .out(R2_num), .sel(Syscall));
  Multiplexer #(.select(1), .width(5), .disabled("Z"), .enable("false")) multiplexer_4 (
    .in0(RT), .in1(RD), .out(multiplexer_4_out), .sel(RegDst_WB));
  Multiplexer #(.select(1), .width(5), .disabled("Z"), .enable("false")) multiplexer_5 (
    .in0(multiplexer_4_out), .in1({5{1'b1}}), .out(multiplexer_5_out), .sel(JAL_WB));
  Comparator #(.width(32), .mode("twosComplement")) comparator_1 (
    .a(v0), .b(32'h22), .eq(comparator_1_eq));  // open: gt, lt
  Register #(.width(32), .trigger("rising"), .Select("low")) register_1 (
    .D(a0), .en(LED_en), .Q(LedData), .clk(CLK));  // open: clr
  // Probe on WB_PC[11:0]
  Comparator #(.width(13), .mode("twosComplement")) comparator_2 (
    .a(CNT_num), .b(13'hc), .eq(comparator_2_eq), .lt(comparator_2_lt));  // open: gt
  Clock #(.highDuration(1), .lowDuration(1)) clock_2 (.out(clock_2_out));
  \寄存器  \u_寄存器_1  (
    .OP0(ID_IR[26]), .OP1(ID_IR[27]), .OP2(ID_IR[28]), .OP3(ID_IR[29]), .OP4(ID_IR[30]), .OP5(ID_IR[31]),
    .F0(ID_IR[0]), .F1(ID_IR[1]), .F2(ID_IR[2]), .F3(ID_IR[3]), .F4(ID_IR[4]), .F5(ID_IR[5]),
    .rs(\寄存器_1_rs ), .rt(\寄存器_1_rt ));
  \单周期硬布线控制器  \u_单周期硬布线控制器_1  (
    .Func(ID_IR[5:0]), .OP(ID_IR[31:26]), .ALU_OP(AluOP), .MemToReg(MemToReg), .MemWrite(MemWrite_t),
    .ALU_SRC(AluSrcB), .RegWrite(RegWrite_t), .SysCALL(Syscall), .SignedExt(SignedExt), .RegDst(RegDst),
    .JR(JR), .JMP(JMP), .Beq(Beq), .JAL(JAL), .Bne(Bne));  // open: DIVU, MFLO, BGEZ, SB, ERET
  and and_3 (stop, ~comparator_1_eq, Syscall);  // AND_Gate
  and and_4 (LED_en, comparator_1_eq, Syscall);
  nand nand_1 (nand_1_out, d_ff_1_q, comparator_2_eq);
  Counter #(.width(13), .max('h1fff), .ongoal("stay"), .trigger("rising"), .behavior("old")) counter_1 (
    .count(comparator_2_lt), .Q(CNT_num), .clk(clock_2_out));  // open: load, D, carry, clr, preset
  Counter #(.width(16), .max('hffff), .ongoal("stay"), .trigger("rising"), .behavior("old")) counter_2 (
    .Q(\总周期数 ), .clk(clock_2_out));  // open: load, D, count, carry, clr, preset
  MIPS_Regifile mips_regifile_1 (
    .Din(RDin), .Clk(CLK), .R1(v0), .R2(a0), .WE(RegWrite), .W_num(multiplexer_5_out), .R1_num(R1_num),
    .R2_num(R2_num));
  assign CLK = nand_1_out ? clock_2_out : 1'bz;  // Controlled_Buffer controlled_buffer_1
  // Probe on R2_num
  or or_3 (or_3_out, RST, \数据冲突 , \分支成功 );
  ID_EX id_ex_1 (
    .IR_in(ID_IR), .BEQ_in(Beq), .PC_in(ID_PC), .BNE_in(Bne), .R1_in(v0), .MemToReg_in(MemToReg),
    .MemWrite_in(MemWrite_t), .R2_in(a0), .AluSrcB_in(AluSrcB), .Imm_in(ID_IR[15:0]),
    .RegWrite_in(RegWrite_t), .Address_in({if_id_1_pc_4_out[31:28], ID_IR[25:0], 2'b00}), .JAL_in(JAL),
    .AluOP_in(AluOP), .RegDst_in(RegDst), .Shamt_in(ID_IR[10:6]), .Syscall_in(stop), .JMP_in(JMP),
    .JR_in(JR), .PC_4_in(if_id_1_pc_4_out), .signedext_in(SignedExt), .IR_out(EX_IR), .BEQ_out(Beq_EX),
    .PC_out(EX_PC), .BNE_out(Bne_EX), .R1_out(JR_PC), .MemToReg_out(id_ex_1_memtoreg_out),
    .MemWrite_out(MemWrite_EX), .R2_out(R2_EX), .AluSrcB_out(id_ex_1_alusrcb_out), .Imm_out(id_ex_1_imm_out),
    .RegWrite_out(EX_RegWrite), .Address_out(J_JAL_PC), .JAL_out(id_ex_1_jal_out), .AluOP_out(AluOP_EX),
    .RegDst_out(id_ex_1_regdst_out), .Shamt_out(id_ex_1_shamt_out), .Syscall_out(id_ex_1_syscall_out),
    .JMP_out(JMP_EX), .JR_out(JR_EX), .PC_4_out(PC_4_EX), .signedext_out(id_ex_1_signedext_out),
    .Reset(or_3_out), .Enable(en), .CLK(CLK));
  Pull_Resistor #(.pull(1)) pull_resistor_1 (.node(CLK));
  // Probe on R1_num
  \数据冲突检测  \u_数据冲突检测_1  (
    .rs(\寄存器_1_rs ), .rt(\寄存器_1_rt ), .r1_num(R1_num), .r2_num(R2_num), .EX_REG_num(EX_REG_num),
    .EX_RegWrite(EX_RegWrite), .MEM_REG_num(MEM_REG_num), .MEM_RegWrite(MEM_RegWrite), .\数据冲突 (\数据冲突 ));
  // Probe on nothing
  assign bit_extender_1_out = {{16{1'b0}}, id_ex_1_imm_out};  // Bit_Extender bit_extender_1
  assign bit_extender_2_out = {{16{id_ex_1_imm_out[15]}}, id_ex_1_imm_out};  // Bit_Extender bit_extender_2
  Multiplexer #(.select(1), .width(32), .disabled("Z"), .enable("false")) multiplexer_6 (
    .in0(bit_extender_1_out), .in1(bit_extender_2_out), .out(multiplexer_6_out), .sel(id_ex_1_signedext_out));
  and and_5 (and_5_out, Beq_EX, EQUAL);
  or or_4 (JMP_IF, and_5_out, and_6_out);
  and and_6 (and_6_out, Bne_EX, ~EQUAL);  // AND_Gate
  Multiplexer #(.select(1), .width(32), .disabled("Z"), .enable("false")) multiplexer_7 (
    .in0(R2_EX), .in1(multiplexer_6_out), .out(multiplexer_7_out), .sel(id_ex_1_alusrcb_out));
  Shifter #(.width(32), .shift("ll")) shifter_1 (.in(bit_extender_2_out), .\dist (5'b00010), .out(shifter_1_out));
  or or_5 (\分支成功 , JMP_EX, JMP_IF);
  MIPS_ALU mips_alu_1 (
    .X(JR_PC), .Y(multiplexer_7_out), .AluOP(AluOP_EX), .Equal(EQUAL), .Result(mips_alu_1_result),
    .shamt(id_ex_1_shamt_out));  // open: Result_2
  Adder #(.width(32)) adder_2 (.a(shifter_1_out), .b(PC_4_EX), .out(PC_imm));  // open: cin, cout
  Multiplexer #(.select(1), .width(5), .disabled("Z"), .enable("false")) multiplexer_8 (
    .in0(EX_IR[20:16]), .in1(EX_IR[15:11]), .out(multiplexer_8_out), .sel(id_ex_1_regdst_out));
  Multiplexer #(.select(1), .width(5), .disabled("Z"), .enable("false")) multiplexer_9 (
    .in0(multiplexer_8_out), .in1({5{1'b1}}), .out(EX_REG_num), .sel(id_ex_1_jal_out));
  EX_MEM ex_mem_1 (
    .MemToReg_in(id_ex_1_memtoreg_out), .IR_in(EX_IR), .MemWrite_in(MemWrite_EX), .PC_in(EX_PC),
    .RegWrite_in(EX_RegWrite), .R2_in(R2_EX), .JAL_in(id_ex_1_jal_out), .AluR_in(mips_alu_1_result),
    .RegDst_in(id_ex_1_regdst_out), .Syscall_in(id_ex_1_syscall_out), .PC_4_in(PC_4_EX),
    .MemToReg_out(ex_mem_1_memtoreg_out), .IR_out(MEM_IR), .MemWrite_out(MemWrite), .PC_out(M_PC),
    .RegWrite_out(MEM_RegWrite), .R2_out(MDin), .JAL_out(ex_mem_1_jal_out),
    .AluR_out({ex_mem_1_alur_out[31:12], ex_mem_1_alur_out_2, ex_mem_1_alur_out[1:0]}),
    .RegDst_out(ex_mem_1_regdst_out), .Syscall_out(ex_mem_1_syscall_out), .PC_4_out(ex_mem_1_pc_4_out),
    .Reset(RST), .Enable(en), .CLK(CLK));  // open: _2out, _1in, W__in, _3in, _2out_2, _1out, W__out, _4out
  RAM #(.addrWidth(10), .dataWidth(32), .bus("separate"), .Select("high")) ram_1 (
    .addr(ex_mem_1_alur_out_2), .din(MDin), .data(ram_1_data), .str(MemWrite), .clk(CLK));  // open: sel, ld, clr
  Multiplexer #(.select(1), .width(5), .disabled("Z"), .enable("false")) multiplexer_10 (
    .in0(MEM_IR[20:16]), .in1(MEM_IR[15:11]), .out(multiplexer_10_out), .sel(ex_mem_1_regdst_out));
  Multiplexer #(.select(1), .width(5), .disabled("Z"), .enable("false")) multiplexer_11 (
    .in0(multiplexer_10_out), .in1({5{1'b1}}), .out(MEM_REG_num), .sel(ex_mem_1_jal_out));
  MEM_WB mem_wb_1 (
    .MemToReg_in(ex_mem_1_memtoreg_out), .IR_in(MEM_IR), .RegWrite_in(MEM_RegWrite), .PC_in(M_PC),
    .JAL_in(ex_mem_1_jal_out), .MemD_in(ram_1_data), .RegDst_in(ex_mem_1_regdst_out),
    .AluR_in({ex_mem_1_alur_out[31:12], ex_mem_1_alur_out_2, ex_mem_1_alur_out[1:0]}),
    .Syscall_in(ex_mem_1_syscall_out), .PC_4_in(ex_mem_1_pc_4_out), .MemToReg_out(mem_wb_1_memtoreg_out),
    .IR_out({WB_IR[31:21], RT, RD, WB_IR[10:0]}), .RegWrite_out(RegWrite), .PC_out(WB_PC), .JAL_out(JAL_WB),
    .MemD_out(mem_wb_1_memd_out), .RegDst_out(RegDst_WB), .AluR_out(mem_wb_1_alur_out),
    .Syscall_out(stop_final), .PC_4_out(mem_wb_1_pc_4_out), .Reset(RST), .Enable(en), .CLK(CLK));  // open: Halt_in, W__in, Interrupt_in, R2_in, Halt_out, W__out, Interrupt_out, R2_out
  or or_6 (en, ~stop_final, Go);  // OR_Gate
  Multiplexer #(.select(1), .width(32), .disabled("Z"), .enable("false")) multiplexer_12 (
    .in0(mem_wb_1_alur_out), .in1(mem_wb_1_memd_out), .out(multiplexer_12_out), .sel(mem_wb_1_memtoreg_out));
  // Probe on RDin
  Multiplexer #(.select(1), .width(32), .disabled("Z"), .enable("false")) multiplexer_13 (
    .in0(multiplexer_12_out), .in1(mem_wb_1_pc_4_out), .out(RDin), .sel(JAL_WB));

  // Other names for the same wires on the sheet: MEM_PC[31:0] = M_PC; MemWrite_MEM = MemWrite; PC[31:0] = IF_PC;
  //   RegWrite_WB = RegWrite; WB_IR[20:11] = {RT, RD}

  // Notes on the sheet:
  //   中断源
  //   时空图监测，可删除
  //   中断等待指示
  //   数码管输出
  //   指令存储器
  //   contents of rom_1 (hex, n*v repeats v):
  //   20110001 8000c05 20110001 20120002 20130003 8000c09 20110001 20120002 20130003 8000c0d 20110001
  //   20120002 20130003 8000c11 20110001 20120002 20130003 c000cb8 20100001 20110001 118fc0 112020
  //   20020022 c 118882 12200001 8000c15 112020 20020022 c 20110001 118880 112020 20020022 c 12200001
  //   8000c1f 20110001 118fc0 112020 20020022 c 1188c3 112020 20020022 c 118903 112020 20020022 c 118903
  //   112020 20020022 c 118903 112020 20020022 c 118903 112020 20020022 c 118903 112020 20020022 c 118903
  //   112020 20020022 c 118903 112020 20020022 c 20100001 109fc0 139fc3 8021 2012000c 24160003 26100001
  //   3210000f 20080008 20090001 139900 2709825 132020 20020022 c 1094022 1500fff9 22100001 2018000f
  //   2188024 108700 20080008 20090001 139902 2709825 132021 20020022 c 1094022 1500fff9 108702 2c9b022
  //   12c00001 8000c50 4020 1084027 84400 3508ffff 82021 20020022 c 2010ffff 20110000 ae300000 22100001
  //   22310004 ae300000 22100001 22310004 ae300000 22100001 22310004 ae300000 22100001 22310004 ae300000
  //   22100001 22310004 ae300000 22100001 22310004 ae300000 22100001 22310004 ae300000 22100001 22310004
  //   ae300000 22100001 22310004 ae300000 22100001 22310004 ae300000 22100001 22310004 ae300000 22100001
  //   22310004 ae300000 22100001 22310004 ae300000 22100001 22310004 ae300000 22100001 22310004 ae300000
  //   22100001 22310004 22100001 8020 2011003c 8e130000 8e340000 274402a 11000002 ae330000 ae140000
  //   2231fffc 1611fff8 102020 20020022 c 22100004 2011003c 1611fff2 20020032 c 20100000 22100001 102020
  //   20020022 c 22100002 102020 20020022 c 22100003 102020 20020022 c 22100004 102020 20020022 c 22100005
  //   102020 20020022 c 22100006 102020 20020022 c 22100007 102020 20020022 c 22100008 102020 20020022
  //   20020022 c 3e00008
  //   控制位
  //   OP
  //   Func
  //   rt
  //   rd
  //   shmat
  //   imm
  //   addr
  //   流水调试日志用
  //   暂停节拍，不能为0
  //   JMP
  //   JR
  //   OP
  //   Func
  //   戳工具置1进入计数暂停模式，ctrl+k时钟自动运行到对应节拍暂停
  //   ctrl+k关闭时钟连续运行，将控制位置零，进入单步调试模式调试
  //   Beq
  //   Bne
  //   MemToReg
  //   MemWrite
  //   AluOP
  //   AluSrcB
  //   RegWrite
  //   JAL
  //   RegDst
  //   可计数暂停的时钟源
  //   为方便自动评测，需要输出流水线各段保存的PC值，注意是PC不是PC+4，另外ID段寄存器写入信息，Mem段内存写入信息也要输出
  //   bne beq的转跳地址
  //   rt
  //   rt
  //   rd
  //   rt
  //   rd
endmodule

module \重定向流水线  (
  output RegWrite,
  output MemWrite,
  output [31:0] IF_PC,
  output [31:0] ID_PC,
  output [31:0] EX_PC,
  output [31:0] M_PC,
  output [31:0] WB_PC,
  output [31:0] RDin,
  output [31:0] MDin,
  output [31:0] LedData
);

  wire CLK, clock_2_out, comparator_1_eq, comparator_1_lt, d_ff_1_q, Go, IR1, IR2, IR3, nand_1_out, RST, W1,
       W2, W3;
  wire [12:0] CNT_num;
  wire [15:0] \LoadUse次数 , \总周期数 , \插入气泡数 , \无条件分支数 , \条件分支成功数 ;
  wire [31:0] EX_IR, ID_IR, IF_IR, MEM_IR, WB_IR;

  Button \u_总复位  (.out(RST));
  Button _1 (.out(IR1));
  Button _2 (.out(IR2));
  Button _3 (.out(IR3));
  // Probe on \总周期数 
  // Probe on \总周期数 
  Button \u_继续运行  (.out(Go));
  LED #(.active("true")) led_1 (.in(W1));
  LED #(.active("true")) led_2 (.in(W2));
  LED #(.active("true")) led_3 (.in(W3));
  Hex_Digit_Display hex_digit_display_1 (.value(LedData[31:28]));  // open: dp
  // Probe on IF_PC[19:0]
  // Mips_Probe mips_probe_1: pin names not known; wires that end beside it: IF_IR
  Hex_Digit_Display hex_digit_display_2 (.value(LedData[23:20]));  // open: dp
  Hex_Digit_Display hex_digit_display_3 (.value(LedData[27:24]));  // open: dp
  // Probe on ID_PC[19:0]
  // Mips_Probe mips_probe_2: pin names not known; wires that end beside it: ID_IR
  Hex_Digit_Display hex_digit_display_4 (.value(LedData[19:16]));  // open: dp
  Hex_Digit_Display hex_digit_display_5 (.value(LedData[15:12]));  // open: dp
  Hex_Digit_Display hex_digit_display_6 (.value(LedData[11:8]));  // open: dp
  Hex_Digit_Display hex_digit_display_7 (.value(LedData[7:4]));  // open: dp
  Clock #(.highDuration(1), .lowDuration(1)) clock_1 (.out(CLK));
  // Probe on EX_PC[19:0]
  // Mips_Probe mips_probe_3: pin names not known; wires that end beside it: EX_IR
  Hex_Digit_Display hex_digit_display_8 (.value(LedData[3:0]));  // open: dp
  // Probe on \总周期数 
  // Probe on M_PC[19:0]
  // Mips_Probe mips_probe_4: pin names not known; wires that end beside it: MEM_IR
  // Probe on \总周期数 
  // Probe on \无条件分支数 
  // Probe on \条件分支成功数 
  // Probe on \插入气泡数 
  // Probe on \LoadUse次数 
  // Probe on IF_PC[11:0]
  // Probe on WB_PC[19:0]
  // Mips_Probe mips_probe_5: pin names not known; wires that end beside it: WB_IR
  // Probe on ID_PC[11:0]
  // Probe on EX_PC[11:0]
  // Probe on M_PC[11:0]
  D_Flip_Flop #(.trigger("high"), .Pre_Clr_Positions("LEGACY"), .NegatePresetClear("false"), .enable("true"), .NewFFLayout("false")) d_ff_1 (.Q(d_ff_1_q));  // open: clk, D, Qn, preset, en, reset
  // Probe on 13'hc
  // Probe on WB_PC[11:0]
  Comparator #(.width(13), .mode("twosComplement")) comparator_1 (
    .a(CNT_num), .b(13'hc), .eq(comparator_1_eq), .lt(comparator_1_lt));  // open: gt
  Clock #(.highDuration(1), .lowDuration(1)) clock_2 (.out(clock_2_out));
  nand nand_1 (nand_1_out, d_ff_1_q, comparator_1_eq);
  Counter #(.width(13), .max('h1fff), .ongoal("stay"), .trigger("rising"), .behavior("old")) counter_1 (
    .count(comparator_1_lt), .Q(CNT_num), .clk(clock_2_out));  // open: load, D, carry, clr, preset
  assign CLK = nand_1_out ? clock_2_out : 1'bz;  // Controlled_Buffer controlled_buffer_1
  Pull_Resistor #(.pull(1)) pull_resistor_1 (.node(CLK));

  // Other names for the same wires on the sheet: MEM_PC[31:0] = M_PC

  // Notes on the sheet:
  //   中断源
  //   时空图监测，可删除
  //   中断等待指示
  //   数码管输出
  //   控制位
  //   流水调试日志用
  //   暂停节拍，不能为0
  //   戳工具置1进入计数暂停模式，ctrl+k时钟自动运行到对应节拍暂停
  //   ctrl+k关闭时钟连续运行，将控制位置零，进入单步调试模式调试
  //   可计数暂停的时钟源
  //   为方便自动评测，需要输出流水线各段保存的PC值，注意是PC不是PC+4，另外ID段寄存器写入信息，Mem段内存写入信息也要输出
endmodule

module \中断按键参考电路  (
  input  \同步清零信号 ,
  output \与中断屏蔽位与 
);

  wire \_1号中断_out , and_1_out, clock_1_out, d_ff_1_q, or_1_out, or_2_out;

  Clock #(.highDuration(1), .lowDuration(1)) clock_1 (.out(clock_1_out));
  Button \_1号中断  (.out(\_1号中断_out ));
  LED #(.active("true")) \_1号中断等待指示灯  (.in(or_1_out));
  or or_1 (or_1_out, \与中断屏蔽位与 , d_ff_1_q);
  D_Flip_Flop #(.trigger("rising"), .Pre_Clr_Positions("LEGACY"), .NegatePresetClear("false"), .enable("true"), .NewFFLayout("false")) d_ff_1 (
    .clk(\_1号中断_out ), .D(1'b1), .Q(d_ff_1_q), .reset(\与中断屏蔽位与 ));  // open: Qn, preset, en
  or or_2 (or_2_out, d_ff_1_q, \与中断屏蔽位与 );
  and and_1 (and_1_out, or_2_out, ~\同步清零信号 );  // AND_Gate
  D_Flip_Flop #(.trigger("rising"), .Pre_Clr_Positions("LEGACY"), .NegatePresetClear("false"), .enable("true"), .NewFFLayout("false")) IR1 (
    .clk(clock_1_out), .D(and_1_out), .Q(\与中断屏蔽位与 ));  // open: Qn, preset, en, reset

  // Notes on the sheet:
  //   中断信号采样参考电路
  //   Reset 
endmodule

module \单周期MIPS_单级中断  (
  input  IR1,
  input  IR2,
  input  IR3,
  output RegWrite,
  output MemWrite,
  output [31:0] PC,
  output [31:0] IR,
  output [31:0] RDin,
  output [31:0] MDin,
  output [31:0] LedData
);

  wire AluSrcB, and_1_out, and_2_out, and_3_out, and_10_out, and_11_out, and_12_out, Beq, BGEZ, Bne, CLK,
       clock_2_out, comparator_1_eq, comparator_2_eq, comparator_3_eq, comparator_4_eq, comparator_5_eq,
       comparator_5_lt, comparator_6_eq, comparator_7_eq, comparator_7_gt, d_ff_1_q, decoder_1_out0,
       decoder_1_out1, decoder_1_out2, DIVU, EQUAL, ERET, Go, IE, IE_q, \int , IR1_t, IR2_t, IR3_t, IRA, IRB,
       IRC, JAL, JMP, JMP_IF, JR, LED_en, MemToReg, MFLO, multiplexer_3_out, nand_1_out, not_1_out, or_1_out,
       or_2_out, or_9_out, or_10_out, or_11_out, or_12_out, priority_encoder_1_gs, RegDst, register_1_q,
       register_2_q, register_3_q, register_4_q, register_5_q, register_7_q, register_8_q, register_9_q,
       register_10_q, register_11_q, SB, SignedExt, stop, Syscall, W1, W2, W3, \同步清零1 , \同步清零2 , \同步清零3 ;
  wire [1:0] priority_encoder_1_out, register_12_q;
  wire [3:0] AluOP;
  wire [4:0] multiplexer_5_out, multiplexer_6_out, multiplexer_7_out, multiplexer_8_out;
  wire [12:0] CNT_num;
  wire [15:0] \总周期数 ;
  wire [27:0] PC_4;
  wire [31:0] a0, bit_extender_1_out, bit_extender_2_out, high_out, int_PC, JR_PC, low_out, mem_read,
       multiplexer_2_out, multiplexer_4_out, multiplexer_9_out, multiplexer_10_out, multiplexer_13_out,
       multiplexer_14_out, multiplexer_15_out, PC_imm, PC_save, re_PC, result1, result2, shifter_1_out;
  wire [31:28] J_JAR_PC;

  Clock #(.highDuration(1), .lowDuration(1)) clock_1 ();  // open: out
  Button _1 ();  // open: out
  Button _2 ();  // open: out
  Button _3 ();  // open: out
  // Probe on {JR, JMP, JMP_IF}
  Button \u_继续运行  (.out(Go));
  LED #(.active("true")) led_1 (.in(W1));
  LED #(.active("true")) led_2 (.in(W2));
  LED #(.active("true")) led_3 (.in(W3));
  Multiplexer #(.select(3), .width(32), .disabled("Z"), .enable("false")) multiplexer_1 (
    .in0({J_JAR_PC, PC_4}), .in1(PC_imm), .in2({J_JAR_PC, IR[25:0], 2'b00}), .in6(JR_PC), .out(PC_save),
    .sel({JR, JMP, JMP_IF}));  // open: in3, in4, in5, in7
  Hex_Digit_Display hex_digit_display_1 (.value(LedData[31:28]));  // open: dp
  Comparator #(.width(16), .mode("twosComplement")) comparator_1 (
    .a(16'h23b), .b(\总周期数 ), .eq(comparator_1_eq));  // open: gt, lt
  Comparator #(.width(16), .mode("twosComplement")) comparator_2 (
    .a(\总周期数 ), .b(16'h1), .eq(comparator_2_eq));  // open: gt, lt
  Comparator #(.width(16), .mode("twosComplement")) comparator_3 (
    .a(\总周期数 ), .b(16'h4), .eq(comparator_3_eq));  // open: gt, lt
  Comparator #(.width(16), .mode("twosComplement")) comparator_4 (
    .a(\总周期数 ), .b(16'h7), .eq(comparator_4_eq));  // open: gt, lt
  D_Flip_Flop #(.trigger("high"), .Pre_Clr_Positions("LEGACY"), .NegatePresetClear("false"), .enable("true"), .NewFFLayout("false")) d_ff_1 (.Q(d_ff_1_q));  // open: clk, D, Qn, preset, en, reset
  // Probe on 13'h368
  Adder #(.width(32)) adder_1 (.a(PC), .b(32'h4), .out({J_JAR_PC, PC_4}));  // open: cin, cout
  Multiplexer #(.select(1), .width(32), .disabled("Z"), .enable("false")) multiplexer_2 (
    .in0(PC_save), .in1(re_PC), .out(multiplexer_2_out), .sel(ERET));
  Register #(.width(1), .trigger("rising"), .Select("low")) register_1 (
    .D(1'b1), .Q(register_1_q), .clk(\int ), .clr(register_2_q));  // open: en
  Register #(.width(1), .trigger("rising"), .Select("low")) register_2 (
    .D(1'b1), .Q(register_2_q), .clk(multiplexer_3_out), .clr(register_2_q));  // open: en
  Multiplexer #(.select(1), .width(1), .disabled("Z"), .enable("false")) multiplexer_3 (
    .in0(1'b1), .in1(CLK), .out(multiplexer_3_out), .sel(register_1_q));
  Hex_Digit_Display hex_digit_display_2 (.value(LedData[23:20]));  // open: dp
  Hex_Digit_Display hex_digit_display_3 (.value(LedData[27:24]));  // open: dp
  or or_1 (or_1_out, comparator_1_eq, comparator_2_eq);
  assign IRA = or_1_out ? ~CLK : 1'bz;  // Controlled_Inverter controlled_inverter_1
  assign IRB = comparator_3_eq ? ~CLK : 1'bz;  // Controlled_Inverter controlled_inverter_2
  assign IRC = comparator_4_eq ? ~CLK : 1'bz;  // Controlled_Inverter controlled_inverter_3
  Comparator #(.width(13), .mode("twosComplement")) comparator_5 (
    .a(CNT_num), .b(13'h368), .eq(comparator_5_eq), .lt(comparator_5_lt));  // open: gt
  Clock #(.highDuration(1), .lowDuration(1)) clock_2 (.out(clock_2_out));
  Multiplexer #(.select(1), .width(32), .disabled("Z"), .enable("false")) multiplexer_4 (
    .in0(multiplexer_2_out), .in1(int_PC), .out(multiplexer_4_out), .sel(register_1_q));
  Hex_Digit_Display hex_digit_display_4 (.value(LedData[19:16]));  // open: dp
  Hex_Digit_Display hex_digit_display_5 (.value(LedData[15:12]));  // open: dp
  Pull_Resistor #(.pull(0)) pull_resistor_1 (.node(IRA));
  Pull_Resistor #(.pull(0)) pull_resistor_2 (.node(IRB));
  Pull_Resistor #(.pull(0)) pull_resistor_3 (.node(IRC));
  Counter #(.width(13), .max('h1fff), .ongoal("stay"), .trigger("rising"), .behavior("old")) counter_1 (
    .count(comparator_5_lt), .Q(CNT_num), .clk(clock_2_out));  // open: load, D, carry, clr, preset
  // Probe on {J_JAR_PC, PC_4}
  // Probe on multiplexer_4_out
  Hex_Digit_Display hex_digit_display_6 (.value(LedData[7:4]));  // open: dp
  Hex_Digit_Display hex_digit_display_7 (.value(LedData[11:8]));  // open: dp
  // Probe on \总周期数 
  Counter #(.width(16), .max('hffff), .ongoal("wrap"), .trigger("rising"), .behavior("new")) counter_2 (.clk(CLK));  // open: load, D, count, Q, carry, clr, preset, down
  Counter #(.width(16), .max('hffff), .ongoal("stay"), .trigger("rising"), .behavior("old")) counter_3 (
    .Q(\总周期数 ), .clk(clock_2_out));  // open: load, D, count, carry, clr, preset
  nand nand_1 (nand_1_out, d_ff_1_q, comparator_5_eq);
  Hex_Digit_Display hex_digit_display_8 (.value(LedData[3:0]));  // open: dp
  assign CLK = nand_1_out ? clock_2_out : 1'bz;  // Controlled_Buffer controlled_buffer_1
  Pull_Resistor #(.pull(1)) pull_resistor_4 (.node(CLK));
  // Mips_Probe mips_probe_1: pin names not known; wires that end beside it: 32'h8000c07, PC[11:2]
  Register #(.width(32), .trigger("rising"), .Select("low")) u_PC (
    .D(multiplexer_4_out), .en(or_2_out), .Q(PC), .clk(CLK));  // open: clr
  or or_2 (or_2_out, ~stop, Go);  // OR_Gate
  // Probe on PC
  or or_3 (IR1_t, IR1, IRA);
  or or_4 (IR2_t, IR2, IRB);
  // Mips_Probe mips_probe_2: pin names not known; wires that end beside it: IR
  ROM #(.addrWidth(10), .dataWidth(32), .Select("high")) rom_1 (.addr(PC[11:2]), .data(IR));
  Register #(.width(1), .trigger("rising"), .Select("low")) register_3 (
    .D(1'b1), .Q(register_3_q), .clk(IR1_t), .clr(register_7_q));  // open: en
  or or_5 (W1, register_3_q, register_7_q);
  Register #(.width(1), .trigger("rising"), .Select("low")) register_4 (
    .D(1'b1), .Q(register_4_q), .clk(IR2_t), .clr(register_8_q));  // open: en
  or or_6 (W2, register_4_q, register_8_q);
  Register #(.width(1), .trigger("rising"), .Select("low")) register_5 (
    .D(1'b1), .Q(register_5_q), .clk(IR3_t), .clr(register_9_q));  // open: en
  or or_7 (W3, register_5_q, register_9_q);
  or or_8 (IR3_t, IR3, IRC);
  or or_9 (or_9_out, register_3_q, register_7_q);
  or or_10 (or_10_out, register_4_q, register_8_q);
  or or_11 (or_11_out, register_5_q, register_9_q);
  \单周期硬布线控制器  \u_单周期硬布线控制器_1  (
    .Func(IR[5:0]), .OP(IR[31:26]), .ALU_OP(AluOP), .MemToReg(MemToReg), .MemWrite(MemWrite),
    .ALU_SRC(AluSrcB), .RegWrite(RegWrite), .SysCALL(Syscall), .SignedExt(SignedExt), .RegDst(RegDst),
    .JR(JR), .JMP(JMP), .Beq(Beq), .JAL(JAL), .Bne(Bne), .DIVU(DIVU), .MFLO(MFLO), .BGEZ(BGEZ), .SB(SB),
    .ERET(ERET));
  Multiplexer #(.select(1), .width(5), .disabled("Z"), .enable("false")) multiplexer_5 (
    .in0(IR[25:21]), .in1(5'b00010), .out(multiplexer_5_out), .sel(Syscall));
  // Probe on multiplexer_5_out
  Multiplexer #(.select(1), .width(5), .disabled("Z"), .enable("false")) multiplexer_6 (
    .in0(IR[20:16]), .in1(5'b00100), .out(multiplexer_6_out), .sel(Syscall));
  // Probe on multiplexer_6_out
  Multiplexer #(.select(1), .width(5), .disabled("Z"), .enable("false")) multiplexer_7 (
    .in0(IR[20:16]), .in1(IR[15:11]), .out(multiplexer_7_out), .sel(RegDst));
  Multiplexer #(.select(1), .width(5), .disabled("Z"), .enable("false")) multiplexer_8 (
    .in0(multiplexer_7_out), .in1({5{1'b1}}), .out(multiplexer_8_out), .sel(JAL));
  // Probe on RDin
  // Probe on multiplexer_8_out
  and and_1 (and_1_out, or_9_out, ~\同步清零1 );  // AND_Gate
  and and_2 (and_2_out, or_10_out, ~\同步清零2 );  // AND_Gate
  and and_3 (and_3_out, or_11_out, ~\同步清零3 );  // AND_Gate
  assign bit_extender_1_out = {{16{1'b0}}, IR[15:0]};  // Bit_Extender bit_extender_1
  assign bit_extender_2_out = {{16{IR[15]}}, IR[15:0]};  // Bit_Extender bit_extender_2
  Register #(.width(32), .trigger("rising"), .Select("low")) register_6 (
    .D(a0), .en(LED_en), .Q(LedData), .clk(CLK));  // open: clr
  Register #(.width(1), .trigger("rising"), .Select("low")) register_7 (
    .D(and_1_out), .Q(register_7_q), .clk(CLK));  // open: en, clr
  Register #(.width(1), .trigger("rising"), .Select("low")) register_8 (
    .D(and_2_out), .Q(register_8_q), .clk(CLK));  // open: en, clr
  Register #(.width(1), .trigger("rising"), .Select("low")) register_9 (
    .D(and_3_out), .Q(register_9_q), .clk(CLK));  // open: en, clr
  MIPS_Regifile mips_regifile_1 (
    .Din(RDin), .Clk(CLK), .R1(JR_PC), .R2(a0), .WE(RegWrite), .W_num(multiplexer_8_out),
    .R1_num(multiplexer_5_out), .R2_num(multiplexer_6_out));
  // Probe on a0
  Multiplexer #(.select(1), .width(32), .disabled("Z"), .enable("false")) multiplexer_9 (
    .in0(bit_extender_1_out), .in1(bit_extender_2_out), .out(multiplexer_9_out), .sel(SignedExt));
  Register #(.width(1), .trigger("rising"), .Select("low")) register_10 (
    .Q(register_10_q), .clr(register_11_q), .preset(\int ));  // open: D, en, clk, cs
  // Probe on JR_PC
  Multiplexer #(.select(1), .width(32), .disabled("Z"), .enable("false")) multiplexer_10 (
    .in0(a0), .in1(multiplexer_9_out), .out(multiplexer_10_out), .sel(AluSrcB));
  Shifter #(.width(32), .shift("ll")) shifter_1 (.in(bit_extender_2_out), .\dist (5'b00010), .out(shifter_1_out));
  Adder #(.width(32)) adder_2 (.a(shifter_1_out), .b({J_JAR_PC, PC_4}), .out(PC_imm));  // open: cin, cout
  Register #(.width(1), .trigger("rising"), .Select("low")) register_11 (
    .D(register_10_q), .Q(register_11_q), .clk(CLK));  // open: en, clr
  MIPS_ALU mips_alu_1 (
    .X(JR_PC), .Y(multiplexer_10_out), .AluOP(AluOP), .Equal(EQUAL), .Result(result1), .Result_2(result2),
    .shamt(IR[10:6]));
  Register #(.width(32), .trigger("rising"), .Select("low")) hi (
    .D(result2), .en(DIVU), .Q(high_out), .clk(CLK));  // open: clr
  Register #(.width(32), .trigger("rising"), .Select("low")) lo (
    .D(result1), .en(DIVU), .Q(low_out), .clk(CLK));  // open: clr
  Priority_Encoder #(.select(2), .disabled("Z")) priority_encoder_1 (
    .in0(register_7_q), .in1(register_8_q), .in2(register_9_q), .out(priority_encoder_1_out),
    .gs(priority_encoder_1_gs), .en_in(1'b1));  // open: in3, en_out
  and and_4 (\int , priority_encoder_1_gs, IE);
  Register #(.width(1), .trigger("rising"), .Select("low")) u_IE (
    .D(1'b0), .Q(IE_q), .clk(not_1_out), .preset(\int ));  // open: en, clr, cs
  not not_1 (not_1_out, ERET);
  Register #(.width(32), .trigger("rising"), .Select("low")) EPC (
    .D(PC_save), .Q(re_PC), .clk(register_11_q));  // open: en, clr
  Comparator #(.width(32), .mode("twosComplement")) comparator_6 (
    .a(JR_PC), .b(32'h22), .eq(comparator_6_eq));  // open: gt, lt
  // Probe on result1
  Multiplexer #(.select(2), .width(32), .disabled("Z"), .enable("false")) multiplexer_11 (
    .in0(32'h30ac), .in1(32'h3150), .in2(32'h31f4), .out(int_PC), .sel(priority_encoder_1_out));  // open: in3
  not not_2 (IE, IE_q);
  and and_5 (stop, ~comparator_6_eq, Syscall);  // AND_Gate
  and and_6 (LED_en, comparator_6_eq, Syscall);
  Multiplexer #(.select(1), .width(32), .disabled("Z"), .enable("false")) multiplexer_12 (
    .in0(a0), .in1(multiplexer_13_out), .out(MDin), .sel(SB));
  Register #(.width(2), .trigger("rising"), .Select("low")) register_12 (
    .D(priority_encoder_1_out), .Q(register_12_q), .clk(\int ));  // open: en, clr
  Multiplexer #(.select(2), .width(32), .disabled("Z"), .enable("false")) multiplexer_13 (
    .in0({mem_read[31:8], a0[7:0]}), .in1({mem_read[31:16], a0[7:0], mem_read[7:0]}),
    .in2({mem_read[31:24], a0[7:0], mem_read[15:0]}), .in3({a0[7:0], mem_read[23:0]}),
    .out(multiplexer_13_out), .sel(result1[1:0]));
  Decoder #(.select(2), .tristate("false"), .disabled("Z"), .enable("false")) decoder_1 (
    .out0(decoder_1_out0), .out1(decoder_1_out1), .out2(decoder_1_out2), .sel(register_12_q));  // open: out3
  and and_7 (\同步清零1 , decoder_1_out0, ERET);
  and and_8 (\同步清零2 , decoder_1_out1, ERET);
  and and_9 (\同步清零3 , decoder_1_out2, ERET);
  and and_10 (and_10_out, Beq, EQUAL);
  and and_11 (and_11_out, Bne, ~EQUAL);  // AND_Gate
  Comparator #(.width(32), .mode("twosComplement")) comparator_7 (
    .a(JR_PC), .b({32{1'b0}}), .gt(comparator_7_gt), .eq(comparator_7_eq));  // open: lt
  RAM #(.addrWidth(10), .dataWidth(32), .bus("separate"), .Select("high")) ram_1 (
    .addr(result1[11:2]), .din(MDin), .data(mem_read), .str(MemWrite), .clk(CLK));  // open: sel, ld, clr
  and and_12 (and_12_out, BGEZ, or_12_out);
  or or_12 (or_12_out, comparator_7_gt, comparator_7_eq);
  Multiplexer #(.select(1), .width(32), .disabled("Z"), .enable("false")) multiplexer_14 (
    .in0(result1), .in1(mem_read), .out(multiplexer_14_out), .sel(MemToReg));
  or or_13 (JMP_IF, and_10_out, and_11_out, and_12_out);
  Multiplexer #(.select(1), .width(32), .disabled("Z"), .enable("false")) multiplexer_15 (
    .in0(multiplexer_14_out), .in1({J_JAR_PC, PC_4}), .out(multiplexer_15_out), .sel(JAL));
  Multiplexer #(.select(1), .width(32), .disabled("Z"), .enable("false")) multiplexer_16 (
    .in0(multiplexer_15_out), .in1(low_out), .out(RDin), .sel(MFLO));

  // Other names for the same wires on the sheet: rt[31:0] = a0; J_JAR_PC[27:2] = IR[25:0]; PC_4[31:28] = J_JAR_PC;
  //   select[2:0] = {JR, JMP, JMP_IF}; rs[31:0] = JR_PC; v0[31:0] = JR_PC

  // Notes on the sheet:
  //   中断源
  //   中断等待指示
  //   单级中断测试信号模拟器
  //   控制位
  //   暂停节拍，不能为0
  //   总复位信号应将除ROM以外所有存储组件全部清零
  //   戳工具置1进入计数暂停模式，ctrl+k时钟自动运行到对应节拍暂停
  //   ctrl+k关闭时钟连续运行，将控制位置零，进入单步调试模式调试
  //   用这个时钟源需要去掉电路中的其他时钟源
  //   数码管输出
  //   数码管输出应该用寄存器锁存，否则显示数据只能一闪而过
  //   可计数暂停的时钟源
  //   指令存储器
  //   指令字
  //   contents of rom_1 (hex, n*v repeats v):
  //   201d07d0 20100001 109fc0 139fc3 8021 2012000c 24160008 26100001 3210000f 20080008 20090001 139900
  //   2709825 132020 20020022 c 1094022 1500fff9 22100001 2018000f 2188024 108700 20080008 20090001 139902
  //   2709825 132021 20020022 c 1094022 1500fff9 108702 2c9b022 12c00001 8000c07 4020 1084027 84400
  //   3508ffff 82021 20020022 c 8100001 afa20000 23bd0004 afa40000 23bd0004 afb00000 23bd0004 afb30000
  //   23bd0004 afb40000 23bd0004 afb50000 23bd0004 afb60000 23bd0004 20160001 20140003 20150001 168020
  //   108100 2149825 132020 20020022 c 1600fffa 295a022 1680fff7 23bdfffc 8fb60000 23bdfffc 8fb50000
  //   23bdfffc 8fb40000 23bdfffc 8fb30000 23bdfffc 8fb00000 23bdfffc 8fa40000 23bdfffc 8fa20000 42000018
  //   afa20000 23bd0004 afa40000 23bd0004 afb00000 23bd0004 afb30000 23bd0004 afb40000 23bd0004 afb50000
  //   23bd0004 afb60000 23bd0004 20160002 20140003 20150001 168020 108100 2149825 132020 20020022 c
  //   1600fffa 295a022 1680fff7 23bdfffc 8fb60000 23bdfffc 8fb50000 23bdfffc 8fb40000 23bdfffc 8fb30000
  //   23bdfffc 8fb00000 23bdfffc 8fa40000 23bdfffc 8fa20000 42000018 afa20000 23bd0004 afa40000 23bd0004
  //   afb00000 23bd0004 afb30000 23bd0004 afb40000 23bd0004 afb50000 23bd0004 afb60000 23bd0004 20160003
  //   20140003 20150001 168020 108100 2149825 132020 20020022 c 1600fffa 295a022 1680fff7 23bdfffc
  //   8fb60000 23bdfffc 8fb50000 23bdfffc 8fb40000 23bdfffc 8fb30000 23bdfffc 8fb00000 23bdfffc 8fa40000
  //   23bdfffc 8fa20000 42000018
  //   OP
  //   Func
  //   rs
  //   rt
  //   rd
  //   shmat
  //   imm
  //   addr
  //   JMP
  //   JR
  //   OP
  //   Func
  //   Syscall
  //   Beq
  //   Bne
  //   MemToReg
  //   MemWrite
  //   AluOP
  //   AluSrcB
  //   RegWrite
  //   JAL
  //   RegDst
  //   为方便自动评测，需要输出PC，IR，寄存器堆写如数据RDin
  //   RAM写使能MemWrite、RAM写入数据MDin等信号
  //   0是开中断
endmodule
module \单周期MIPS_多级中断  (
  input  IR1,
  input  IR2,
  input  IR3,
  output RegWrite,
  output MemWrite,
  output [31:0] PC,
  output [31:0] IR,
  output [31:0] RDin,
  output [31:0] MDin,
  output [31:0] LedData
);

  wire AluSrcB, and_1_out, and_2_out, and_3_out, and_10_out, and_11_out, and_12_out, Beq, BGEZ, Bne, CLK,
       clock_2_out, comparator_1_eq, comparator_2_eq, comparator_3_eq, comparator_4_eq, comparator_5_eq,
       comparator_6_eq, comparator_6_lt, comparator_7_eq, comparator_8_eq, comparator_8_gt, d_ff_1_q,
       decoder_1_out0, decoder_1_out1, decoder_1_out2, DIVU, EQUAL, ERET, Go, IE, IE_q, \int , IR1_t, IR2_t,
       IR3_t, IRA, IRB, IRC, JAL, JMP, JMP_IF, JR, LED_en, MemToReg, MFLO, multiplexer_3_out, nand_1_out,
       not_1_out, or_1_out, or_2_out, or_6_out, or_10_out, or_11_out, or_12_out, or_13_out,
       priority_encoder_1_gs, RegDst, register_1_q, register_2_q, register_3_q, register_4_q, register_5_q,
       register_7_q, register_8_q, register_9_q, register_10_q, register_11_q, SB, SignedExt, stop, Syscall,
       W1, W2, W3, \同步清零1 , \同步清零2 , \同步清零3 ;
  wire [1:0] priority_encoder_1_out, register_12_q;
  wire [3:0] AluOP;
  wire [4:0] multiplexer_5_out, multiplexer_6_out, multiplexer_7_out, multiplexer_8_out;
  wire [12:0] CNT_num;
  wire [15:0] \总周期数 ;
  wire [27:0] PC_4;
  wire [31:0] a0, bit_extender_1_out, bit_extender_2_out, high_out, int_PC, JR_PC, low_out, mem_read,
       multiplexer_2_out, multiplexer_4_out, multiplexer_9_out, multiplexer_10_out, multiplexer_13_out,
       multiplexer_14_out, multiplexer_15_out, PC_imm, PC_save, re_PC, result1, result2, shifter_1_out;
  wire [31:28] J_JAR_PC;

  Clock #(.highDuration(1), .lowDuration(1)) clock_1 (.out(CLK));
  Button _1 ();  // open: out
  Button _2 ();  // open: out
  Button _3 ();  // open: out
  Button \u_继续运行  (.out(Go));
  LED #(.active("true")) led_1 (.in(W1));
  LED #(.active("true")) led_2 (.in(W2));
  LED #(.active("true")) led_3 (.in(W3));
  Hex_Digit_Display hex_digit_display_1 (.value(LedData[31:28]));  // open: dp
  Comparator #(.width(16), .mode("twosComplement")) comparator_1 (
    .a(\总周期数 ), .b(16'h7), .eq(comparator_1_eq));  // open: gt, lt
  Comparator #(.width(16), .mode("twosComplement")) comparator_2 (
    .a(\总周期数 ), .b(16'h241), .eq(comparator_2_eq));  // open: gt, lt
  Hex_Digit_Display hex_digit_display_2 (.value(LedData[23:20]));  // open: dp
  Hex_Digit_Display hex_digit_display_3 (.value(LedData[27:24]));  // open: dp
  Comparator #(.width(16), .mode("twosComplement")) comparator_3 (
    .a(16'h258), .b(\总周期数 ), .eq(comparator_3_eq));  // open: gt, lt
  or or_1 (or_1_out, comparator_3_eq, comparator_4_eq);
  Comparator #(.width(16), .mode("twosComplement")) comparator_4 (
    .a(\总周期数 ), .b(16'h1), .eq(comparator_4_eq));  // open: gt, lt
  Comparator #(.width(16), .mode("twosComplement")) comparator_5 (
    .a(\总周期数 ), .b(16'h4), .eq(comparator_5_eq));  // open: gt, lt
  or or_2 (or_2_out, comparator_1_eq, comparator_2_eq);
  Hex_Digit_Display hex_digit_display_4 (.value(LedData[19:16]));  // open: dp
  Hex_Digit_Display hex_digit_display_5 (.value(LedData[15:12]));  // open: dp
  Pull_Resistor #(.pull(0)) pull_resistor_1 (.node(IRA));
  assign IRA = or_1_out ? ~CLK : 1'bz;  // Controlled_Inverter controlled_inverter_1
  Pull_Resistor #(.pull(0)) pull_resistor_2 (.node(IRB));
  assign IRB = comparator_5_eq ? ~CLK : 1'bz;  // Controlled_Inverter controlled_inverter_2
  Pull_Resistor #(.pull(0)) pull_resistor_3 (.node(IRC));
  assign IRC = or_2_out ? ~CLK : 1'bz;  // Controlled_Inverter controlled_inverter_3
  Hex_Digit_Display hex_digit_display_6 (.value(LedData[7:4]));  // open: dp
  Hex_Digit_Display hex_digit_display_7 (.value(LedData[11:8]));  // open: dp
  // Probe on \总周期数 
  // Probe on {JR, JMP, JMP_IF}
  Hex_Digit_Display hex_digit_display_8 (.value(LedData[3:0]));  // open: dp
  Multiplexer #(.select(3), .width(32), .disabled("Z"), .enable("false")) multiplexer_1 (
    .in0({J_JAR_PC, PC_4}), .in1(PC_imm), .in2({J_JAR_PC, IR[25:0], 2'b00}), .in6(JR_PC), .out(PC_save),
    .sel({JR, JMP, JMP_IF}));  // open: in3, in4, in5, in7
  D_Flip_Flop #(.trigger("high"), .Pre_Clr_Positions("LEGACY"), .NegatePresetClear("false"), .enable("true"), .NewFFLayout("false")) d_ff_1 (.Q(d_ff_1_q));  // open: clk, D, Qn, preset, en, reset
  // Probe on 13'h368
  Adder #(.width(32)) adder_1 (.a(PC), .b(32'h4), .out({J_JAR_PC, PC_4}));  // open: cin, cout
  Multiplexer #(.select(1), .width(32), .disabled("Z"), .enable("false")) multiplexer_2 (
    .in0(PC_save), .in1(re_PC), .out(multiplexer_2_out), .sel(ERET));
  Register #(.width(1), .trigger("rising"), .Select("low")) register_1 (
    .D(1'b1), .Q(register_1_q), .clk(\int ), .clr(register_2_q));  // open: en
  Register #(.width(1), .trigger("rising"), .Select("low")) register_2 (
    .D(1'b1), .Q(register_2_q), .clk(multiplexer_3_out), .clr(register_2_q));  // open: en
  Multiplexer #(.select(1), .width(1), .disabled("Z"), .enable("false")) multiplexer_3 (
    .in0(1'b1), .in1(CLK), .out(multiplexer_3_out), .sel(register_1_q));
  or or_3 (IR1_t, IR1, IRA);
  Comparator #(.width(13), .mode("twosComplement")) comparator_6 (
    .a(CNT_num), .b(13'h368), .eq(comparator_6_eq), .lt(comparator_6_lt));  // open: gt
  Clock #(.highDuration(1), .lowDuration(1)) clock_2 (.out(clock_2_out));
  Multiplexer #(.select(1), .width(32), .disabled("Z"), .enable("false")) multiplexer_4 (
    .in0(multiplexer_2_out), .in1(int_PC), .out(multiplexer_4_out), .sel(register_1_q));
  or or_4 (IR2_t, IR2, IRB);
  Counter #(.width(13), .max('h1fff), .ongoal("stay"), .trigger("rising"), .behavior("old")) counter_1 (
    .count(comparator_6_lt), .Q(CNT_num), .clk(clock_2_out));  // open: load, D, carry, clr, preset
  // Probe on {J_JAR_PC, PC_4}
  // Probe on multiplexer_4_out
  Counter #(.width(16), .max('hffff), .ongoal("stay"), .trigger("rising"), .behavior("old")) counter_2 (
    .Q(\总周期数 ), .clk(clock_2_out));  // open: load, D, count, carry, clr, preset
  nand nand_1 (nand_1_out, d_ff_1_q, comparator_6_eq);
  or or_5 (IR3_t, IR3, IRC);
  assign CLK = nand_1_out ? clock_2_out : 1'bz;  // Controlled_Buffer controlled_buffer_1
  Pull_Resistor #(.pull(1)) pull_resistor_4 (.node(CLK));
  // Mips_Probe mips_probe_1: pin names not known; wires that end beside it: 32'h8000c07, PC[11:2]
  Register #(.width(32), .trigger("rising"), .Select("low")) u_PC (
    .D(multiplexer_4_out), .en(or_6_out), .Q(PC), .clk(CLK));  // open: clr
  or or_6 (or_6_out, ~stop, Go);  // OR_Gate
  // Probe on PC
  // Mips_Probe mips_probe_2: pin names not known; wires that end beside it: IR
  ROM #(.addrWidth(10), .dataWidth(32), .Select("high")) rom_1 (.addr(PC[11:2]), .data(IR));
  Register #(.width(1), .trigger("rising"), .Select("low")) register_3 (
    .D(1'b1), .Q(register_3_q), .clk(IR1_t), .clr(register_7_q));  // open: en
  or or_7 (W1, register_3_q, register_7_q);
  Register #(.width(1), .trigger("rising"), .Select("low")) register_4 (
    .D(1'b1), .Q(register_4_q), .clk(IR2_t), .clr(register_8_q));  // open: en
  or or_8 (W2, register_4_q, register_8_q);
  Register #(.width(1), .trigger("rising"), .Select("low")) register_5 (
    .D(1'b1), .Q(register_5_q), .clk(IR3_t), .clr(register_9_q));  // open: en
  or or_9 (W3, register_5_q, register_9_q);
  or or_10 (or_10_out, register_3_q, register_7_q);
  or or_11 (or_11_out, register_4_q, register_8_q);
  or or_12 (or_12_out, register_5_q, register_9_q);
  \单周期硬布线控制器  \u_单周期硬布线控制器_1  (
    .Func(IR[5:0]), .OP(IR[31:26]), .ALU_OP(AluOP), .MemToReg(MemToReg), .MemWrite(MemWrite),
    .ALU_SRC(AluSrcB), .RegWrite(RegWrite), .SysCALL(Syscall), .SignedExt(SignedExt), .RegDst(RegDst),
    .JR(JR), .JMP(JMP), .Beq(Beq), .JAL(JAL), .Bne(Bne), .DIVU(DIVU), .MFLO(MFLO), .BGEZ(BGEZ), .SB(SB),
    .ERET(ERET));
  Multiplexer #(.select(1), .width(5), .disabled("Z"), .enable("false")) multiplexer_5 (
    .in0(IR[25:21]), .in1(5'b00010), .out(multiplexer_5_out), .sel(Syscall));
  // Probe on multiplexer_5_out
  Multiplexer #(.select(1), .width(5), .disabled("Z"), .enable("false")) multiplexer_6 (
    .in0(IR[20:16]), .in1(5'b00100), .out(multiplexer_6_out), .sel(Syscall));
  // Probe on multiplexer_6_out
  Multiplexer #(.select(1), .width(5), .disabled("Z"), .enable("false")) multiplexer_7 (
    .in0(IR[20:16]), .in1(IR[15:11]), .out(multiplexer_7_out), .sel(RegDst));
  Multiplexer #(.select(1), .width(5), .disabled("Z"), .enable("false")) multiplexer_8 (
    .in0(multiplexer_7_out), .in1({5{1'b1}}), .out(multiplexer_8_out), .sel(JAL));
  // Probe on RDin
  // Probe on multiplexer_8_out
  and and_1 (and_1_out, or_10_out, ~\同步清零1 );  // AND_Gate
  and and_2 (and_2_out, or_11_out, ~\同步清零2 );  // AND_Gate
  and and_3 (and_3_out, or_12_out, ~\同步清零3 );  // AND_Gate
  assign bit_extender_1_out = {{16{1'b0}}, IR[15:0]};  // Bit_Extender bit_extender_1
  assign bit_extender_2_out = {{16{IR[15]}}, IR[15:0]};  // Bit_Extender bit_extender_2
  Register #(.width(32), .trigger("rising"), .Select("low")) register_6 (
    .D(a0), .en(LED_en), .Q(LedData), .clk(CLK));  // open: clr
  Register #(.width(1), .trigger("rising"), .Select("low")) register_7 (
    .D(and_1_out), .Q(register_7_q), .clk(CLK));  // open: en, clr
  Register #(.width(1), .trigger("rising"), .Select("low")) register_8 (
    .D(and_2_out), .Q(register_8_q), .clk(CLK));  // open: en, clr
  Register #(.width(1), .trigger("rising"), .Select("low")) register_9 (
    .D(and_3_out), .Q(register_9_q), .clk(CLK));  // open: en, clr
  MIPS_Regifile mips_regifile_1 (
    .Din(RDin), .Clk(CLK), .R1(JR_PC), .R2(a0), .WE(RegWrite), .W_num(multiplexer_8_out),
    .R1_num(multiplexer_5_out), .R2_num(multiplexer_6_out));
  // Probe on a0
  Multiplexer #(.select(1), .width(32), .disabled("Z"), .enable("false")) multiplexer_9 (
    .in0(bit_extender_1_out), .in1(bit_extender_2_out), .out(multiplexer_9_out), .sel(SignedExt));
  Register #(.width(1), .trigger("rising"), .Select("low")) register_10 (
    .Q(register_10_q), .clr(register_11_q), .preset(\int ));  // open: D, en, clk, cs
  // Probe on JR_PC
  Multiplexer #(.select(1), .width(32), .disabled("Z"), .enable("false")) multiplexer_10 (
    .in0(a0), .in1(multiplexer_9_out), .out(multiplexer_10_out), .sel(AluSrcB));
  Shifter #(.width(32), .shift("ll")) shifter_1 (.in(bit_extender_2_out), .\dist (5'b00010), .out(shifter_1_out));
  Adder #(.width(32)) adder_2 (.a(shifter_1_out), .b({J_JAR_PC, PC_4}), .out(PC_imm));  // open: cin, cout
  Register #(.width(1), .trigger("rising"), .Select("low")) register_11 (
    .D(register_10_q), .Q(register_11_q), .clk(CLK));  // open: en, clr
  MIPS_ALU mips_alu_1 (
    .X(JR_PC), .Y(multiplexer_10_out), .AluOP(AluOP), .Equal(EQUAL), .Result(result1), .Result_2(result2),
    .shamt(IR[10:6]));
  Register #(.width(32), .trigger("rising"), .Select("low")) hi (
    .D(result2), .en(DIVU), .Q(high_out), .clk(CLK));  // open: clr
  Register #(.width(32), .trigger("rising"), .Select("low")) lo (
    .D(result1), .en(DIVU), .Q(low_out), .clk(CLK));  // open: clr
  Priority_Encoder #(.select(2), .disabled("Z")) priority_encoder_1 (
    .in0(register_7_q), .in1(register_8_q), .in2(register_9_q), .out(priority_encoder_1_out),
    .gs(priority_encoder_1_gs), .en_in(1'b1));  // open: in3, en_out
  and and_4 (\int , priority_encoder_1_gs, IE);
  Register #(.width(1), .trigger("rising"), .Select("low")) u_IE (
    .D(1'b0), .Q(IE_q), .clk(not_1_out), .preset(\int ));  // open: en, clr, cs
  not not_1 (not_1_out, ERET);
  Register #(.width(32), .trigger("rising"), .Select("low")) EPC (
    .D(PC_save), .Q(re_PC), .clk(register_11_q));  // open: en, clr
  Comparator #(.width(32), .mode("twosComplement")) comparator_7 (
    .a(JR_PC), .b(32'h22), .eq(comparator_7_eq));  // open: gt, lt
  // Probe on result1
  Multiplexer #(.select(2), .width(32), .disabled("Z"), .enable("false")) multiplexer_11 (
    .in0(32'h30ac), .in1(32'h3150), .in2(32'h31f4), .out(int_PC), .sel(priority_encoder_1_out));  // open: in3
  not not_2 (IE, IE_q);
  and and_5 (stop, ~comparator_7_eq, Syscall);  // AND_Gate
  and and_6 (LED_en, comparator_7_eq, Syscall);
  Multiplexer #(.select(1), .width(32), .disabled("Z"), .enable("false")) multiplexer_12 (
    .in0(a0), .in1(multiplexer_13_out), .out(MDin), .sel(SB));
  Register #(.width(2), .trigger("rising"), .Select("low")) register_12 (
    .D(priority_encoder_1_out), .Q(register_12_q), .clk(\int ));  // open: en, clr
  Multiplexer #(.select(2), .width(32), .disabled("Z"), .enable("false")) multiplexer_13 (
    .in0({mem_read[31:8], a0[7:0]}), .in1({mem_read[31:16], a0[7:0], mem_read[7:0]}),
    .in2({mem_read[31:24], a0[7:0], mem_read[15:0]}), .in3({a0[7:0], mem_read[23:0]}),
    .out(multiplexer_13_out), .sel(result1[1:0]));
  Decoder #(.select(2), .tristate("false"), .disabled("Z"), .enable("false")) decoder_1 (
    .out0(decoder_1_out0), .out1(decoder_1_out1), .out2(decoder_1_out2), .sel(register_12_q));  // open: out3
  and and_7 (\同步清零1 , decoder_1_out0, ERET);
  and and_8 (\同步清零2 , decoder_1_out1, ERET);
  and and_9 (\同步清零3 , decoder_1_out2, ERET);
  and and_10 (and_10_out, Beq, EQUAL);
  and and_11 (and_11_out, Bne, ~EQUAL);  // AND_Gate
  Comparator #(.width(32), .mode("twosComplement")) comparator_8 (
    .a(JR_PC), .b({32{1'b0}}), .gt(comparator_8_gt), .eq(comparator_8_eq));  // open: lt
  RAM #(.addrWidth(10), .dataWidth(32), .bus("separate"), .Select("high")) ram_1 (
    .addr(result1[11:2]), .din(MDin), .data(mem_read), .str(MemWrite), .clk(CLK));  // open: sel, ld, clr
  and and_12 (and_12_out, BGEZ, or_13_out);
  or or_13 (or_13_out, comparator_8_gt, comparator_8_eq);
  Multiplexer #(.select(1), .width(32), .disabled("Z"), .enable("false")) multiplexer_14 (
    .in0(result1), .in1(mem_read), .out(multiplexer_14_out), .sel(MemToReg));
  or or_14 (JMP_IF, and_10_out, and_11_out, and_12_out);
  Multiplexer #(.select(1), .width(32), .disabled("Z"), .enable("false")) multiplexer_15 (
    .in0(multiplexer_14_out), .in1({J_JAR_PC, PC_4}), .out(multiplexer_15_out), .sel(JAL));
  Multiplexer #(.select(1), .width(32), .disabled("Z"), .enable("false")) multiplexer_16 (
    .in0(multiplexer_15_out), .in1(low_out), .out(RDin), .sel(MFLO));

  // Other names for the same wires on the sheet: rt[31:0] = a0; J_JAR_PC[27:2] = IR[25:0]; PC_4[31:28] = J_JAR_PC;
  //   select[2:0] = {JR, JMP, JMP_IF}; rs[31:0] = JR_PC; v0[31:0] = JR_PC

  // Notes on the sheet:
  //   中断源
  //   中断等待指示
  //   总复位信号应将除ROM以外所有存储组件全部清零
  //   多级中断测试信号模拟器
  //   数码管输出
  //   数码管输出应该用寄存器锁存，否则显示数据只能一闪而过
  //   控制位
  //   暂停节拍，不能为0
  //   戳工具置1进入计数暂停模式，ctrl+k时钟自动运行到对应节拍暂停
  //   ctrl+k关闭时钟连续运行，将控制位置零，进入单步调试模式调试
  //   用这个时钟源需要去掉电路中的其他时钟源
  //   可计数暂停的时钟源
  //   指令存储器
  //   为方便自动评测，需要输出PC，IR，寄存器堆写如数据RDin
  //   指令字
  //   contents of rom_1 (hex, n*v repeats v):
  //   201d07d0 20100001 109fc0 139fc3 8021 2012000c 24160008 26100001 3210000f 20080008 20090001 139900
  //   2709825 132020 20020022 c 1094022 1500fff9 22100001 2018000f 2188024 108700 20080008 20090001 139902
  //   2709825 132021 20020022 c 1094022 1500fff9 108702 2c9b022 12c00001 8000c07 4020 1084027 84400
  //   3508ffff 82021 20020022 c 8100001 afa20000 23bd0004 afa40000 23bd0004 afb00000 23bd0004 afb30000
  //   23bd0004 afb40000 23bd0004 afb50000 23bd0004 afb60000 23bd0004 20160001 20140003 20150001 168020
  //   108100 2149825 132020 20020022 c 1600fffa 295a022 1680fff7 23bdfffc 8fb60000 23bdfffc 8fb50000
  //   23bdfffc 8fb40000 23bdfffc 8fb30000 23bdfffc 8fb00000 23bdfffc 8fa40000 23bdfffc 8fa20000 42000018
  //   afa20000 23bd0004 afa40000 23bd0004 afb00000 23bd0004 afb30000 23bd0004 afb40000 23bd0004 afb50000
  //   23bd0004 afb60000 23bd0004 20160002 20140003 20150001 168020 108100 2149825 132020 20020022 c
  //   1600fffa 295a022 1680fff7 23bdfffc 8fb60000 23bdfffc 8fb50000 23bdfffc 8fb40000 23bdfffc 8fb30000
  //   23bdfffc 8fb00000 23bdfffc 8fa40000 23bdfffc 8fa20000 42000018 afa20000 23bd0004 afa40000 23bd0004
  //   afb00000 23bd0004 afb30000 23bd0004 afb40000 23bd0004 afb50000 23bd0004 afb60000 23bd0004 20160003
  //   20140003 20150001 168020 108100 2149825 132020 20020022 c 1600fffa 295a022 1680fff7 23bdfffc
  //   8fb60000 23bdfffc 8fb50000 23bdfffc 8fb40000 23bdfffc 8fb30000 23bdfffc 8fb00000 23bdfffc 8fa40000
  //   23bdfffc 8fa20000 42000018
  //   RAM写使能MemWrite、RAM写入数据MDin等信号
  //   OP
  //   Func
  //   rs
  //   rt
  //   rd
  //   shmat
  //   imm
  //   addr
  //   JMP
  //   JR
  //   OP
  //   Func
  //   Syscall
  //   Beq
  //   Bne
  //   MemToReg
  //   MemWrite
  //   AluOP
  //   AluSrcB
  //   RegWrite
  //   JAL
  //   RegDst
  //   0是开中断
endmodule

module \封装正确性测试  (
);

  wire IR1, IR2, IR3, MemW, RegW;
  wire [31:0] EX_PC, ID_PC, IF_PC, IR, LED, MDin, MDinr, MEM_PC, PC, RDin, RDinr, WB_PC;

  \单周期MIPS  \u_单周期mips_1  (
    .IR1(IR1), .IR2(IR2), .IR3(IR3), .RegWrite(RegW), .MemWrite(MemW), .PC(PC), .IR(IR), .RDin(RDin),
    .MDin(MDin), .LedData(LED));
  \气泡流水线  \u_气泡流水线_1  (
    .RegWrite(RegW), .MemWrite(MemW), .IF_PC(IF_PC), .ID_PC(ID_PC), .EX_PC(EX_PC), .M_PC(MEM_PC),
    .WB_PC(WB_PC), .RDin(RDinr), .MDin(MDinr), .LedData(LED));
  \单周期MIPS_单级中断  \u_单周期mips_单级中断_1  (
    .IR1(IR1), .IR2(IR2), .IR3(IR3), .RegWrite(RegW), .MemWrite(MemW), .PC(PC), .IR(IR), .RDin(RDin),
    .MDin(MDin), .LedData(LED));
  \理想流水线  \u_理想流水线_1  (
    .RegWrite(RegW), .MemWrite(MemW), .IF_PC(IF_PC), .ID_PC(ID_PC), .EX_PC(EX_PC), .M_PC(MEM_PC),
    .WB_PC(WB_PC), .RDin(RDinr), .MDin(MDinr), .LedData(LED));
  \重定向流水线  \u_重定向流水线_1  (
    .RegWrite(RegW), .MemWrite(MemW), .IF_PC(IF_PC), .ID_PC(ID_PC), .EX_PC(EX_PC), .M_PC(MEM_PC),
    .WB_PC(WB_PC), .RDin(RDinr), .MDin(MDinr), .LedData(LED));
  \单周期MIPS_多级中断  \u_单周期mips_多级中断_1  (
    .IR1(IR1), .IR2(IR2), .IR3(IR3), .RegWrite(RegW), .MemWrite(MemW), .PC(PC), .IR(IR), .RDin(RDin),
    .MDin(MDin), .LedData(LED));

  // Notes on the sheet:
  //   单周期封装测试
  //   气泡流水封装测试
  //   单周期+单级中断封装测试
  //   请检查上面封装有无位宽不匹配，引脚标签是否和连接的标签相对应，否则无法在educoder平台上正确测试
  //   理想流水封装测试
  //   重定向流水封装测试
  //   单周期+多级中断封装测试
endmodule

module IF_ID (
  input  [31:0] PC_4_in,
  input  [31:0] PC_in,
  input  [31:0] IR_in,
  input  in_4,
  input  Reset,
  input  CLK,
  input  Enable,
  output [31:0] PC_4_out,
  output [31:0] PC_out,
  output [31:0] IR_out,
  output out_11
);

  wire [31:0] multiplexer_1_out, multiplexer_2_out, multiplexer_3_out;

  Pull_Resistor #(.pull(1)) pull_resistor_1 (.node(in_4));
  Multiplexer #(.select(1), .width(32), .disabled("Z"), .enable("false")) multiplexer_1 (
    .in0(PC_4_in), .in1({32{1'b0}}), .out(multiplexer_1_out), .sel(Reset));
  Multiplexer #(.select(1), .width(32), .disabled("Z"), .enable("false")) multiplexer_2 (
    .in0(PC_in), .in1({32{1'b0}}), .out(multiplexer_2_out), .sel(Reset));
  Multiplexer #(.select(1), .width(32), .disabled("Z"), .enable("false")) multiplexer_3 (
    .in0(IR_in), .in1({32{1'b0}}), .out(multiplexer_3_out), .sel(Reset));
  Register #(.width(32), .trigger("rising"), .Select("low")) register_1 (
    .D(multiplexer_1_out), .en(Enable), .Q(PC_4_out), .clk(CLK));  // open: clr
  Register #(.width(32), .trigger("rising"), .Select("low")) register_2 (
    .D(multiplexer_2_out), .en(Enable), .Q(PC_out), .clk(CLK));  // open: clr
  Register #(.width(32), .trigger("rising"), .Select("low")) register_3 (
    .D(multiplexer_3_out), .en(Enable), .Q(IR_out), .clk(CLK));  // open: clr

  assign out_11 = in_4;

  // Notes on the sheet:
  //   高电平有效
endmodule

module ID_EX (
  input  [31:0] IR_in,
  input  BEQ_in,
  input  [31:0] PC_in,
  input  BNE_in,
  input  [31:0] R1_in,
  input  MemToReg_in,
  input  MemWrite_in,
  input  [31:0] R2_in,
  input  AluSrcB_in,
  input  [15:0] Imm_in,
  input  RegWrite_in,
  input  [31:0] Address_in,
  input  JAL_in,
  input  [3:0] AluOP_in,
  input  RegDst_in,
  input  [4:0] Shamt_in,
  input  Syscall_in,
  input  JMP_in,
  input  JR_in,
  input  [31:0] PC_4_in,
  input  signedext_in,
  input  Reset,
  input  Enable,
  input  CLK,
  output [31:0] IR_out,
  output BEQ_out,
  output [31:0] PC_out,
  output BNE_out,
  output [31:0] R1_out,
  output MemToReg_out,
  output MemWrite_out,
  output [31:0] R2_out,
  output AluSrcB_out,
  output [15:0] Imm_out,
  output RegWrite_out,
  output [31:0] Address_out,
  output JAL_out,
  output [3:0] AluOP_out,
  output RegDst_out,
  output [4:0] Shamt_out,
  output Syscall_out,
  output JMP_out,
  output JR_out,
  output [31:0] PC_4_out,
  output signedext_out
);

  wire multiplexer_9_out, multiplexer_10_out, multiplexer_11_out, multiplexer_12_out, multiplexer_13_out,
       multiplexer_14_out, multiplexer_15_out, multiplexer_16_out, multiplexer_17_out, multiplexer_18_out,
       multiplexer_19_out, multiplexer_21_out;
  wire [3:0] multiplexer_7_out;
  wire [4:0] multiplexer_8_out;
  wire [15:0] multiplexer_5_out;
  wire [31:0] multiplexer_1_out, multiplexer_2_out, multiplexer_3_out, multiplexer_4_out, multiplexer_6_out,
       multiplexer_20_out;

  Multiplexer #(.select(1), .width(32), .disabled("Z"), .enable("false")) multiplexer_1 (
    .in0(IR_in), .in1({32{1'b0}}), .out(multiplexer_1_out), .sel(Reset));
  Multiplexer #(.select(1), .width(32), .disabled("Z"), .enable("false")) multiplexer_2 (
    .in0(PC_in), .in1({32{1'b0}}), .out(multiplexer_2_out), .sel(Reset));
  Multiplexer #(.select(1), .width(32), .disabled("Z"), .enable("false")) multiplexer_3 (
    .in0(R1_in), .in1({32{1'b0}}), .out(multiplexer_3_out), .sel(Reset));
  Multiplexer #(.select(1), .width(32), .disabled("Z"), .enable("false")) multiplexer_4 (
    .in0(R2_in), .in1({32{1'b0}}), .out(multiplexer_4_out), .sel(Reset));
  Multiplexer #(.select(1), .width(16), .disabled("Z"), .enable("false")) multiplexer_5 (
    .in0(Imm_in), .in1({16{1'b0}}), .out(multiplexer_5_out), .sel(Reset));
  Multiplexer #(.select(1), .width(32), .disabled("Z"), .enable("false")) multiplexer_6 (
    .in0(Address_in), .in1({32{1'b0}}), .out(multiplexer_6_out), .sel(Reset));
  Multiplexer #(.select(1), .width(4), .disabled("Z"), .enable("false")) multiplexer_7 (
    .in0(AluOP_in), .in1(4'b0000), .out(multiplexer_7_out), .sel(Reset));
  Multiplexer #(.select(1), .width(5), .disabled("Z"), .enable("false")) multiplexer_8 (
    .in0(Shamt_in), .in1({5{1'b0}}), .out(multiplexer_8_out), .sel(Reset));
  Register #(.width(32), .trigger("rising"), .Select("low")) register_1 (
    .D(multiplexer_1_out), .en(Enable), .Q(IR_out), .clk(CLK));  // open: clr
  Register #(.width(32), .trigger("rising"), .Select("low")) register_2 (
    .D(multiplexer_2_out), .en(Enable), .Q(PC_out), .clk(CLK));  // open: clr
  Register #(.width(32), .trigger("rising"), .Select("low")) register_3 (
    .D(multiplexer_3_out), .en(Enable), .Q(R1_out), .clk(CLK));  // open: clr
  Register #(.width(32), .trigger("rising"), .Select("low")) register_4 (
    .D(multiplexer_4_out), .en(Enable), .Q(R2_out), .clk(CLK));  // open: clr
  Register #(.width(16), .trigger("rising"), .Select("low")) register_5 (
    .D(multiplexer_5_out), .en(Enable), .Q(Imm_out), .clk(CLK));  // open: clr
  Register #(.width(32), .trigger("rising"), .Select("low")) register_6 (
    .D(multiplexer_6_out), .en(Enable), .Q(Address_out), .clk(CLK));  // open: clr
  Register #(.width(4), .trigger("rising"), .Select("low")) register_7 (
    .D(multiplexer_7_out), .en(Enable), .Q(AluOP_out), .clk(CLK));  // open: clr
  Register #(.width(5), .trigger("rising"), .Select("low")) register_8 (
    .D(multiplexer_8_out), .en(Enable), .Q(Shamt_out), .clk(CLK));  // open: clr
  Multiplexer #(.select(1), .width(1), .disabled("Z"), .enable("false")) multiplexer_9 (
    .in0(BEQ_in), .in1(1'b0), .out(multiplexer_9_out), .sel(Reset));
  Multiplexer #(.select(1), .width(1), .disabled("Z"), .enable("false")) multiplexer_10 (
    .in0(BNE_in), .in1(1'b0), .out(multiplexer_10_out), .sel(Reset));
  Multiplexer #(.select(1), .width(1), .disabled("Z"), .enable("false")) multiplexer_11 (
    .in0(MemToReg_in), .in1(1'b0), .out(multiplexer_11_out), .sel(Reset));
  Multiplexer #(.select(1), .width(1), .disabled("Z"), .enable("false")) multiplexer_12 (
    .in0(MemWrite_in), .in1(1'b0), .out(multiplexer_12_out), .sel(Reset));
  Multiplexer #(.select(1), .width(1), .disabled("Z"), .enable("false")) multiplexer_13 (
    .in0(AluSrcB_in), .in1(1'b0), .out(multiplexer_13_out), .sel(Reset));
  Multiplexer #(.select(1), .width(1), .disabled("Z"), .enable("false")) multiplexer_14 (
    .in0(RegWrite_in), .in1(1'b0), .out(multiplexer_14_out), .sel(Reset));
  Multiplexer #(.select(1), .width(1), .disabled("Z"), .enable("false")) multiplexer_15 (
    .in0(JAL_in), .in1(1'b0), .out(multiplexer_15_out), .sel(Reset));
  Multiplexer #(.select(1), .width(1), .disabled("Z"), .enable("false")) multiplexer_16 (
    .in0(RegDst_in), .in1(1'b0), .out(multiplexer_16_out), .sel(Reset));
  Multiplexer #(.select(1), .width(1), .disabled("Z"), .enable("false")) multiplexer_17 (
    .in0(Syscall_in), .in1(1'b0), .out(multiplexer_17_out), .sel(Reset));
  Multiplexer #(.select(1), .width(1), .disabled("Z"), .enable("false")) multiplexer_18 (
    .in0(JMP_in), .in1(1'b0), .out(multiplexer_18_out), .sel(Reset));
  Multiplexer #(.select(1), .width(1), .disabled("Z"), .enable("false")) multiplexer_19 (
    .in0(JR_in), .in1(1'b0), .out(multiplexer_19_out), .sel(Reset));
  Multiplexer #(.select(1), .width(32), .disabled("Z"), .enable("false")) multiplexer_20 (
    .in0(PC_4_in), .in1({32{1'b0}}), .out(multiplexer_20_out), .sel(Reset));
  Multiplexer #(.select(1), .width(1), .disabled("Z"), .enable("false")) multiplexer_21 (
    .in0(signedext_in), .in1(1'b0), .out(multiplexer_21_out), .sel(Reset));
  Register #(.width(1), .trigger("rising"), .Select("low")) register_9 (
    .D(multiplexer_9_out), .en(Enable), .Q(BEQ_out), .clk(CLK));  // open: clr
  Register #(.width(1), .trigger("rising"), .Select("low")) register_10 (
    .D(multiplexer_10_out), .en(Enable), .Q(BNE_out), .clk(CLK));  // open: clr
  Register #(.width(1), .trigger("rising"), .Select("low")) register_11 (
    .D(multiplexer_11_out), .en(Enable), .Q(MemToReg_out), .clk(CLK));  // open: clr
  Register #(.width(1), .trigger("rising"), .Select("low")) register_12 (
    .D(multiplexer_12_out), .en(Enable), .Q(MemWrite_out), .clk(CLK));  // open: clr
  Register #(.width(1), .trigger("rising"), .Select("low")) register_13 (
    .D(multiplexer_13_out), .en(Enable), .Q(AluSrcB_out), .clk(CLK));  // open: clr
  Register #(.width(1), .trigger("rising"), .Select("low")) register_14 (
    .D(multiplexer_14_out), .en(Enable), .Q(RegWrite_out), .clk(CLK));  // open: clr
  Register #(.width(1), .trigger("rising"), .Select("low")) register_15 (
    .D(multiplexer_15_out), .en(Enable), .Q(JAL_out), .clk(CLK));  // open: clr
  Register #(.width(1), .trigger("rising"), .Select("low")) register_16 (
    .D(multiplexer_16_out), .en(Enable), .Q(RegDst_out), .clk(CLK));  // open: clr
  Register #(.width(1), .trigger("rising"), .Select("low")) register_17 (
    .D(multiplexer_17_out), .en(Enable), .Q(Syscall_out), .clk(CLK));  // open: clr
  Register #(.width(1), .trigger("rising"), .Select("low")) register_18 (
    .D(multiplexer_18_out), .en(Enable), .Q(JMP_out), .clk(CLK));  // open: clr
  Register #(.width(1), .trigger("rising"), .Select("low")) register_19 (
    .D(multiplexer_19_out), .en(Enable), .Q(JR_out), .clk(CLK));  // open: clr
  Register #(.width(32), .trigger("rising"), .Select("low")) register_20 (
    .D(multiplexer_20_out), .en(Enable), .Q(PC_4_out), .clk(CLK));  // open: clr
  Register #(.width(1), .trigger("rising"), .Select("low")) register_21 (
    .D(multiplexer_21_out), .en(Enable), .Q(signedext_out), .clk(CLK));  // open: clr
endmodule

module EX_MEM (
  input  MemToReg_in,
  input  [31:0] IR_in,
  input  MemWrite_in,
  input  [31:0] PC_in,
  input  RegWrite_in,
  input  [31:0] R2_in,
  input  JAL_in,
  input  [31:0] AluR_in,
  input  RegDst_in,
  input  _2out,
  input  Syscall_in,
  input  _1in,
  input  [31:0] PC_4_in,
  input  [4:0] W__in,
  input  [2:0] _3in,
  input  Reset,
  input  Enable,
  input  CLK,
  output MemToReg_out,
  output [31:0] IR_out,
  output MemWrite_out,
  output [31:0] PC_out,
  output RegWrite_out,
  output [31:0] R2_out,
  output JAL_out,
  output [31:0] AluR_out,
  output RegDst_out,
  output _2out_2,
  output Syscall_out,
  output _1out,
  output [31:0] PC_4_out,
  output [4:0] W__out,
  output [2:0] _4out
);

  wire multiplexer_5_out, multiplexer_6_out, multiplexer_9_out, multiplexer_10_out, multiplexer_11_out,
       multiplexer_12_out, multiplexer_13_out, multiplexer_14_out;
  wire [2:0] multiplexer_8_out;
  wire [4:0] multiplexer_7_out;
  wire [31:0] multiplexer_1_out, multiplexer_2_out, multiplexer_3_out, multiplexer_4_out, multiplexer_15_out;

  Multiplexer #(.select(1), .width(32), .disabled("Z"), .enable("false")) multiplexer_1 (
    .in0(IR_in), .in1({32{1'b0}}), .out(multiplexer_1_out), .sel(Reset));
  Multiplexer #(.select(1), .width(32), .disabled("Z"), .enable("false")) multiplexer_2 (
    .in0(PC_in), .in1({32{1'b0}}), .out(multiplexer_2_out), .sel(Reset));
  Multiplexer #(.select(1), .width(32), .disabled("Z"), .enable("false")) multiplexer_3 (
    .in0(R2_in), .in1({32{1'b0}}), .out(multiplexer_3_out), .sel(Reset));
  Multiplexer #(.select(1), .width(32), .disabled("Z"), .enable("false")) multiplexer_4 (
    .in0(AluR_in), .in1({32{1'b0}}), .out(multiplexer_4_out), .sel(Reset));
  Multiplexer #(.select(1), .width(1), .disabled("Z"), .enable("false")) multiplexer_5 (
    .in0(_2out), .in1(1'b0), .out(multiplexer_5_out), .sel(Reset));
  Multiplexer #(.select(1), .width(1), .disabled("Z"), .enable("false")) multiplexer_6 (
    .in0(_1in), .in1(1'b0), .out(multiplexer_6_out), .sel(Reset));
  Multiplexer #(.select(1), .width(5), .disabled("Z"), .enable("false")) multiplexer_7 (
    .in0(W__in), .in1({5{1'b0}}), .out(multiplexer_7_out), .sel(Reset));
  Multiplexer #(.select(1), .width(3), .disabled("Z"), .enable("false")) multiplexer_8 (
    .in0(_3in), .in1(3'b000), .out(multiplexer_8_out), .sel(Reset));
  Register #(.width(32), .trigger("rising"), .Select("low")) register_1 (
    .D(multiplexer_1_out), .en(Enable), .Q(IR_out), .clk(CLK));  // open: clr
  Register #(.width(32), .trigger("rising"), .Select("low")) register_2 (
    .D(multiplexer_2_out), .en(Enable), .Q(PC_out), .clk(CLK));  // open: clr
  Register #(.width(32), .trigger("rising"), .Select("low")) register_3 (
    .D(multiplexer_3_out), .en(Enable), .Q(R2_out), .clk(CLK));  // open: clr
  Register #(.width(32), .trigger("rising"), .Select("low")) register_4 (
    .D(multiplexer_4_out), .en(Enable), .Q(AluR_out), .clk(CLK));  // open: clr
  Register #(.width(1), .trigger("rising"), .Select("low")) register_5 (
    .D(multiplexer_5_out), .en(Enable), .Q(_2out_2), .clk(CLK));  // open: clr
  Register #(.width(1), .trigger("rising"), .Select("low")) register_6 (
    .D(multiplexer_6_out), .en(Enable), .Q(_1out), .clk(CLK));  // open: clr
  Register #(.width(5), .trigger("rising"), .Select("low")) register_7 (
    .D(multiplexer_7_out), .en(Enable), .Q(W__out), .clk(CLK));  // open: clr
  Register #(.width(3), .trigger("rising"), .Select("low")) register_8 (
    .D(multiplexer_8_out), .en(Enable), .Q(_4out), .clk(CLK));  // open: clr
  Multiplexer #(.select(1), .width(1), .disabled("Z"), .enable("false")) multiplexer_9 (
    .in0(MemToReg_in), .in1(1'b0), .out(multiplexer_9_out), .sel(Reset));
  Multiplexer #(.select(1), .width(1), .disabled("Z"), .enable("false")) multiplexer_10 (
    .in0(MemWrite_in), .in1(1'b0), .out(multiplexer_10_out), .sel(Reset));
  Multiplexer #(.select(1), .width(1), .disabled("Z"), .enable("false")) multiplexer_11 (
    .in0(RegWrite_in), .in1(1'b0), .out(multiplexer_11_out), .sel(Reset));
  Multiplexer #(.select(1), .width(1), .disabled("Z"), .enable("false")) multiplexer_12 (
    .in0(JAL_in), .in1(1'b0), .out(multiplexer_12_out), .sel(Reset));
  Multiplexer #(.select(1), .width(1), .disabled("Z"), .enable("false")) multiplexer_13 (
    .in0(RegDst_in), .in1(1'b0), .out(multiplexer_13_out), .sel(Reset));
  Multiplexer #(.select(1), .width(1), .disabled("Z"), .enable("false")) multiplexer_14 (
    .in0(Syscall_in), .in1(1'b0), .out(multiplexer_14_out), .sel(Reset));
  Multiplexer #(.select(1), .width(32), .disabled("Z"), .enable("false")) multiplexer_15 (
    .in0(PC_4_in), .in1({32{1'b0}}), .out(multiplexer_15_out), .sel(Reset));
  Register #(.width(1), .trigger("rising"), .Select("low")) register_9 (
    .D(multiplexer_9_out), .en(Enable), .Q(MemToReg_out), .clk(CLK));  // open: clr
  Register #(.width(1), .trigger("rising"), .Select("low")) register_10 (
    .D(multiplexer_10_out), .en(Enable), .Q(MemWrite_out), .clk(CLK));  // open: clr
  Register #(.width(1), .trigger("rising"), .Select("low")) register_11 (
    .D(multiplexer_11_out), .en(Enable), .Q(RegWrite_out), .clk(CLK));  // open: clr
  Register #(.width(1), .trigger("rising"), .Select("low")) register_12 (
    .D(multiplexer_12_out), .en(Enable), .Q(JAL_out), .clk(CLK));  // open: clr
  Register #(.width(1), .trigger("rising"), .Select("low")) register_13 (
    .D(multiplexer_13_out), .en(Enable), .Q(RegDst_out), .clk(CLK));  // open: clr
  Register #(.width(1), .trigger("rising"), .Select("low")) register_14 (
    .D(multiplexer_14_out), .en(Enable), .Q(Syscall_out), .clk(CLK));  // open: clr
  Register #(.width(32), .trigger("rising"), .Select("low")) register_15 (
    .D(multiplexer_15_out), .en(Enable), .Q(PC_4_out), .clk(CLK));  // open: clr
endmodule

module MEM_WB (
  input  MemToReg_in,
  input  [31:0] IR_in,
  input  RegWrite_in,
  input  [31:0] PC_in,
  input  JAL_in,
  input  [31:0] MemD_in,
  input  RegDst_in,
  input  [31:0] AluR_in,
  input  Syscall_in,
  input  Halt_in,
  input  [4:0] W__in,
  input  [31:0] PC_4_in,
  input  [2:0] Interrupt_in,
  input  [31:0] R2_in,
  input  Reset,
  input  Enable,
  input  CLK,
  output MemToReg_out,
  output [31:0] IR_out,
  output RegWrite_out,
  output [31:0] PC_out,
  output JAL_out,
  output [31:0] MemD_out,
  output RegDst_out,
  output [31:0] AluR_out,
  output Syscall_out,
  output Halt_out,
  output [4:0] W__out,
  output [31:0] PC_4_out,
  output [2:0] Interrupt_out,
  output [31:0] R2_out
);

  wire multiplexer_5_out, multiplexer_8_out, multiplexer_9_out, multiplexer_10_out, multiplexer_11_out,
       multiplexer_12_out;
  wire [2:0] multiplexer_7_out;
  wire [4:0] multiplexer_6_out;
  wire [31:0] multiplexer_1_out, multiplexer_2_out, multiplexer_3_out, multiplexer_4_out, multiplexer_13_out,
       multiplexer_14_out;

  Multiplexer #(.select(1), .width(32), .disabled("Z"), .enable("false")) multiplexer_1 (
    .in0(IR_in), .in1({32{1'b0}}), .out(multiplexer_1_out), .sel(Reset));
  Multiplexer #(.select(1), .width(32), .disabled("Z"), .enable("false")) multiplexer_2 (
    .in0(PC_in), .in1({32{1'b0}}), .out(multiplexer_2_out), .sel(Reset));
  Multiplexer #(.select(1), .width(32), .disabled("Z"), .enable("false")) multiplexer_3 (
    .in0(MemD_in), .in1({32{1'b0}}), .out(multiplexer_3_out), .sel(Reset));
  Multiplexer #(.select(1), .width(32), .disabled("Z"), .enable("false")) multiplexer_4 (
    .in0(AluR_in), .in1({32{1'b0}}), .out(multiplexer_4_out), .sel(Reset));
  Multiplexer #(.select(1), .width(1), .disabled("Z"), .enable("false")) multiplexer_5 (
    .in0(Halt_in), .in1(1'b0), .out(multiplexer_5_out), .sel(Reset));
  Multiplexer #(.select(1), .width(5), .disabled("Z"), .enable("false")) multiplexer_6 (
    .in0(W__in), .in1({5{1'b0}}), .out(multiplexer_6_out), .sel(Reset));
  Multiplexer #(.select(1), .width(3), .disabled("Z"), .enable("false")) multiplexer_7 (
    .in0(Interrupt_in), .in1(3'b000), .out(multiplexer_7_out), .sel(Reset));
  Register #(.width(32), .trigger("rising"), .Select("low")) register_1 (
    .D(multiplexer_1_out), .en(Enable), .Q(IR_out), .clk(CLK));  // open: clr
  Register #(.width(32), .trigger("rising"), .Select("low")) register_2 (
    .D(multiplexer_2_out), .en(Enable), .Q(PC_out), .clk(CLK));  // open: clr
  Register #(.width(32), .trigger("rising"), .Select("low")) register_3 (
    .D(multiplexer_3_out), .en(Enable), .Q(MemD_out), .clk(CLK));  // open: clr
  Register #(.width(32), .trigger("rising"), .Select("low")) register_4 (
    .D(multiplexer_4_out), .en(Enable), .Q(AluR_out), .clk(CLK));  // open: clr
  Register #(.width(1), .trigger("rising"), .Select("low")) register_5 (
    .D(multiplexer_5_out), .en(Enable), .Q(Halt_out), .clk(CLK));  // open: clr
  Register #(.width(5), .trigger("rising"), .Select("low")) register_6 (
    .D(multiplexer_6_out), .en(Enable), .Q(W__out), .clk(CLK));  // open: clr
  Register #(.width(3), .trigger("rising"), .Select("low")) register_7 (
    .D(multiplexer_7_out), .en(Enable), .Q(Interrupt_out), .clk(CLK));  // open: clr
  Multiplexer #(.select(1), .width(1), .disabled("Z"), .enable("false")) multiplexer_8 (
    .in0(MemToReg_in), .in1(1'b0), .out(multiplexer_8_out), .sel(Reset));
  Multiplexer #(.select(1), .width(1), .disabled("Z"), .enable("false")) multiplexer_9 (
    .in0(RegWrite_in), .in1(1'b0), .out(multiplexer_9_out), .sel(Reset));
  Multiplexer #(.select(1), .width(1), .disabled("Z"), .enable("false")) multiplexer_10 (
    .in0(JAL_in), .in1(1'b0), .out(multiplexer_10_out), .sel(Reset));
  Multiplexer #(.select(1), .width(1), .disabled("Z"), .enable("false")) multiplexer_11 (
    .in0(RegDst_in), .in1(1'b0), .out(multiplexer_11_out), .sel(Reset));
  Multiplexer #(.select(1), .width(1), .disabled("Z"), .enable("false")) multiplexer_12 (
    .in0(Syscall_in), .in1(1'b0), .out(multiplexer_12_out), .sel(Reset));
  Multiplexer #(.select(1), .width(32), .disabled("Z"), .enable("false")) multiplexer_13 (
    .in0(PC_4_in), .in1({32{1'b0}}), .out(multiplexer_13_out), .sel(Reset));
  Multiplexer #(.select(1), .width(32), .disabled("Z"), .enable("false")) multiplexer_14 (
    .in0(R2_in), .in1({32{1'b0}}), .out(multiplexer_14_out), .sel(Reset));
  Register #(.width(1), .trigger("rising"), .Select("low")) register_8 (
    .D(multiplexer_8_out), .en(Enable), .Q(MemToReg_out), .clk(CLK));  // open: clr
  Register #(.width(1), .trigger("rising"), .Select("low")) register_9 (
    .D(multiplexer_9_out), .en(Enable), .Q(RegWrite_out), .clk(CLK));  // open: clr
  Register #(.width(1), .trigger("rising"), .Select("low")) register_10 (
    .D(multiplexer_10_out), .en(Enable), .Q(JAL_out), .clk(CLK));  // open: clr
  Register #(.width(1), .trigger("rising"), .Select("low")) register_11 (
    .D(multiplexer_11_out), .en(Enable), .Q(RegDst_out), .clk(CLK));  // open: clr
  Register #(.width(1), .trigger("rising"), .Select("low")) register_12 (
    .D(multiplexer_12_out), .en(Enable), .Q(Syscall_out), .clk(CLK));  // open: clr
  Register #(.width(32), .trigger("rising"), .Select("low")) register_13 (
    .D(multiplexer_13_out), .en(Enable), .Q(PC_4_out), .clk(CLK));  // open: clr
  Register #(.width(32), .trigger("rising"), .Select("low")) register_14 (
    .D(multiplexer_14_out), .en(Enable), .Q(R2_out), .clk(CLK));  // open: clr
endmodule

module \寄存器  (
  input  OP0,
  input  OP1,
  input  OP2,
  input  OP3,
  input  OP4,
  input  OP5,
  input  F0,
  input  F1,
  input  F2,
  input  F3,
  input  F4,
  input  F5,
  output rs,
  output rt
);

  wire and_1_out, and_2_out, and_3_out, and_4_out, and_5_out, and_6_out, and_7_out, and_8_out, and_9_out,
       and_10_out, and_11_out, and_12_out, and_13_out, and_14_out, and_15_out, and_16_out, and_17_out,
       and_18_out, and_19_out, and_20_out, and_21_out, and_22_out, and_23_out, and_24_out, and_25_out,
       and_26_out, and_27_out, and_28_out, and_29_out, and_30_out, and_31_out, and_32_out, and_33_out,
       and_34_out, not_1_out, not_2_out, not_3_out, not_4_out, not_5_out, not_6_out, not_7_out, not_8_out,
       not_9_out, not_10_out, not_11_out, not_12_out, not_13_out, not_14_out, not_15_out, not_16_out,
       not_17_out, not_18_out, not_19_out, not_20_out, not_21_out, not_22_out, not_23_out, not_24_out,
       not_25_out, not_26_out, not_27_out, not_28_out, not_29_out, not_30_out, not_31_out, not_32_out,
       not_33_out, not_34_out, not_35_out, not_36_out, not_37_out, not_38_out, not_39_out, not_40_out,
       not_41_out, not_42_out, not_43_out, not_44_out, not_45_out, not_46_out, not_47_out, not_48_out,
       not_49_out, not_50_out, not_51_out, not_52_out, not_53_out, not_54_out, not_55_out, not_56_out,
       not_57_out, not_58_out, not_59_out, not_60_out, not_61_out, not_62_out, not_63_out, not_64_out,
       not_65_out, not_66_out, not_67_out, not_68_out, not_69_out, not_70_out, not_71_out, not_72_out,
       not_73_out, not_74_out, not_75_out, not_76_out, not_77_out, not_78_out, not_79_out, not_80_out,
       not_81_out, not_82_out, not_83_out, not_84_out, not_85_out, not_86_out, not_87_out, not_88_out,
       not_89_out, not_90_out, not_91_out, not_92_out, not_93_out, not_94_out, not_95_out, not_96_out,
       not_97_out, not_98_out, not_99_out, not_100_out, not_101_out, not_102_out, not_103_out, not_104_out,
       not_105_out, not_106_out, not_107_out, not_108_out, not_109_out, not_110_out, not_111_out,
       not_112_out, not_113_out, not_114_out, not_115_out, not_116_out, not_117_out, not_118_out,
       not_119_out, not_120_out, not_121_out, not_122_out, not_123_out, not_124_out, not_125_out,
       not_126_out, not_127_out, not_128_out, not_129_out, not_130_out, not_131_out, not_132_out,
       not_133_out, not_134_out, not_135_out, not_136_out, not_137_out, not_138_out, not_139_out,
       not_140_out, not_141_out, not_142_out, not_143_out, not_144_out, not_145_out, not_146_out,
       not_147_out, not_148_out, not_149_out, not_150_out, not_151_out, not_152_out, not_153_out,
       not_154_out, not_155_out, not_156_out, not_157_out, not_158_out, not_159_out, not_160_out,
       not_161_out, not_162_out, not_163_out, not_164_out, not_165_out, not_166_out, not_167_out,
       not_168_out, not_169_out, not_170_out, not_171_out, not_172_out, not_173_out, not_174_out,
       not_175_out, not_176_out, not_177_out, not_178_out, not_179_out, not_180_out, not_181_out,
       not_182_out, not_183_out, not_184_out, not_185_out, not_186_out, not_187_out, not_188_out,
       not_189_out, not_190_out, not_191_out, not_192_out, not_193_out, not_194_out, not_195_out,
       not_196_out, not_197_out, not_198_out, not_199_out, not_200_out, not_201_out, not_202_out,
       not_203_out, not_204_out, not_205_out, not_206_out, not_207_out, not_208_out, not_209_out,
       not_210_out, not_211_out, not_212_out, not_213_out, not_214_out, not_215_out, not_216_out,
       not_217_out, not_218_out, not_219_out, not_220_out, not_221_out, not_222_out, not_223_out,
       not_224_out, not_225_out, not_226_out, not_227_out, not_228_out, not_229_out, not_230_out,
       not_231_out, not_232_out, not_233_out, not_234_out, not_235_out, not_236_out, not_237_out,
       not_238_out, not_239_out, not_240_out, not_241_out, not_242_out, not_243_out, not_244_out,
       not_245_out, not_246_out, not_247_out, not_248_out, not_249_out, not_250_out, not_251_out,
       not_252_out, not_253_out, not_254_out, not_255_out, not_256_out, not_257_out, not_258_out, not_259_out;

  not not_1 (not_1_out, OP5);
  not not_2 (not_2_out, OP4);
  not not_3 (not_3_out, OP3);
  not not_4 (not_4_out, OP2);
  not not_5 (not_5_out, OP1);
  not not_6 (not_6_out, OP0);
  not not_7 (not_7_out, F4);
  not not_8 (not_8_out, F3);
  not not_9 (not_9_out, F2);
  not not_10 (not_10_out, F1);
  not not_11 (not_11_out, F0);
  not not_12 (not_12_out, OP5);
  not not_13 (not_13_out, OP4);
  not not_14 (not_14_out, OP3);
  not not_15 (not_15_out, OP2);
  not not_16 (not_16_out, OP1);
  not not_17 (not_17_out, OP0);
  not not_18 (not_18_out, F4);
  not not_19 (not_19_out, F3);
  not not_20 (not_20_out, F2);
  not not_21 (not_21_out, F1);
  not not_22 (not_22_out, OP5);
  not not_23 (not_23_out, OP4);
  not not_24 (not_24_out, OP3);
  not not_25 (not_25_out, OP2);
  not not_26 (not_26_out, OP1);
  not not_27 (not_27_out, OP0);
  not not_28 (not_28_out, F4);
  not not_29 (not_29_out, F3);
  not not_30 (not_30_out, F2);
  not not_31 (not_31_out, F0);
  not not_32 (not_32_out, OP5);
  not not_33 (not_33_out, OP4);
  not not_34 (not_34_out, OP3);
  not not_35 (not_35_out, OP2);
  not not_36 (not_36_out, OP1);
  not not_37 (not_37_out, OP0);
  not not_38 (not_38_out, F4);
  not not_39 (not_39_out, F3);
  not not_40 (not_40_out, F1);
  not not_41 (not_41_out, F0);
  not not_42 (not_42_out, OP5);
  not not_43 (not_43_out, OP4);
  not not_44 (not_44_out, OP3);
  not not_45 (not_45_out, OP2);
  not not_46 (not_46_out, OP1);
  not not_47 (not_47_out, OP0);
  not not_48 (not_48_out, F4);
  not not_49 (not_49_out, F3);
  not not_50 (not_50_out, F1);
  not not_51 (not_51_out, OP5);
  not not_52 (not_52_out, OP4);
  not not_53 (not_53_out, OP3);
  not not_54 (not_54_out, OP2);
  not not_55 (not_55_out, OP1);
  not not_56 (not_56_out, OP0);
  not not_57 (not_57_out, F4);
  not not_58 (not_58_out, F3);
  not not_59 (not_59_out, OP5);
  not not_60 (not_60_out, OP4);
  not not_61 (not_61_out, OP3);
  not not_62 (not_62_out, OP2);
  not not_63 (not_63_out, OP1);
  not not_64 (not_64_out, OP0);
  not not_65 (not_65_out, F4);
  not not_66 (not_66_out, F2);
  not not_67 (not_67_out, F0);
  not not_68 (not_68_out, OP5);
  not not_69 (not_69_out, OP4);
  not not_70 (not_70_out, OP3);
  not not_71 (not_71_out, OP2);
  not not_72 (not_72_out, OP1);
  not not_73 (not_73_out, OP0);
  not not_74 (not_74_out, F4);
  not not_75 (not_75_out, F2);
  not not_76 (not_76_out, OP5);
  not not_77 (not_77_out, OP4);
  not not_78 (not_78_out, OP3);
  not not_79 (not_79_out, OP2);
  not not_80 (not_80_out, OP1);
  not not_81 (not_81_out, OP0);
  not not_82 (not_82_out, F5);
  not not_83 (not_83_out, F4);
  not not_84 (not_84_out, F2);
  not not_85 (not_85_out, F1);
  not not_86 (not_86_out, F0);
  not not_87 (not_87_out, OP5);
  not not_88 (not_88_out, OP4);
  not not_89 (not_89_out, OP3);
  not not_90 (not_90_out, OP2);
  not not_91 (not_91_out, OP1);
  not not_92 (not_92_out, OP0);
  not not_93 (not_93_out, F5);
  not not_94 (not_94_out, F4);
  not not_95 (not_95_out, F1);
  not not_96 (not_96_out, F0);
  not not_97 (not_97_out, OP5);
  not not_98 (not_98_out, OP4);
  not not_99 (not_99_out, OP3);
  not not_100 (not_100_out, OP1);
  not not_101 (not_101_out, OP0);
  not not_102 (not_102_out, OP5);
  not not_103 (not_103_out, OP4);
  not not_104 (not_104_out, OP3);
  not not_105 (not_105_out, OP1);
  not not_106 (not_106_out, OP5);
  not not_107 (not_107_out, OP4);
  not not_108 (not_108_out, OP2);
  not not_109 (not_109_out, OP1);
  not not_110 (not_110_out, OP0);
  not not_111 (not_111_out, OP5);
  not not_112 (not_112_out, OP4);
  not not_113 (not_113_out, OP1);
  not not_114 (not_114_out, OP0);
  not not_115 (not_115_out, OP5);
  not not_116 (not_116_out, OP4);
  not not_117 (not_117_out, OP2);
  not not_118 (not_118_out, OP1);
  not not_119 (not_119_out, OP5);
  not not_120 (not_120_out, OP4);
  not not_121 (not_121_out, OP2);
  not not_122 (not_122_out, OP0);
  not not_123 (not_123_out, OP5);
  not not_124 (not_124_out, OP4);
  not not_125 (not_125_out, OP1);
  not not_126 (not_126_out, OP4);
  not not_127 (not_127_out, OP3);
  not not_128 (not_128_out, OP2);
  not not_129 (not_129_out, OP4);
  not not_130 (not_130_out, OP2);
  not not_131 (not_131_out, OP5);
  not not_132 (not_132_out, OP4);
  not not_133 (not_133_out, OP3);
  not not_134 (not_134_out, OP2);
  not not_135 (not_135_out, OP1);
  not not_136 (not_136_out, OP0);
  not not_137 (not_137_out, F5);
  not not_138 (not_138_out, F4);
  not not_139 (not_139_out, F3);
  not not_140 (not_140_out, F2);
  not not_141 (not_141_out, F1);
  not not_142 (not_142_out, F0);
  not not_143 (not_143_out, OP5);
  not not_144 (not_144_out, OP4);
  not not_145 (not_145_out, OP3);
  not not_146 (not_146_out, OP2);
  not not_147 (not_147_out, OP1);
  not not_148 (not_148_out, OP0);
  not not_149 (not_149_out, F5);
  not not_150 (not_150_out, F4);
  not not_151 (not_151_out, F3);
  not not_152 (not_152_out, F2);
  not not_153 (not_153_out, OP5);
  not not_154 (not_154_out, OP4);
  not not_155 (not_155_out, OP3);
  not not_156 (not_156_out, OP2);
  not not_157 (not_157_out, OP1);
  not not_158 (not_158_out, OP0);
  not not_159 (not_159_out, F5);
  not not_160 (not_160_out, F4);
  not not_161 (not_161_out, F3);
  not not_162 (not_162_out, F2);
  not not_163 (not_163_out, F0);
  not not_164 (not_164_out, OP5);
  not not_165 (not_165_out, OP4);
  not not_166 (not_166_out, OP3);
  not not_167 (not_167_out, OP2);
  not not_168 (not_168_out, OP1);
  not not_169 (not_169_out, OP0);
  not not_170 (not_170_out, F4);
  not not_171 (not_171_out, F3);
  not not_172 (not_172_out, F2);
  not not_173 (not_173_out, F1);
  not not_174 (not_174_out, F0);
  not not_175 (not_175_out, OP5);
  not not_176 (not_176_out, OP4);
  not not_177 (not_177_out, OP3);
  not not_178 (not_178_out, OP2);
  not not_179 (not_179_out, OP1);
  not not_180 (not_180_out, OP0);
  not not_181 (not_181_out, F4);
  not not_182 (not_182_out, F3);
  not not_183 (not_183_out, F2);
  not not_184 (not_184_out, F1);
  not not_185 (not_185_out, OP5);
  not not_186 (not_186_out, OP4);
  not not_187 (not_187_out, OP3);
  not not_188 (not_188_out, OP2);
  not not_189 (not_189_out, OP1);
  not not_190 (not_190_out, OP0);
  not not_191 (not_191_out, F4);
  not not_192 (not_192_out, F3);
  not not_193 (not_193_out, F2);
  not not_194 (not_194_out, F0);
  not not_195 (not_195_out, OP5);
  not not_196 (not_196_out, OP4);
  not not_197 (not_197_out, OP3);
  not not_198 (not_198_out, OP2);
  not not_199 (not_199_out, OP1);
  not not_200 (not_200_out, OP0);
  not not_201 (not_201_out, F4);
  not not_202 (not_202_out, F3);
  not not_203 (not_203_out, F1);
  not not_204 (not_204_out, F0);
  not not_205 (not_205_out, OP5);
  not not_206 (not_206_out, OP4);
  not not_207 (not_207_out, OP3);
  not not_208 (not_208_out, OP2);
  not not_209 (not_209_out, OP1);
  not not_210 (not_210_out, OP0);
  not not_211 (not_211_out, F4);
  not not_212 (not_212_out, F3);
  not not_213 (not_213_out, F1);
  not not_214 (not_214_out, OP5);
  not not_215 (not_215_out, OP4);
  not not_216 (not_216_out, OP3);
  not not_217 (not_217_out, OP2);
  not not_218 (not_218_out, OP1);
  not not_219 (not_219_out, OP0);
  not not_220 (not_220_out, F4);
  not not_221 (not_221_out, F3);
  not not_222 (not_222_out, OP5);
  not not_223 (not_223_out, OP4);
  not not_224 (not_224_out, OP3);
  not not_225 (not_225_out, OP2);
  not not_226 (not_226_out, OP1);
  not not_227 (not_227_out, OP0);
  not not_228 (not_228_out, F4);
  not not_229 (not_229_out, F2);
  not not_230 (not_230_out, F0);
  not not_231 (not_231_out, OP5);
  not not_232 (not_232_out, OP4);
  not not_233 (not_233_out, OP3);
  not not_234 (not_234_out, OP2);
  not not_235 (not_235_out, OP1);
  not not_236 (not_236_out, OP0);
  not not_237 (not_237_out, F4);
  not not_238 (not_238_out, F2);
  not not_239 (not_239_out, OP5);
  not not_240 (not_240_out, OP4);
  not not_241 (not_241_out, OP3);
  not not_242 (not_242_out, OP2);
  not not_243 (not_243_out, OP1);
  not not_244 (not_244_out, OP0);
  not not_245 (not_245_out, F5);
  not not_246 (not_246_out, F4);
  not not_247 (not_247_out, F1);
  not not_248 (not_248_out, F0);
  not not_249 (not_249_out, OP5);
  not not_250 (not_250_out, OP4);
  not not_251 (not_251_out, OP3);
  not not_252 (not_252_out, OP1);
  not not_253 (not_253_out, OP0);
  not not_254 (not_254_out, OP5);
  not not_255 (not_255_out, OP4);
  not not_256 (not_256_out, OP3);
  not not_257 (not_257_out, OP1);
  not not_258 (not_258_out, OP4);
  not not_259 (not_259_out, OP2);
  and and_1 (and_1_out, not_1_out, not_2_out, not_3_out, not_4_out, not_5_out, not_6_out, F5, not_7_out, not_8_out, not_9_out, not_10_out, not_11_out);
  and and_2 (and_2_out, not_12_out, not_13_out, not_14_out, not_15_out, not_16_out, not_17_out, F5, not_18_out, not_19_out, not_20_out, not_21_out, F0);
  and and_3 (and_3_out, not_22_out, not_23_out, not_24_out, not_25_out, not_26_out, not_27_out, F5, not_28_out, not_29_out, not_30_out, F1, not_31_out);
  and and_4 (and_4_out, not_32_out, not_33_out, not_34_out, not_35_out, not_36_out, not_37_out, F5, not_38_out, not_39_out, F2, not_40_out, not_41_out);
  and and_5 (and_5_out, not_42_out, not_43_out, not_44_out, not_45_out, not_46_out, not_47_out, F5, not_48_out, not_49_out, F2, not_50_out, F0);
  and and_6 (and_6_out, not_51_out, not_52_out, not_53_out, not_54_out, not_55_out, not_56_out, F5, not_57_out, not_58_out, F2, F1, F0);
  and and_7 (and_7_out, not_59_out, not_60_out, not_61_out, not_62_out, not_63_out, not_64_out, F5, not_65_out, F3, not_66_out, F1, not_67_out);
  and and_8 (and_8_out, not_68_out, not_69_out, not_70_out, not_71_out, not_72_out, not_73_out, F5, not_74_out, F3, not_75_out, F1, F0);
  and and_9 (and_9_out, not_76_out, not_77_out, not_78_out, not_79_out, not_80_out, not_81_out, not_82_out, not_83_out, F3, not_84_out, not_85_out, not_86_out);
  and and_10 (and_10_out, not_87_out, not_88_out, not_89_out, not_90_out, not_91_out, not_92_out, not_93_out, not_94_out, F3, F2, not_95_out, not_96_out);
  and and_11 (and_11_out, not_97_out, not_98_out, not_99_out, OP2, not_100_out, not_101_out);
  and and_12 (and_12_out, not_102_out, not_103_out, not_104_out, OP2, not_105_out, OP0);
  and and_13 (and_13_out, not_106_out, not_107_out, OP3, not_108_out, not_109_out, not_110_out);
  and and_14 (and_14_out, not_111_out, not_112_out, OP3, OP2, not_113_out, not_114_out);
  and and_15 (and_15_out, not_115_out, not_116_out, OP3, not_117_out, not_118_out, OP0);
  and and_16 (and_16_out, not_119_out, not_120_out, OP3, not_121_out, OP1, not_122_out);
  and and_17 (and_17_out, not_123_out, not_124_out, OP3, OP2, not_125_out, OP0);
  and and_18 (and_18_out, OP5, not_126_out, not_127_out, not_128_out, OP1, OP0);
  and and_19 (and_19_out, OP5, not_129_out, OP3, not_130_out, OP1, OP0);
  and and_20 (and_20_out, not_131_out, not_132_out, not_133_out, not_134_out, not_135_out, not_136_out, not_137_out, not_138_out, not_139_out, not_140_out, not_141_out, not_142_out);
  and and_21 (and_21_out, not_143_out, not_144_out, not_145_out, not_146_out, not_147_out, not_148_out, not_149_out, not_150_out, not_151_out, not_152_out, F1, F0);
  and and_22 (and_22_out, not_153_out, not_154_out, not_155_out, not_156_out, not_157_out, not_158_out, not_159_out, not_160_out, not_161_out, not_162_out, F1, not_163_out);
  and and_23 (and_23_out, not_164_out, not_165_out, not_166_out, not_167_out, not_168_out, not_169_out, F5, not_170_out, not_171_out, not_172_out, not_173_out, not_174_out);
  and and_24 (and_24_out, not_175_out, not_176_out, not_177_out, not_178_out, not_179_out, not_180_out, F5, not_181_out, not_182_out, not_183_out, not_184_out, F0);
  and and_25 (and_25_out, not_185_out, not_186_out, not_187_out, not_188_out, not_189_out, not_190_out, F5, not_191_out, not_192_out, not_193_out, F1, not_194_out);
  and and_26 (and_26_out, not_195_out, not_196_out, not_197_out, not_198_out, not_199_out, not_200_out, F5, not_201_out, not_202_out, F2, not_203_out, not_204_out);
  and and_27 (and_27_out, not_205_out, not_206_out, not_207_out, not_208_out, not_209_out, not_210_out, F5, not_211_out, not_212_out, F2, not_213_out, F0);
  and and_28 (and_28_out, not_214_out, not_215_out, not_216_out, not_217_out, not_218_out, not_219_out, F5, not_220_out, not_221_out, F2, F1, F0);
  and and_29 (and_29_out, not_222_out, not_223_out, not_224_out, not_225_out, not_226_out, not_227_out, F5, not_228_out, F3, not_229_out, F1, not_230_out);
  and and_30 (and_30_out, not_231_out, not_232_out, not_233_out, not_234_out, not_235_out, not_236_out, F5, not_237_out, F3, not_238_out, F1, F0);
  and and_31 (and_31_out, not_239_out, not_240_out, not_241_out, not_242_out, not_243_out, not_244_out, not_245_out, not_246_out, F3, F2, not_247_out, not_248_out);
  and and_32 (and_32_out, not_249_out, not_250_out, not_251_out, OP2, not_252_out, not_253_out);
  and and_33 (and_33_out, not_254_out, not_255_out, not_256_out, OP2, not_257_out, OP0);
  and and_34 (and_34_out, OP5, not_258_out, OP3, not_259_out, OP1, OP0);
  or or_1 (rs, and_1_out, and_2_out, and_3_out, and_4_out, and_5_out, and_6_out, and_7_out, and_8_out, and_9_out, and_10_out, and_11_out, and_12_out, and_13_out, and_14_out, and_15_out, and_16_out, and_17_out, and_18_out, and_19_out);
  or or_2 (rt, and_20_out, and_21_out, and_22_out, and_23_out, and_24_out, and_25_out, and_26_out, and_27_out, and_28_out, and_29_out, and_30_out, and_31_out, and_32_out, and_33_out, and_34_out);
endmodule

module \数据冲突检测  (
  input  rs,
  input  rt,
  input  [4:0] r1_num,
  input  [4:0] r2_num,
  input  [4:0] EX_REG_num,
  input  EX_RegWrite,
  input  [4:0] MEM_REG_num,
  input  MEM_RegWrite,
  output \数据冲突 
);

  wire and_1_out, and_2_out, and_3_out, and_4_out, comparator_1_eq, comparator_2_eq, comparator_3_eq,
       comparator_4_eq, comparator_5_eq, comparator_6_eq, comparator_7_eq, comparator_8_eq, not_1_out,
       not_2_out, not_3_out, not_4_out;

  Comparator #(.width(5), .mode("unsigned")) comparator_1 (
    .a(r1_num), .b({5{1'b0}}), .eq(comparator_1_eq));  // open: gt, lt
  Comparator #(.width(5), .mode("unsigned")) comparator_2 (
    .a(r1_num), .b(EX_REG_num), .eq(comparator_2_eq));  // open: gt, lt
  Comparator #(.width(5), .mode("unsigned")) comparator_3 (
    .a(r2_num), .b({5{1'b0}}), .eq(comparator_3_eq));  // open: gt, lt
  Comparator #(.width(5), .mode("unsigned")) comparator_4 (
    .a(r2_num), .b(EX_REG_num), .eq(comparator_4_eq));  // open: gt, lt
  Comparator #(.width(5), .mode("unsigned")) comparator_5 (
    .a(r1_num), .b({5{1'b0}}), .eq(comparator_5_eq));  // open: gt, lt
  Comparator #(.width(5), .mode("unsigned")) comparator_6 (
    .a(r1_num), .b(MEM_REG_num), .eq(comparator_6_eq));  // open: gt, lt
  Comparator #(.width(5), .mode("unsigned")) comparator_7 (
    .a(r2_num), .b({5{1'b0}}), .eq(comparator_7_eq));  // open: gt, lt
  Comparator #(.width(5), .mode("unsigned")) comparator_8 (
    .a(r2_num), .b(MEM_REG_num), .eq(comparator_8_eq));  // open: gt, lt
  not not_1 (not_1_out, comparator_1_eq);
  not not_2 (not_2_out, comparator_3_eq);
  not not_3 (not_3_out, comparator_5_eq);
  not not_4 (not_4_out, comparator_7_eq);
  and and_1 (and_1_out, rs, not_1_out, comparator_2_eq, EX_RegWrite);
  and and_2 (and_2_out, rt, not_2_out, EX_RegWrite, comparator_4_eq);
  and and_3 (and_3_out, rs, not_3_out, comparator_6_eq, MEM_RegWrite);
  and and_4 (and_4_out, not_4_out, comparator_8_eq, rt, MEM_RegWrite);
  or or_1 (\数据冲突 , and_1_out, and_2_out, and_3_out, and_4_out);

  // Notes on the sheet:
  //   r1冲突
  //   ex阶段的冲突
  //   r2冲突
endmodule
